// Logisim project ok-computer.circ as structural Verilog: 31 circuits, main circuit main
module main (
  input  On_Off,
  input  in_2,
  input  [3:0] in_3,
  input  _7,
  input  _8,
  input  _9,
  input  _4,
  input  _5,
  input  _6,
  input  _1,
  input  _2,
  input  _3,
  input  _0,
  output [7:0] SYSTEM_BUS,
  output [7:0] R0000,
  output [7:0] R0001,
  output [7:0] R0010,
  output [7:0] R0011,
  output [7:0] R0100,
  output [7:0] R0101,
  output [7:0] R0110,
  output [7:0] R0111,
  output [3:0] out_23,
  output [7:0] R1000,
  output [7:0] R1001,
  output [7:0] R1010,
  output [7:0] R1011,
  output [7:0] out_28,
  output [7:0] R1100,
  output [7:0] R1101,
  output [7:0] R1110,
  output [7:0] R1111,
  output [7:0] out_33,
  output [3:0] out_34,
  output [7:0] out_35,
  output [7:0] out_36,
  output [7:0] CPU_BUS,
  output [7:0] out_38,
  output [7:0] out_39,
  output [7:0] MULT_OUT,
  output [7:0] D0,
  output [2:0] out_42,
  output [7:0] D1,
  output [7:0] out_44,
  output out_45,
  output out_46
);

  wire and_8_out, and_19_out, and_21_out, and_23_out, and_25_out, clock_1_out, cu_1_ar_mode, cu_1_cycle,
       cu_1_d0_addr, cu_1_d0_inorout, cu_1_d1_addr, cu_1_d1_inorout, cu_1_dcr_noin, cu_1_eq_negate,
       cu_1_eq_out, cu_1_inc_on, cu_1_ir_noin, cu_1_lin_noin, cu_1_mar_inorout, cu_1_mbr_inmode,
       cu_1_pc_inmode, cu_1_pc_noin, cu_1_rammode_in, cu_1_rin_noin, d_ff_1_q, eq_1_eq, not_1_out, not_2_out,
       not_3_out, not_4_out, not_5_out, not_6_out, not_7_out, not_8_out, not_9_out, not_10_out;
  wire [1:0] cu_1_alu_op;
  wire [2:0] alu_1_status;
  wire [3:0] and_2_out, and_13_out, and_24_out, and_26_out, cu_1_ar_in, cu_1_mar_ir_in, cu_1_mar_pc_in,
       double_dabble_1_out_2, double_dabble_1_out_3, double_dabble_1_out_4, inc_1_out_0, or_2_out;
  wire [3:3] or_5_out;
  wire [6:0] encode_display_1_out_2, encode_display_2_out_2, encode_display_3_out_2;
  wire [7:0] alu_1_a_out, and_1_out, and_3_out, and_4_out, and_5_out, and_6_out, and_7_out, and_9_out,
       and_10_out, and_11_out, and_12_out, and_14_out, and_15_out, and_16_out, and_17_out, and_18_out,
       and_20_out, and_22_out, and_27_out, and_28_out, cu_1_alu_lin, cu_1_alu_out, cu_1_alu_rin, cu_1_d0_in,
       cu_1_d0_out, cu_1_d1_in, cu_1_d1_out, cu_1_dcr_in, cu_1_ir_cycle_in, cu_1_ir_mbr_in, cu_1_kb_out,
       cu_1_mar_out, cu_1_mbr_cpu_in, cu_1_mbr_cpu_out, cu_1_mbr_sys_in, cu_1_mbr_sys_out, cu_1_mult_out,
       cu_1_out_43, cu_1_ram_in, cu_1_ram_out, cycle_1_cycle_out, gen_register_1_data_out,
       gen_register_2_data_out, mar_1_outadr, mbr_1_out_0, mult_1_ans, or_3_out, or_4_out;
  wire [31:0] prog_rom_1_rom_out_0000_0011, prog_rom_1_rom_out_0100_0111, prog_rom_1_rom_out_1000_1011,
       prog_rom_1_rom_out_1100_1111;

  PROG_ROM prog_rom_1 (
    .ROM_OUT_0000_0011(prog_rom_1_rom_out_0000_0011), .ROM_ON(in_2),
    .ROM_OUT_1100_1111(prog_rom_1_rom_out_1100_1111), .ROM_OUT_0100_0111(prog_rom_1_rom_out_0100_0111),
    .PROG(in_3), .ROM_OUT_1000_1011(prog_rom_1_rom_out_1000_1011));
  ENCODE_DISPLAY encode_display_1 (.out_2(encode_display_1_out_2), .in_1(double_dabble_1_out_2));
  KeyPad keypad_1 (
    .Zero(_0), .One(_1), .Two(_2), .Three(_3), .Four(_4), .Five(_5), .Six(_6), .Seven(_7), .Eight(_8),
    .Nine(_9), .Output(out_38));
  _7_Segment_Display u_7_segment_display_1 (
    .g(encode_display_1_out_2[0]), .f(encode_display_1_out_2[1]), .a(encode_display_1_out_2[2]),
    .b(encode_display_1_out_2[3]), .e(encode_display_1_out_2[4]), .d(encode_display_1_out_2[5]),
    .c(encode_display_1_out_2[6]));  // open: dp
  DOUBLE_DABBLE double_dabble_1 (
    .out_4(double_dabble_1_out_4), .out_3(double_dabble_1_out_3), .in_1(out_44), .out_2(double_dabble_1_out_2));
  _7_Segment_Display u_7_segment_display_2 (
    .g(encode_display_2_out_2[0]), .f(encode_display_2_out_2[1]), .a(encode_display_2_out_2[2]),
    .b(encode_display_2_out_2[3]), .e(encode_display_2_out_2[4]), .d(encode_display_2_out_2[5]),
    .c(encode_display_2_out_2[6]));  // open: dp
  ENCODE_DISPLAY encode_display_2 (.out_2(encode_display_2_out_2), .in_1(double_dabble_1_out_3));
  D_Flip_Flop d_ff_1 (.D(cu_1_rammode_in), .clk(clock_1_out), .Q(d_ff_1_q), .reset(and_8_out));  // open: Qn, preset
  ENCODE_DISPLAY encode_display_3 (.out_2(encode_display_3_out_2), .in_1(double_dabble_1_out_4));
  _7_Segment_Display u_7_segment_display_3 (
    .g(encode_display_3_out_2[0]), .f(encode_display_3_out_2[1]), .a(encode_display_3_out_2[2]),
    .b(encode_display_3_out_2[3]), .e(encode_display_3_out_2[4]), .d(encode_display_3_out_2[5]),
    .c(encode_display_3_out_2[6]));  // open: dp
  DATA_BYTE_ONOFF data_byte_onoff_1 (
    .On_Off_In(and_8_out), .CLK(clock_1_out), .NO_IN(not_1_out), .Byte_Out(out_44), .Byte_In(and_3_out));
  not not_1 (not_1_out, cu_1_dcr_noin);
  RAM ram_1 (
    .CLK(clock_1_out), .READ_WRITE(d_ff_1_q), .ADDR(out_34), .DR_IN(and_1_out), .DR_OUT(out_28),
    .out_11(R0000), .out_12(R0001), .out_13(R0010), .out_14(R0011), .out_15(R0100), .out_16(R0101),
    .out_17(R0110), .out_18(R0111), .out_19(R1000), .out_20(R1001), .out_21(R1010), .out_22(R1011),
    .out_23(R1100), .out_24(R1101), .out_25(R1110), .out_26(R1111),
    .ROM_IN_0000_0011(prog_rom_1_rom_out_0000_0011), .ROM_IN_0100_0111(prog_rom_1_rom_out_0100_0111),
    .ROM_IN_1000_1011(prog_rom_1_rom_out_1000_1011), .ROM_IN_1100_1111(prog_rom_1_rom_out_1100_1111),
    .ROM_ON(in_2), .On_Off_In(and_8_out));  // open: out_27
  AR ar_1 (.CLK_IN(clock_1_out), .IN_OR_OUT(cu_1_ar_mode), .ADR_OUT(out_34), .ADR_IN(and_2_out), .On_Off_In(and_8_out));
  assign and_1_out = cu_1_ram_in & SYSTEM_BUS;  // AND_Gate and_1, 8 bits wide
  assign and_2_out = SYSTEM_BUS[3:0] & cu_1_ar_in;  // AND_Gate and_2, 4 bits wide
  assign and_3_out = SYSTEM_BUS & cu_1_dcr_in;  // AND_Gate and_3, 8 bits wide
  assign and_4_out = out_28 & cu_1_ram_out;  // AND_Gate and_4, 8 bits wide
  assign and_5_out = out_38 & cu_1_kb_out;  // AND_Gate and_5, 8 bits wide
  assign SYSTEM_BUS = and_4_out | and_5_out | and_7_out | and_6_out;  // OR_Gate or_1, 8 bits wide
  assign and_6_out = mar_1_outadr & cu_1_mar_out;  // AND_Gate and_6, 8 bits wide
  assign and_7_out = mbr_1_out_0 & cu_1_mbr_sys_out;  // AND_Gate and_7, 8 bits wide
  Clock clock_1 (.out(clock_1_out));
  and and_8 (and_8_out, ~in_2, ~On_Off);  // AND_Gate
  assign and_9_out = cu_1_d0_out & gen_register_1_data_out;  // AND_Gate and_9, 8 bits wide
  GEN_REGISTER gen_register_1 (
    .CONTENTS(D0), .DATA_OUT(gen_register_1_data_out), .ADDR(cu_1_d0_addr), .DATA_IN(and_12_out),
    .CLK_IN(clock_1_out), .IN_OR_OUT(not_2_out), .On_Off_In(and_8_out));
  not not_2 (not_2_out, cu_1_d0_inorout);
  assign and_10_out = cu_1_d1_out & gen_register_2_data_out;  // AND_Gate and_10, 8 bits wide
  GEN_REGISTER gen_register_2 (
    .CONTENTS(D1), .DATA_OUT(gen_register_2_data_out), .ADDR(cu_1_d1_addr), .DATA_IN(and_16_out),
    .CLK_IN(clock_1_out), .IN_OR_OUT(not_3_out), .On_Off_In(and_8_out));
  not not_3 (not_3_out, cu_1_d1_inorout);
  MAR mar_1 (
    .OutAdr(mar_1_outadr), .Contents(out_33), .InAdr(or_2_out), .in_or_out(not_4_out), .Clock(clock_1_out),
    .On_Off_In(and_8_out));
  assign and_11_out = mbr_1_out_0 & cu_1_mbr_cpu_out;  // AND_Gate and_11, 8 bits wide
  MBR mbr_1 (
    .OUT_0(mbr_1_out_0), .Contents(out_35), .CLK(clock_1_out), .IN_MODE(not_5_out), .IN_0(or_3_out),
    .On_Off_In(and_8_out));
  CU cu_1 (
    .D0_IN(cu_1_d0_in), .D1_IN(cu_1_d1_in), .AR_MODE(cu_1_ar_mode), .MBR_SYS_OUT(cu_1_mbr_sys_out),
    .D1_ADDR(cu_1_d1_addr), .INC_ON(cu_1_inc_on), .MAR_IR_IN(cu_1_mar_ir_in), .D0_ADDR(cu_1_d0_addr),
    .D0_INOROUT(cu_1_d0_inorout), .MAR_INOROUT(cu_1_mar_inorout), .D1_INOROUT(cu_1_d1_inorout),
    .MAR_PC_IN(cu_1_mar_pc_in), .MBR_SYS_IN(cu_1_mbr_sys_in), .MBR_CPU_IN(cu_1_mbr_cpu_in),
    .ALU_LIN(cu_1_alu_lin), .MAR_OUT(cu_1_mar_out), .ALU_OP(cu_1_alu_op), .D0_OUT(cu_1_d0_out),
    .DCR_IN(cu_1_dcr_in), .ALU_OUT(cu_1_alu_out), .RAM_OUT(cu_1_ram_out), .RAMMODE_IN(cu_1_rammode_in),
    .MBR_INMODE(cu_1_mbr_inmode), .KB_OUT(cu_1_kb_out), .INSTR_IN(out_36), .LIN_NOIN(cu_1_lin_noin),
    .IR_MBR_IN(cu_1_ir_mbr_in), .ALU_RIN(cu_1_alu_rin), .DCR_NOIN(cu_1_dcr_noin), .PC_NOIN(cu_1_pc_noin),
    .RAM_IN(cu_1_ram_in), .D1_OUT(cu_1_d1_out), .PC_INMODE(cu_1_pc_inmode), .IR_NOIN(cu_1_ir_noin),
    .MBR_CPU_OUT(cu_1_mbr_cpu_out), .RIN_NOIN(cu_1_rin_noin), .AR_IN(cu_1_ar_in), .EQ_OUT(cu_1_eq_out),
    .EQ_NEGATE(cu_1_eq_negate), .IR_CYCLE_IN(cu_1_ir_cycle_in), .CYCLE(cu_1_cycle), .CLK(clock_1_out),
    .ON_OFF(and_19_out), .out_47(out_45), .MULT_OUT(cu_1_mult_out), .out_43(cu_1_out_43));  // open: out_46
  assign or_2_out = and_24_out | and_13_out;  // OR_Gate or_2, 4 bits wide
  not not_4 (not_4_out, cu_1_mar_inorout);
  assign and_12_out = CPU_BUS & cu_1_d0_in;  // AND_Gate and_12, 8 bits wide
  assign and_13_out = out_23 & cu_1_mar_pc_in;  // AND_Gate and_13, 4 bits wide
  not not_5 (not_5_out, cu_1_mbr_inmode);
  assign or_3_out = and_14_out | and_15_out;  // OR_Gate or_3, 8 bits wide
  assign and_14_out = SYSTEM_BUS & cu_1_mbr_sys_in;  // AND_Gate and_14, 8 bits wide
  assign and_15_out = CPU_BUS & cu_1_mbr_cpu_in;  // AND_Gate and_15, 8 bits wide
  assign and_16_out = CPU_BUS & cu_1_d1_in;  // AND_Gate and_16, 8 bits wide
  PC pc_1 (
    .OUT_0(out_23), .IN_1(inc_1_out_0), .CLK(clock_1_out), .IN_0(and_26_out), .IN_MODE(not_7_out),
    .NO_IN(cu_1_pc_noin), .On_Off_In(and_8_out));
  CYCLE cycle_1 (.CYCLE_IN(cu_1_cycle), .CYCLE_OUT(cycle_1_cycle_out));
  INC inc_1 (.OUT_0(inc_1_out_0), .ON_0(cu_1_inc_on), .IN_0(out_23));
  assign and_17_out = mbr_1_out_0 & cu_1_ir_mbr_in;  // AND_Gate and_17, 8 bits wide
  assign or_4_out = and_17_out | and_18_out;  // OR_Gate or_4, 8 bits wide
  assign and_18_out = cycle_1_cycle_out & cu_1_ir_cycle_in;  // AND_Gate and_18, 8 bits wide
  and and_19 (and_19_out, On_Off, not_6_out);
  not not_6 (not_6_out, and_8_out);
  not not_7 (not_7_out, and_21_out);
  not not_8 (not_8_out, cu_1_ir_noin);
  DATA_BYTE_ONOFF data_byte_onoff_2 (
    .On_Off_In(and_8_out), .CLK(clock_1_out), .NO_IN(not_9_out), .Byte_Out(out_39), .Byte_In(and_20_out));
  DATA_BYTE_ONOFF data_byte_onoff_3 (
    .On_Off_In(and_8_out), .CLK(clock_1_out), .NO_IN(not_8_out), .Byte_Out(out_36), .Byte_In(or_4_out));
  not not_9 (not_9_out, cu_1_lin_noin);
  assign and_20_out = CPU_BUS & cu_1_alu_lin;  // AND_Gate and_20, 8 bits wide
  ALU alu_1 (.A_Out(alu_1_a_out), .Op(cu_1_alu_op), .L_In(out_39), .Status(alu_1_status), .R_In(MULT_OUT));
  and and_21 (and_21_out, cu_1_pc_inmode, or_5_out[3]);
  assign and_22_out = CPU_BUS & cu_1_alu_rin;  // AND_Gate and_22, 8 bits wide
  and and_23 (and_23_out, eq_1_eq, cu_1_eq_out, ~cu_1_eq_negate);  // AND_Gate
  assign and_24_out = out_36[3:0] & cu_1_mar_ir_in;  // AND_Gate and_24, 4 bits wide
  not not_10 (not_10_out, cu_1_rin_noin);
  DATA_BYTE_ONOFF data_byte_onoff_4 (
    .On_Off_In(and_8_out), .CLK(clock_1_out), .NO_IN(not_10_out), .Byte_Out(MULT_OUT), .Byte_In(and_22_out));
  or or_5 (or_5_out[3], and_23_out, and_25_out);
  and and_25 (and_25_out, ~eq_1_eq, cu_1_eq_out, cu_1_eq_negate);  // AND_Gate
  EQ eq_1 (.EQ(eq_1_eq), .IN_1(gen_register_2_data_out), .IN_0(gen_register_1_data_out));
  MULT mult_1 (.ANS(mult_1_ans), .IN_1(out_39), .IN_0(cu_1_out_43), .OVERFLOW(out_46));
  assign and_26_out = out_36[3:0] & {4{or_5_out[3]}};  // AND_Gate and_26, 4 bits wide
  assign and_27_out = cu_1_mult_out & mult_1_ans;  // AND_Gate and_27, 8 bits wide
  STATUS status_1 (.On_Off_In(and_8_out), .CLK(clock_1_out), .in_1(alu_1_status), .out_4(out_42));
  assign and_28_out = cu_1_alu_out & alu_1_a_out;  // AND_Gate and_28, 8 bits wide
  assign CPU_BUS = and_11_out | and_28_out | and_27_out | and_10_out | and_9_out;  // OR_Gate or_6, 8 bits wide

  // Notes on the sheet:
  //   (values stored in RAM)
  //   DCR_NOIN
  //   AR_MODE
  //   RAMMODE_IN
  //   display companion register
  //   RAM_IN
  //   AR_IN
  //   DCR_IN
  //   RAM_OUT
  //   KB_OUT
  //   MAR_OUT
  //   MBR_SYS_OUT
  //   D0_INOROUT
  //   D0_ADDR
  //   D1_OUT
  //   D1_INOROUT
  //   D1_ADDR
  //   1 = On, 0 = Off
  //   D0_OUT
  //   MBR_INMODE
  //   MBR_CPU_OUT
  //   MBR_SYS_IN
  //   D0_IN
  //   MAR_PC_IN
  //   MAR_INOROUT
  //   D1_IN
  //   MBR_CPU_IN
  //   IR_MBR_IN
  //   IR_CYCLE_IN
  //   PC_INMODE
  //   IR_NOIN
  //   ALU_LIN
  //   ALU_OP
  //   ALU_RIN
  //   MAR_IR_IN
  //   input 1: EQ_OUT
  //   input 2: EQ_NEGATE
  //   BEQ/BNQ MODIFIER
  //   ALU_OUT
endmodule

module CU (
  input  ON_OFF,
  input  CLK,
  input  [7:0] INSTR_IN,
  output DCR_NOIN,
  output [7:0] DCR_IN,
  output [7:0] KB_OUT,
  output [7:0] IR_MBR_IN,
  output RAMMODE_IN,
  output AR_MODE,
  output [7:0] RAM_IN,
  output [7:0] RAM_OUT,
  output [7:0] MAR_OUT,
  output MAR_INOROUT,
  output PC_INMODE,
  output IR_NOIN,
  output [3:0] MAR_IR_IN,
  output [3:0] MAR_PC_IN,
  output PC_NOIN,
  output INC_ON,
  output [7:0] MBR_SYS_OUT,
  output MBR_INMODE,
  output [7:0] MBR_CPU_IN,
  output [7:0] MBR_SYS_IN,
  output [7:0] MBR_CPU_OUT,
  output [7:0] D0_OUT,
  output [7:0] D0_IN,
  output D0_INOROUT,
  output D0_ADDR,
  output [7:0] D1_OUT,
  output [7:0] D1_IN,
  output D1_ADDR,
  output D1_INOROUT,
  output [7:0] ALU_LIN,
  output LIN_NOIN,
  output [7:0] ALU_RIN,
  output RIN_NOIN,
  output [1:0] ALU_OP,
  output [7:0] ALU_OUT,
  output [3:0] AR_IN,
  output EQ_OUT,
  output EQ_NEGATE,
  output [7:0] MULT_OUT,
  output [7:0] out_43,
  output [7:0] IR_CYCLE_IN,
  output CYCLE,
  output [7:0] out_46,
  output out_47
);

  wire A_S_0_out, A_S_1_out, A_S_2_out, and_2_out, and_18_out, and_19_out, and_20_out, and_21_out,
       and_22_out, and_23_out, and_24_out, and_25_out, and_26_out, and_27_out, and_28_out, and_29_out,
       and_30_out, and_31_out, and_32_out, and_33_out, and_34_out, and_35_out, B_NE_0_out, CYC_0_out,
       CYC_1_out, CYC_2_out, CYC_3_out, CYC_4_out, CYC_5_out, INP_0_out, INP_1_out, LD_1_out, LD_2_out,
       LD_3_out, LD_4_out, LD_5_out, MUL_0_out, not_1_out, PRT_0_out, PRT_1_out, STR_1_out, STR_2_out,
       STR_3_out, STR_4_out, STR_5_out;
  wire [0:0] not_5_out, not_6_out, not_9_out, not_10_out;
  wire [1:1] not_4_out;
  wire [2:0] not_8_out;
  wire [3:0] and_1_out, and_3_out, and_4_out, and_5_out, and_6_out, and_7_out, and_8_out, and_9_out,
       and_10_out, and_11_out, and_12_out, and_13_out, and_14_out, and_15_out, and_16_out, and_17_out,
       count_1_out_0, inc_1_out_0, or_8_out;
  wire [3:2] not_2_out, STR_out;
  wire [3:3] ADD_SUB_out, BEQ_BNQ_out, CYC_out, INP_out, MULT_out_2, PRT_out;
  wire [7:0] and_36_out;
  wire [7:7] MUL_1_out;

  or or_1 (DCR_NOIN, PRT_1_out, 1'b0);
  and LD_1 (LD_1_out, and_1_out[3], ~and_1_out[2], and_1_out[1], and_1_out[0]);  // AND_Gate
  or or_2 (DCR_IN[7], PRT_1_out, 1'b0);
  and LD_2 (LD_2_out, and_1_out[3], and_1_out[2], ~and_1_out[1], ~and_1_out[0]);  // AND_Gate
  and LD_3 (LD_3_out, and_1_out[3], and_1_out[2], ~and_1_out[1], and_1_out[0]);  // AND_Gate
  assign and_1_out = count_1_out_0 & {4{not_2_out[3]}};  // AND_Gate and_1, 4 bits wide
  or or_3 (KB_OUT[7], INP_0_out, 1'b0);
  and LD_4 (LD_4_out, and_1_out[3], and_1_out[2], and_1_out[1], ~and_1_out[0]);  // AND_Gate
  and LD_5 (LD_5_out, and_1_out[3], and_1_out[2], and_1_out[1], and_1_out[0]);
  or or_4 (IR_MBR_IN[7], CYC_5_out, 1'b0);
  or or_5 (RAMMODE_IN, STR_3_out, STR_4_out, 1'b0);
  and STR_2 (STR_2_out, and_3_out[3], and_3_out[2], ~and_3_out[1], ~and_3_out[0]);  // AND_Gate
  and STR_1 (STR_1_out, and_3_out[3], ~and_3_out[2], and_3_out[1], and_3_out[0]);  // AND_Gate
  COUNT count_1 (
    .CLK(CLK), .OUT_0(count_1_out_0), .IN_1(or_8_out), .NO_IN(not_1_out), .IN_MODE(and_2_out),
    .IN_0(inc_1_out_0));
  and and_2 (and_2_out, ~count_1_out_0[3], ~count_1_out_0[2], ~count_1_out_0[1], ~count_1_out_0[0]);  // AND_Gate
  or or_6 (AR_MODE, CYC_2_out, STR_3_out, STR_4_out, STR_5_out, LD_3_out, 1'b0);
  and STR_3 (STR_3_out, and_3_out[3], and_3_out[2], ~and_3_out[1], and_3_out[0]);  // AND_Gate
  not not_1 (not_1_out, ON_OFF);
  and STR_4 (STR_4_out, and_3_out[3], and_3_out[2], and_3_out[1], ~and_3_out[0]);  // AND_Gate
  assign and_3_out = count_1_out_0 & {4{STR_out[3]}};  // AND_Gate and_3, 4 bits wide
  INC inc_1 (.OUT_0(inc_1_out_0), .ON_0(ON_OFF), .IN_0(count_1_out_0));
  or or_7 (RAM_IN[7], STR_4_out, 1'b0);
  and STR_5 (STR_5_out, and_3_out[3], and_3_out[2], and_3_out[1], and_3_out[0]);
  assign or_8_out = and_17_out | and_15_out | and_14_out | and_13_out | and_11_out | and_10_out | and_9_out | and_7_out;  // OR_Gate or_8, 4 bits wide
  or or_9 (RAM_OUT[7], CYC_3_out, LD_4_out, 1'b0);
  and A_S_0 (A_S_0_out, and_4_out[3], and_4_out[2], ~and_4_out[1], and_4_out[0]);  // AND_Gate
  or or_10 (MAR_OUT[7], CYC_1_out, STR_2_out, LD_2_out, 1'b0);
  and A_S_1 (A_S_1_out, and_4_out[3], and_4_out[2], and_4_out[1], ~and_4_out[0]);  // AND_Gate
  assign and_4_out = count_1_out_0 & {4{ADD_SUB_out[3]}};  // AND_Gate and_4, 4 bits wide
  and A_S_2 (A_S_2_out, and_4_out[3], and_4_out[2], and_4_out[1], and_4_out[0]);
  or or_11 (MAR_INOROUT, LD_1_out, CYC_0_out, STR_1_out, 1'b0);
  and PRT_0 (PRT_0_out, and_5_out[3], and_5_out[2], and_5_out[1], ~and_5_out[0]);  // AND_Gate
  assign and_5_out = count_1_out_0 & {4{PRT_out[3]}};  // AND_Gate and_5, 4 bits wide
  or or_12 (PC_INMODE, B_NE_0_out, 1'b0);
  and PRT_1 (PRT_1_out, and_5_out[3], and_5_out[2], and_5_out[1], and_5_out[0]);
  and INP_0 (INP_0_out, and_6_out[3], and_6_out[2], and_6_out[1], ~and_6_out[0]);  // AND_Gate
  or or_13 (IR_NOIN, MUL_1_out[7], INP_1_out, B_NE_0_out, PRT_1_out, A_S_2_out, STR_5_out, LD_5_out, CYC_5_out, 1'b0);
  and INP_1 (INP_1_out, and_6_out[3], and_6_out[2], and_6_out[1], and_6_out[0]);
  assign and_6_out = count_1_out_0 & {4{INP_out[3]}};  // AND_Gate and_6, 4 bits wide
  or or_14 (MAR_IR_IN[3], LD_1_out, STR_1_out, 1'b0);
  assign and_7_out = {4{not_2_out[3]}} & {not_2_out, {2{not_2_out[3]}}};  // AND_Gate and_7, 4 bits wide
  not not_2 (not_2_out[2], not_2_out[3]);
  and LD0 (not_2_out[3], INSTR_IN[7], ~INSTR_IN[6], INSTR_IN[5]);  // AND_Gate
  and B_NE_0 (B_NE_0_out, and_8_out[3], and_8_out[2], and_8_out[1], and_8_out[0]);
  assign and_8_out = count_1_out_0 & {4{BEQ_BNQ_out[3]}};  // AND_Gate and_8, 4 bits wide
  assign and_9_out = {4{STR_out[3]}} & {STR_out, {2{STR_out[3]}}};  // AND_Gate and_9, 4 bits wide
  not not_3 (STR_out[2], STR_out[3]);
  and STR (STR_out[3], INSTR_IN[7], INSTR_IN[6], INSTR_IN[5]);
  or or_15 (MAR_PC_IN[3], CYC_0_out, 1'b0);
  assign and_10_out = {4{ADD_SUB_out[3]}} & {{2{ADD_SUB_out[3]}}, not_4_out[1], ADD_SUB_out[3]};  // AND_Gate and_10, 4 bits wide
  and CYC_0 (CYC_0_out, and_12_out[3], ~and_12_out[2], and_12_out[1], ~and_12_out[0]);  // AND_Gate
  not not_4 (not_4_out[1], ADD_SUB_out[3]);
  and ADD_SUB (ADD_SUB_out[3], ~INSTR_IN[7], ~INSTR_IN[6], INSTR_IN[5]);  // AND_Gate
  buf or_16 (PC_NOIN, 1'b0);  // OR_Gate
  and CYC_1 (CYC_1_out, and_12_out[3], ~and_12_out[2], and_12_out[1], and_12_out[0]);  // AND_Gate
  and CYC_2 (CYC_2_out, and_12_out[3], and_12_out[2], ~and_12_out[1], ~and_12_out[0]);  // AND_Gate
  assign and_11_out = {4{PRT_out[3]}} & {{3{PRT_out[3]}}, not_5_out[0]};  // AND_Gate and_11, 4 bits wide
  not not_5 (not_5_out[0], PRT_out[3]);
  and PRT (PRT_out[3], ~INSTR_IN[7], INSTR_IN[6], INSTR_IN[5], ~INSTR_IN[4]);  // AND_Gate
  and CYC_3 (CYC_3_out, and_12_out[3], and_12_out[2], ~and_12_out[1], and_12_out[0]);  // AND_Gate
  assign and_12_out = count_1_out_0 & {4{CYC_out[3]}};  // AND_Gate and_12, 4 bits wide
  assign and_13_out = {4{INP_out[3]}} & {{3{INP_out[3]}}, not_6_out[0]};  // AND_Gate and_13, 4 bits wide
  and INP (INP_out[3], ~INSTR_IN[7], INSTR_IN[6], INSTR_IN[5], INSTR_IN[4]);  // AND_Gate
  or or_17 (INC_ON, CYC_4_out, 1'b0);
  and CYC_4 (CYC_4_out, and_12_out[3], and_12_out[2], and_12_out[1], ~and_12_out[0]);  // AND_Gate
  not not_6 (not_6_out[0], INP_out[3]);
  and CYC_5 (CYC_5_out, and_12_out[3], and_12_out[2], and_12_out[1], and_12_out[0]);
  assign and_14_out = {4{BEQ_BNQ_out[3]}} & {4{BEQ_BNQ_out[3]}};  // AND_Gate and_14, 4 bits wide
  and BEQ_BNQ (BEQ_BNQ_out[3], ~INSTR_IN[7], INSTR_IN[6], ~INSTR_IN[5]);  // AND_Gate
  or or_18 (MBR_SYS_OUT[7], PRT_1_out, STR_4_out, 1'b0);
  assign and_15_out = {4{CYC_out[3]}} & {CYC_out[3], not_8_out[2], CYC_out[3], not_8_out[0]};  // AND_Gate and_15, 4 bits wide
  not not_7 (not_8_out[2], CYC_out[3]);
  not not_8 (not_8_out[0], CYC_out[3]);
  and CYC (CYC_out[3], ~INSTR_IN[7], ~INSTR_IN[6], ~INSTR_IN[5]);  // AND_Gate
  or or_19 (MBR_INMODE, CYC_3_out, INP_0_out, PRT_0_out, STR_3_out, LD_4_out, 1'b0);
  and MUL_0 (MUL_0_out, and_16_out[3], and_16_out[2], and_16_out[1], ~and_16_out[0]);  // AND_Gate
  and STP (out_47, INSTR_IN[7], ~INSTR_IN[6], ~INSTR_IN[5], ~INSTR_IN[4]);  // AND_Gate
  and MUL_1 (MUL_1_out[7], and_16_out[3], and_16_out[2], and_16_out[1], and_16_out[0]);
  assign and_16_out = count_1_out_0 & {4{MULT_out_2[3]}};  // AND_Gate and_16, 4 bits wide
  assign and_17_out = {4{MULT_out_2[3]}} & {{3{MULT_out_2[3]}}, not_9_out[0]};  // AND_Gate and_17, 4 bits wide
  or or_20 (MBR_CPU_IN[7], PRT_0_out, STR_3_out, 1'b0);
  not not_9 (not_9_out[0], MULT_out_2[3]);
  and MULT (MULT_out_2[3], INSTR_IN[7], ~INSTR_IN[6], ~INSTR_IN[5], INSTR_IN[4]);  // AND_Gate
  or or_21 (MBR_SYS_IN[7], CYC_3_out, INP_0_out, LD_4_out, 1'b0);
  or or_22 (MBR_CPU_OUT[7], LD_5_out, INP_1_out, 1'b0);
  and and_18 (and_18_out, PRT_0_out, ~INSTR_IN[3]);  // AND_Gate
  and and_19 (and_19_out, MUL_0_out, ~INSTR_IN[3]);  // AND_Gate
  or or_23 (D0_OUT[7], and_19_out, and_18_out, and_21_out, and_20_out, and_22_out, 1'b0);
  and and_20 (and_20_out, A_S_0_out, ~INSTR_IN[3]);  // AND_Gate
  and and_21 (and_21_out, A_S_1_out, INSTR_IN[3]);
  and and_22 (and_22_out, STR_3_out, ~INSTR_IN[4]);  // AND_Gate
  and and_23 (and_23_out, INP_1_out, ~INSTR_IN[3]);  // AND_Gate
  or or_24 (D0_IN[7], and_26_out, and_23_out, and_25_out, and_24_out, 1'b0);
  and and_24 (and_24_out, LD_5_out, ~INSTR_IN[4]);  // AND_Gate
  and and_25 (and_25_out, A_S_2_out, ~INSTR_IN[3]);  // AND_Gate
  and and_26 (and_26_out, MUL_1_out[7], ~INSTR_IN[3]);  // AND_Gate
  or or_25 (D0_INOROUT, and_26_out, and_23_out, and_25_out, and_24_out, 1'b0);
  or or_26 (D0_ADDR, and_26_out, and_23_out, and_25_out, and_24_out, 1'b0);
  and and_27 (and_27_out, MUL_0_out, INSTR_IN[3]);
  and and_28 (and_28_out, A_S_1_out, ~INSTR_IN[3]);  // AND_Gate
  and and_29 (and_29_out, PRT_0_out, INSTR_IN[3]);
  or or_27 (D1_OUT[7], and_27_out, and_29_out, and_28_out, and_31_out, and_30_out, 1'b0);
  and and_30 (and_30_out, STR_3_out, INSTR_IN[4]);
  and and_31 (and_31_out, A_S_0_out, INSTR_IN[3]);
  and and_32 (and_32_out, INP_1_out, INSTR_IN[3]);
  or or_28 (D1_IN[7], and_35_out, and_32_out, and_34_out, and_33_out, 1'b0);
  and and_33 (and_33_out, LD_5_out, INSTR_IN[4]);
  and and_34 (and_34_out, A_S_2_out, INSTR_IN[3]);
  and and_35 (and_35_out, MUL_1_out[7], INSTR_IN[3]);
  or or_29 (D1_ADDR, and_35_out, and_32_out, and_34_out, and_33_out, 1'b0);
  or or_30 (D1_INOROUT, and_35_out, and_32_out, and_34_out, and_33_out, 1'b0);
  or or_31 (ALU_LIN[7], MUL_0_out, A_S_1_out, 1'b0);
  or or_32 (LIN_NOIN, MUL_0_out, A_S_1_out, 1'b0);
  or or_33 (ALU_RIN[7], A_S_0_out, 1'b0);
  or or_34 (RIN_NOIN, A_S_0_out, 1'b0);
  assign ALU_OP = {1'b0, not_10_out[0]};  // OR_Gate or_35, 2 bits wide OR_Gate
  not not_10 (not_10_out[0], INSTR_IN[4]);
  or or_36 (ALU_OUT[7], A_S_2_out, 1'b0);
  or or_37 (AR_IN[3], CYC_1_out, STR_2_out, LD_2_out, 1'b0);
  or or_38 (EQ_OUT, B_NE_0_out, 1'b0);
  or or_39 (EQ_NEGATE, INSTR_IN[4], 1'b0);
  or or_40 (MULT_OUT[7], MUL_1_out[7], 1'b0);
  assign out_43 = and_36_out;  // OR_Gate or_41, 8 bits wide OR_Gate
  assign and_36_out = {{5{1'b0}}, INSTR_IN[2:0]} & {8{MUL_1_out[7]}};  // AND_Gate and_36, 8 bits wide
  or or_42 (IR_CYCLE_IN[7], MUL_1_out[7], INP_1_out, B_NE_0_out, PRT_1_out, A_S_2_out, STR_5_out, LD_5_out, 1'b0);
  or or_43 (CYCLE, STR_5_out, INP_1_out, B_NE_0_out, PRT_1_out, A_S_2_out, MUL_1_out[7], LD_5_out, 1'b0);

  assign ALU_LIN[6:0] = {7{ALU_LIN[7]}};
  assign ALU_OUT[6:0] = {7{ALU_OUT[7]}};
  assign ALU_RIN[6:0] = {7{ALU_RIN[7]}};
  assign AR_IN[2:0] = {3{AR_IN[3]}};
  assign D0_IN[6:0] = {7{D0_IN[7]}};
  assign D0_OUT[6:0] = {7{D0_OUT[7]}};
  assign D1_IN[6:0] = {7{D1_IN[7]}};
  assign D1_OUT[6:0] = {7{D1_OUT[7]}};
  assign DCR_IN[6:0] = {7{DCR_IN[7]}};
  assign IR_CYCLE_IN[6:0] = {7{IR_CYCLE_IN[7]}};
  assign IR_MBR_IN[6:0] = {7{IR_MBR_IN[7]}};
  assign KB_OUT[6:0] = {7{KB_OUT[7]}};
  assign MAR_IR_IN[2:0] = {3{MAR_IR_IN[3]}};
  assign MAR_OUT[6:0] = {7{MAR_OUT[7]}};
  assign MAR_PC_IN[2:0] = {3{MAR_PC_IN[3]}};
  assign MBR_CPU_IN[6:0] = {7{MBR_CPU_IN[7]}};
  assign MBR_CPU_OUT[6:0] = {7{MBR_CPU_OUT[7]}};
  assign MBR_SYS_IN[6:0] = {7{MBR_SYS_IN[7]}};
  assign MBR_SYS_OUT[6:0] = {7{MBR_SYS_OUT[7]}};
  assign MULT_OUT[6:0] = {7{MULT_OUT[7]}};
  assign out_46 = {{5{1'b0}}, INSTR_IN[2:0]};
  assign RAM_IN[6:0] = {7{RAM_IN[7]}};
  assign RAM_OUT[6:0] = {7{RAM_OUT[7]}};

  // Notes on the sheet:
  //   1111
  //   1110
  //   1101
  //   1100
  //   1011
  //   1010
  //   1001
  //   being all zero activates in mode
  //   add and sub in same circuit
endmodule

module CYCLE (
  input  CYCLE_IN,
  output [7:0] CYCLE_OUT
);

  not not_1 (CYCLE_OUT[0], CYCLE_IN);
  not not_2 (CYCLE_OUT[1], CYCLE_IN);
  not not_3 (CYCLE_OUT[2], CYCLE_IN);
  not not_4 (CYCLE_OUT[3], CYCLE_IN);
  not not_5 (CYCLE_OUT[4], CYCLE_IN);
  not not_6 (CYCLE_OUT[5], CYCLE_IN);
  not not_7 (CYCLE_OUT[6], CYCLE_IN);
  not not_8 (CYCLE_OUT[7], CYCLE_IN);
endmodule

module RAM (
  input  ROM_ON,
  input  CLK,
  input  READ_WRITE,
  input  [3:0] ADDR,
  input  [31:0] ROM_IN_0000_0011,
  input  [31:0] ROM_IN_0100_0111,
  input  [31:0] ROM_IN_1000_1011,
  input  [31:0] ROM_IN_1100_1111,
  input  [7:0] DR_IN,
  input  On_Off_In,
  output [7:0] out_11,
  output [7:0] out_12,
  output [7:0] out_13,
  output [7:0] out_14,
  output [7:0] out_15,
  output [7:0] out_16,
  output [7:0] out_17,
  output [7:0] out_18,
  output [7:0] out_19,
  output [7:0] out_20,
  output [7:0] out_21,
  output [7:0] out_22,
  output [7:0] out_23,
  output [7:0] out_24,
  output [7:0] out_25,
  output [7:0] out_26,
  output [7:0] out_27,
  output [7:0] DR_OUT
);

  wire or_5_out, or_7_out, or_10_out, or_12_out, or_14_out, or_15_out, or_18_out, or_19_out, or_26_out,
       or_29_out, or_30_out, or_33_out, or_43_out, or_44_out, or_47_out, or_48_out;
  wire [0:0] not_28_out;
  wire [1:0] not_11_out;
  wire [1:1] not_20_out;
  wire [2:0] not_8_out, not_26_out;
  wire [2:1] not_18_out;
  wire [2:2] not_32_out;
  wire [3:0] not_1_out, not_5_out, not_21_out, not_24_out, or_1_out, or_2_out, or_3_out, or_4_out, or_13_out,
       or_16_out, or_17_out, or_20_out, or_27_out, or_28_out, or_31_out, or_32_out, or_38_out, or_39_out,
       or_40_out, or_41_out;
  wire [3:1] not_13_out, not_16_out;
  wire [3:2] not_29_out;
  wire [3:3] not_31_out;
  wire [7:0] _0000_data_out, _0001_data_out, _0010_data_out, _0011_data_out, _0100_data_out, _0101_data_out,
       _0110_data_out, _0111_data_out, _1000_data_out, _1001_data_out, _1010_data_out, _1011_data_out,
       _1100_data_out, _1101_data_out, _1110_data_out, _1111_data_out, or_6_out, or_8_out, or_9_out,
       or_11_out, or_21_out, or_22_out, or_23_out, or_24_out, or_25_out, or_34_out, or_35_out, or_36_out,
       or_37_out, or_42_out, or_45_out, or_46_out, or_49_out;

  RAM_BYTE _0000 (
    .CLK_IN(CLK), .MODE(or_5_out), .ADDR(or_1_out), .DATA_OUT(_0000_data_out), .DATA_IN(or_6_out),
    .CONTENTS(out_11), .On_Off_In(On_Off_In));
  assign or_1_out = {4{ROM_ON}} | not_1_out;  // OR_Gate or_1, 4 bits wide
  RAM_BYTE _0100 (
    .CLK_IN(CLK), .MODE(or_7_out), .ADDR(or_2_out), .DATA_OUT(_0100_data_out), .DATA_IN(or_8_out),
    .CONTENTS(out_15), .On_Off_In(On_Off_In));
  assign or_2_out = {4{ROM_ON}} | {not_5_out[3], ADDR[2], not_5_out[1:0]};  // OR_Gate or_2, 4 bits wide
  RAM_BYTE _1000 (
    .CLK_IN(CLK), .MODE(or_10_out), .ADDR(or_3_out), .DATA_OUT(_1000_data_out), .DATA_IN(or_9_out),
    .CONTENTS(out_19), .On_Off_In(On_Off_In));
  assign or_3_out = {4{ROM_ON}} | {ADDR[3], not_8_out};  // OR_Gate or_3, 4 bits wide
  RAM_BYTE _1100 (
    .CLK_IN(CLK), .MODE(or_12_out), .ADDR(or_4_out), .DATA_OUT(_1100_data_out), .DATA_IN(or_11_out),
    .CONTENTS(out_23), .On_Off_In(On_Off_In));
  assign or_4_out = {4{ROM_ON}} | {ADDR[3:2], not_11_out};  // OR_Gate or_4, 4 bits wide
  or or_5 (or_5_out, READ_WRITE, ROM_ON);
  assign or_6_out = out_27 | ROM_IN_0000_0011[7:0];  // OR_Gate or_6, 8 bits wide
  not not_1 (not_1_out[0], ADDR[0]);
  not not_2 (not_1_out[1], ADDR[1]);
  not not_3 (not_1_out[2], ADDR[2]);
  not not_4 (not_1_out[3], ADDR[3]);
  or or_7 (or_7_out, READ_WRITE, ROM_ON);
  assign or_8_out = out_27 | ROM_IN_0100_0111[7:0];  // OR_Gate or_8, 8 bits wide
  not not_5 (not_5_out[0], ADDR[0]);
  not not_6 (not_5_out[1], ADDR[1]);
  not not_7 (not_5_out[3], ADDR[3]);
  assign or_9_out = out_27 | ROM_IN_1000_1011[7:0];  // OR_Gate or_9, 8 bits wide
  or or_10 (or_10_out, READ_WRITE, ROM_ON);
  not not_8 (not_8_out[0], ADDR[0]);
  not not_9 (not_8_out[1], ADDR[1]);
  not not_10 (not_8_out[2], ADDR[2]);
  assign or_11_out = out_27 | ROM_IN_1100_1111[7:0];  // OR_Gate or_11, 8 bits wide
  or or_12 (or_12_out, READ_WRITE, ROM_ON);
  not not_11 (not_11_out[0], ADDR[0]);
  not not_12 (not_11_out[1], ADDR[1]);
  RAM_BYTE _0001 (
    .CLK_IN(CLK), .MODE(or_14_out), .ADDR(or_13_out), .DATA_OUT(_0001_data_out), .DATA_IN(or_21_out),
    .CONTENTS(out_12), .On_Off_In(On_Off_In));
  assign or_13_out = {4{ROM_ON}} | {not_13_out, ADDR[0]};  // OR_Gate or_13, 4 bits wide
  or or_14 (or_14_out, READ_WRITE, ROM_ON);
  RAM_BYTE _0101 (
    .CLK_IN(CLK), .MODE(or_15_out), .ADDR(or_16_out), .DATA_OUT(_0101_data_out), .DATA_IN(or_22_out),
    .CONTENTS(out_16), .On_Off_In(On_Off_In));
  or or_15 (or_15_out, READ_WRITE, ROM_ON);
  assign or_16_out = {4{ROM_ON}} | {not_16_out[3], ADDR[2], not_16_out[1], ADDR[0]};  // OR_Gate or_16, 4 bits wide
  RAM_BYTE _1001 (
    .CLK_IN(CLK), .MODE(or_18_out), .ADDR(or_17_out), .DATA_OUT(_1001_data_out), .DATA_IN(or_23_out),
    .CONTENTS(out_20), .On_Off_In(On_Off_In));
  assign or_17_out = {4{ROM_ON}} | {ADDR[3], not_18_out, ADDR[0]};  // OR_Gate or_17, 4 bits wide
  or or_18 (or_18_out, READ_WRITE, ROM_ON);
  RAM_BYTE _1101 (
    .CLK_IN(CLK), .MODE(or_19_out), .ADDR(or_20_out), .DATA_OUT(_1101_data_out), .DATA_IN(or_24_out),
    .CONTENTS(out_24), .On_Off_In(On_Off_In));
  or or_19 (or_19_out, READ_WRITE, ROM_ON);
  assign or_20_out = {4{ROM_ON}} | {ADDR[3:2], not_20_out[1], ADDR[0]};  // OR_Gate or_20, 4 bits wide
  assign or_21_out = out_27 | ROM_IN_0000_0011[15:8];  // OR_Gate or_21, 8 bits wide
  not not_13 (not_13_out[1], ADDR[1]);
  not not_14 (not_13_out[2], ADDR[2]);
  not not_15 (not_13_out[3], ADDR[3]);
  assign or_22_out = out_27 | ROM_IN_0100_0111[15:8];  // OR_Gate or_22, 8 bits wide
  not not_16 (not_16_out[1], ADDR[1]);
  not not_17 (not_16_out[3], ADDR[3]);
  assign or_23_out = out_27 | ROM_IN_1000_1011[15:8];  // OR_Gate or_23, 8 bits wide
  not not_18 (not_18_out[1], ADDR[1]);
  not not_19 (not_18_out[2], ADDR[2]);
  assign or_24_out = out_27 | ROM_IN_1100_1111[15:8];  // OR_Gate or_24, 8 bits wide
  not not_20 (not_20_out[1], ADDR[1]);
  assign or_25_out = _1100_data_out | _1000_data_out | _0100_data_out | _0000_data_out | _1101_data_out | _1001_data_out | _0101_data_out | _0001_data_out | _1110_data_out | _1010_data_out | _0110_data_out | _0010_data_out | _1111_data_out | _1011_data_out | _0111_data_out | _0011_data_out;  // OR_Gate or_25, 8 bits wide
  RAM_BYTE _0010 (
    .CLK_IN(CLK), .MODE(or_26_out), .ADDR(or_27_out), .DATA_OUT(_0010_data_out), .DATA_IN(or_34_out),
    .CONTENTS(out_13), .On_Off_In(On_Off_In));
  or or_26 (or_26_out, READ_WRITE, ROM_ON);
  assign or_27_out = {4{ROM_ON}} | {not_21_out[3:2], ADDR[1], not_21_out[0]};  // OR_Gate or_27, 4 bits wide
  not not_21 (not_21_out[0], ADDR[0]);
  not not_22 (not_21_out[2], ADDR[2]);
  not not_23 (not_21_out[3], ADDR[3]);
  RAM_BYTE _0110 (
    .CLK_IN(CLK), .MODE(or_29_out), .ADDR(or_28_out), .DATA_OUT(_0110_data_out), .DATA_IN(or_35_out),
    .CONTENTS(out_17), .On_Off_In(On_Off_In));
  assign or_28_out = {4{ROM_ON}} | {not_24_out[3], ADDR[2:1], not_24_out[0]};  // OR_Gate or_28, 4 bits wide
  or or_29 (or_29_out, READ_WRITE, ROM_ON);
  not not_24 (not_24_out[0], ADDR[0]);
  not not_25 (not_24_out[3], ADDR[3]);
  RAM_BYTE _1010 (
    .CLK_IN(CLK), .MODE(or_30_out), .ADDR(or_31_out), .DATA_OUT(_1010_data_out), .DATA_IN(or_36_out),
    .CONTENTS(out_21), .On_Off_In(On_Off_In));
  or or_30 (or_30_out, READ_WRITE, ROM_ON);
  assign or_31_out = {4{ROM_ON}} | {ADDR[3], not_26_out[2], ADDR[1], not_26_out[0]};  // OR_Gate or_31, 4 bits wide
  not not_26 (not_26_out[0], ADDR[0]);
  not not_27 (not_26_out[2], ADDR[2]);
  RAM_BYTE _1110 (
    .CLK_IN(CLK), .MODE(or_33_out), .ADDR(or_32_out), .DATA_OUT(_1110_data_out), .DATA_IN(or_37_out),
    .CONTENTS(out_25), .On_Off_In(On_Off_In));
  assign or_32_out = {4{ROM_ON}} | {ADDR[3:1], not_28_out[0]};  // OR_Gate or_32, 4 bits wide
  or or_33 (or_33_out, READ_WRITE, ROM_ON);
  not not_28 (not_28_out[0], ADDR[0]);
  DATA_REGISTER data_register_1 (
    .DATA_OUT(out_27), .RAM_IN(or_25_out), .MODE(READ_WRITE), .CLK_IN(CLK), .DATA_IN(DR_IN),
    .On_Off_In(On_Off_In));
  assign or_34_out = out_27 | ROM_IN_0000_0011[23:16];  // OR_Gate or_34, 8 bits wide
  assign or_35_out = out_27 | ROM_IN_0100_0111[23:16];  // OR_Gate or_35, 8 bits wide
  assign or_36_out = out_27 | ROM_IN_1000_1011[23:16];  // OR_Gate or_36, 8 bits wide
  assign or_37_out = out_27 | ROM_IN_1100_1111[23:16];  // OR_Gate or_37, 8 bits wide
  RAM_BYTE _0011 (
    .CLK_IN(CLK), .MODE(or_43_out), .ADDR(or_38_out), .DATA_OUT(_0011_data_out), .DATA_IN(or_42_out),
    .CONTENTS(out_14), .On_Off_In(On_Off_In));
  assign or_38_out = {4{ROM_ON}} | {not_29_out, ADDR[1:0]};  // OR_Gate or_38, 4 bits wide
  RAM_BYTE _0111 (
    .CLK_IN(CLK), .MODE(or_44_out), .ADDR(or_39_out), .DATA_OUT(_0111_data_out), .DATA_IN(or_45_out),
    .CONTENTS(out_18), .On_Off_In(On_Off_In));
  assign or_39_out = {4{ROM_ON}} | {not_31_out[3], ADDR[2:0]};  // OR_Gate or_39, 4 bits wide
  RAM_BYTE _1011 (
    .CLK_IN(CLK), .MODE(or_47_out), .ADDR(or_40_out), .DATA_OUT(_1011_data_out), .DATA_IN(or_46_out),
    .CONTENTS(out_22), .On_Off_In(On_Off_In));
  assign or_40_out = {4{ROM_ON}} | {ADDR[3], not_32_out[2], ADDR[1:0]};  // OR_Gate or_40, 4 bits wide
  RAM_BYTE _1111 (
    .CLK_IN(CLK), .MODE(or_48_out), .ADDR(or_41_out), .DATA_OUT(_1111_data_out), .DATA_IN(or_49_out),
    .CONTENTS(out_26), .On_Off_In(On_Off_In));
  assign or_41_out = {4{ROM_ON}} | ADDR;  // OR_Gate or_41, 4 bits wide
  assign or_42_out = out_27 | ROM_IN_0000_0011[31:24];  // OR_Gate or_42, 8 bits wide
  or or_43 (or_43_out, READ_WRITE, ROM_ON);
  not not_29 (not_29_out[2], ADDR[2]);
  not not_30 (not_29_out[3], ADDR[3]);
  or or_44 (or_44_out, READ_WRITE, ROM_ON);
  assign or_45_out = out_27 | ROM_IN_0100_0111[31:24];  // OR_Gate or_45, 8 bits wide
  not not_31 (not_31_out[3], ADDR[3]);
  assign or_46_out = out_27 | ROM_IN_1000_1011[31:24];  // OR_Gate or_46, 8 bits wide
  or or_47 (or_47_out, READ_WRITE, ROM_ON);
  not not_32 (not_32_out[2], ADDR[2]);
  or or_48 (or_48_out, READ_WRITE, ROM_ON);
  assign or_49_out = out_27 | ROM_IN_1100_1111[31:24];  // OR_Gate or_49, 8 bits wide
  assign DR_OUT = out_27 & ~{8{READ_WRITE}};  // AND_Gate and_1, 8 bits wide

  // Notes on the sheet:
  //   read = 0, write = 1
endmodule

module RAM_BYTE (
  input  CLK_IN,
  input  On_Off_In,
  input  [3:0] ADDR,
  input  MODE,
  input  [7:0] DATA_IN,
  output [7:0] DATA_OUT,
  output [7:0] CONTENTS
);

  wire and_1_out, and_3_out, and_4_out, and_6_out, and_7_out, and_9_out, and_10_out, and_12_out, and_13_out,
       and_15_out, and_16_out, and_18_out, and_19_out, and_21_out, and_22_out, and_24_out;

  and and_1 (and_1_out, DATA_IN[7], ADDR[3], ADDR[2], ADDR[1], ADDR[0], MODE);
  and and_2 (DATA_OUT[7], CONTENTS[7], ADDR[3], ADDR[2], ADDR[1], ADDR[0], ~MODE);  // AND_Gate
  S_R_Flip_Flop s_r_ff_1 (
    .S(and_1_out), .R(and_3_out), .clk(CLK_IN), .Q(CONTENTS[7]), .reset(On_Off_In));  // open: Qn, preset
  and and_3 (and_3_out, ~DATA_IN[7], ADDR[3], ADDR[2], ADDR[1], ADDR[0], MODE);  // AND_Gate
  and and_4 (and_4_out, DATA_IN[6], ADDR[3], ADDR[2], ADDR[1], ADDR[0], MODE);
  and and_5 (DATA_OUT[6], CONTENTS[6], ADDR[3], ADDR[2], ADDR[1], ADDR[0], ~MODE);  // AND_Gate
  S_R_Flip_Flop s_r_ff_2 (
    .S(and_4_out), .R(and_6_out), .clk(CLK_IN), .Q(CONTENTS[6]), .reset(On_Off_In));  // open: Qn, preset
  and and_6 (and_6_out, ~DATA_IN[6], ADDR[3], ADDR[2], ADDR[1], ADDR[0], MODE);  // AND_Gate
  S_R_Flip_Flop s_r_ff_3 (
    .S(and_7_out), .R(and_9_out), .clk(CLK_IN), .Q(CONTENTS[5]), .reset(On_Off_In));  // open: Qn, preset
  and and_7 (and_7_out, DATA_IN[5], ADDR[3], ADDR[2], ADDR[1], ADDR[0], MODE);
  and and_8 (DATA_OUT[5], CONTENTS[5], ADDR[3], ADDR[2], ADDR[1], ADDR[0], ~MODE);  // AND_Gate
  and and_9 (and_9_out, ~DATA_IN[5], ADDR[3], ADDR[2], ADDR[1], ADDR[0], MODE);  // AND_Gate
  and and_10 (and_10_out, DATA_IN[4], ADDR[3], ADDR[2], ADDR[1], ADDR[0], MODE);
  S_R_Flip_Flop s_r_ff_4 (
    .S(and_10_out), .R(and_12_out), .clk(CLK_IN), .Q(CONTENTS[4]), .reset(On_Off_In));  // open: Qn, preset
  and and_11 (DATA_OUT[4], CONTENTS[4], ADDR[3], ADDR[2], ADDR[1], ADDR[0], ~MODE);  // AND_Gate
  and and_12 (and_12_out, ~DATA_IN[4], ADDR[3], ADDR[2], ADDR[1], ADDR[0], MODE);  // AND_Gate
  and and_13 (and_13_out, DATA_IN[3], ADDR[3], ADDR[2], ADDR[1], ADDR[0], MODE);
  and and_14 (DATA_OUT[3], CONTENTS[3], ADDR[3], ADDR[2], ADDR[1], ADDR[0], ~MODE);  // AND_Gate
  S_R_Flip_Flop s_r_ff_5 (
    .S(and_13_out), .R(and_15_out), .clk(CLK_IN), .Q(CONTENTS[3]), .reset(On_Off_In));  // open: Qn, preset
  and and_15 (and_15_out, ~DATA_IN[3], ADDR[3], ADDR[2], ADDR[1], ADDR[0], MODE);  // AND_Gate
  and and_16 (and_16_out, DATA_IN[2], ADDR[3], ADDR[2], ADDR[1], ADDR[0], MODE);
  and and_17 (DATA_OUT[2], CONTENTS[2], ADDR[3], ADDR[2], ADDR[1], ADDR[0], ~MODE);  // AND_Gate
  S_R_Flip_Flop s_r_ff_6 (
    .S(and_16_out), .R(and_18_out), .clk(CLK_IN), .Q(CONTENTS[2]), .reset(On_Off_In));  // open: Qn, preset
  and and_18 (and_18_out, ~DATA_IN[2], ADDR[3], ADDR[2], ADDR[1], ADDR[0], MODE);  // AND_Gate
  S_R_Flip_Flop s_r_ff_7 (
    .S(and_19_out), .R(and_21_out), .clk(CLK_IN), .Q(CONTENTS[1]), .reset(On_Off_In));  // open: Qn, preset
  and and_19 (and_19_out, DATA_IN[1], ADDR[3], ADDR[2], ADDR[1], ADDR[0], MODE);
  and and_20 (DATA_OUT[1], CONTENTS[1], ADDR[3], ADDR[2], ADDR[1], ADDR[0], ~MODE);  // AND_Gate
  and and_21 (and_21_out, ~DATA_IN[1], ADDR[3], ADDR[2], ADDR[1], ADDR[0], MODE);  // AND_Gate
  and and_22 (and_22_out, DATA_IN[0], ADDR[3], ADDR[2], ADDR[1], ADDR[0], MODE);
  S_R_Flip_Flop s_r_ff_8 (
    .S(and_22_out), .R(and_24_out), .clk(CLK_IN), .Q(CONTENTS[0]), .reset(On_Off_In));  // open: Qn, preset
  and and_23 (DATA_OUT[0], CONTENTS[0], ADDR[3], ADDR[2], ADDR[1], ADDR[0], ~MODE);  // AND_Gate
  and and_24 (and_24_out, ~DATA_IN[0], ADDR[3], ADDR[2], ADDR[1], ADDR[0], MODE);  // AND_Gate
endmodule

module DATA_REGISTER (
  input  CLK_IN,
  input  On_Off_In,
  input  [7:0] RAM_IN,
  input  MODE,
  input  [7:0] DATA_IN,
  output [7:0] DATA_OUT
);

  wire [7:0] and_1_out, and_2_out, or_1_out;

  D_Flip_Flop d_ff_1 (.D(or_1_out[7]), .clk(CLK_IN), .Q(DATA_OUT[7]), .reset(On_Off_In));  // open: Qn, preset
  D_Flip_Flop d_ff_2 (.D(or_1_out[6]), .clk(CLK_IN), .Q(DATA_OUT[6]), .reset(On_Off_In));  // open: Qn, preset
  D_Flip_Flop d_ff_3 (.D(or_1_out[5]), .clk(CLK_IN), .Q(DATA_OUT[5]), .reset(On_Off_In));  // open: Qn, preset
  D_Flip_Flop d_ff_4 (.D(or_1_out[4]), .clk(CLK_IN), .Q(DATA_OUT[4]), .reset(On_Off_In));  // open: Qn, preset
  assign or_1_out = and_1_out | and_2_out;  // OR_Gate or_1, 8 bits wide
  assign and_1_out = RAM_IN & ~{8{MODE}};  // AND_Gate and_1, 8 bits wide
  assign and_2_out = DATA_IN & {8{MODE}};  // AND_Gate and_2, 8 bits wide
  D_Flip_Flop d_ff_5 (.D(or_1_out[3]), .clk(CLK_IN), .Q(DATA_OUT[3]), .reset(On_Off_In));  // open: Qn, preset
  D_Flip_Flop d_ff_6 (.D(or_1_out[2]), .clk(CLK_IN), .Q(DATA_OUT[2]), .reset(On_Off_In));  // open: Qn, preset
  D_Flip_Flop d_ff_7 (.D(or_1_out[1]), .clk(CLK_IN), .Q(DATA_OUT[1]), .reset(On_Off_In));  // open: Qn, preset
  D_Flip_Flop d_ff_8 (.D(or_1_out[0]), .clk(CLK_IN), .Q(DATA_OUT[0]), .reset(On_Off_In));  // open: Qn, preset
endmodule

module ALU (
  input  [7:0] L_In,
  input  [7:0] R_In,
  input  [1:0] Op,
  output [7:0] A_Out,
  output [2:0] Status
);

  wire and_1_out, and_2_out, full_adder_1_c_out, full_adder_2_c_out, full_adder_3_c_out, full_adder_4_c_out,
       full_adder_5_c_out, full_adder_6_c_out, half_adder_1_c_out;
  wire [7:0] twos_comp_1_out;

  and and_1 (and_1_out, twos_comp_1_out[7], ~A_Out[7], R_In[7]);  // AND_Gate
  // Probe on L_In
  Twos_Comp twos_comp_1 (.In(L_In), .Out(twos_comp_1_out), .ADD_SUB(Op[0]));
  and and_2 (and_2_out, ~twos_comp_1_out[7], A_Out[7], ~R_In[7]);  // AND_Gate
  or or_1 (Status[2], and_2_out, and_1_out);
  // Probe on R_In
  Half_Adder half_adder_1 (.A(R_In[0]), .B(twos_comp_1_out[0]), .R(A_Out[0]), .C_Out(half_adder_1_c_out));
  Full_Adder full_adder_1 (
    .A(twos_comp_1_out[1]), .B(R_In[1]), .C_In(half_adder_1_c_out), .R(A_Out[1]), .C_Out(full_adder_1_c_out));
  Full_Adder full_adder_2 (
    .A(twos_comp_1_out[2]), .B(R_In[2]), .C_In(full_adder_1_c_out), .R(A_Out[2]), .C_Out(full_adder_2_c_out));
  Full_Adder full_adder_3 (
    .A(twos_comp_1_out[3]), .B(R_In[3]), .C_In(full_adder_2_c_out), .R(A_Out[3]), .C_Out(full_adder_3_c_out));
  Full_Adder full_adder_4 (
    .A(twos_comp_1_out[4]), .B(R_In[4]), .C_In(full_adder_3_c_out), .R(A_Out[4]), .C_Out(full_adder_4_c_out));
  Full_Adder full_adder_5 (
    .A(twos_comp_1_out[5]), .B(R_In[5]), .C_In(full_adder_4_c_out), .R(A_Out[5]), .C_Out(full_adder_5_c_out));
  Full_Adder full_adder_6 (
    .A(twos_comp_1_out[6]), .B(R_In[6]), .C_In(full_adder_5_c_out), .R(A_Out[6]), .C_Out(full_adder_6_c_out));
  Full_Adder full_adder_7 (
    .A(twos_comp_1_out[7]), .B(R_In[7]), .C_In(full_adder_6_c_out), .R(A_Out[7]));  // open: C_Out
  and Zero (Status[0], ~A_Out[0], ~A_Out[1], ~A_Out[2], ~A_Out[3], ~A_Out[4], ~A_Out[5], ~A_Out[6], ~A_Out[7]);  // AND_Gate
  // Probe on A_Out

  assign Status[1] = A_Out[7];

  // Notes on the sheet:
  //   00 Sub
  //   01 Add
  //   001 zero result
  //   010 negative result
  //   100 overflow
endmodule

module Half_Adder (
  input  A,
  input  B,
  output R,
  output C_Out
);

  wire or_1_out;

  and and_1 (C_Out, A, B);
  or or_1 (or_1_out, A, B);
  and and_2 (R, ~C_Out, or_1_out);  // AND_Gate
endmodule

module Full_Adder (
  input  A,
  input  B,
  input  C_In,
  output R,
  output C_Out
);

  wire A_B_out, A_C_out, and_1_out, and_2_out, and_3_out, B_C_out, or_1_out;

  and A_B (A_B_out, A, B);
  and A_C (A_C_out, A, C_In);
  and B_C (B_C_out, B, C_In);
  and and_1 (and_1_out, A, B, C_In);
  or or_1 (or_1_out, A, B, C_In);
  and and_2 (and_2_out, ~A_B_out, ~A_C_out, ~B_C_out);  // AND_Gate
  and and_3 (and_3_out, or_1_out, and_2_out);
  or or_2 (C_Out, A_B_out, A_C_out, B_C_out);
  or or_3 (R, and_1_out, and_3_out);
endmodule

module Twos_Comp (
  input  ADD_SUB,
  input  [7:0] In,
  output [7:0] Out
);

  wire and_1_out, and_2_out, and_3_out, and_4_out, and_5_out, and_6_out, and_7_out, and_8_out, and_9_out,
       and_10_out, and_11_out, and_12_out, and_13_out, and_14_out, and_15_out, and_16_out,
       half_adder_1_c_out, half_adder_2_c_out, half_adder_3_c_out, half_adder_4_c_out, half_adder_5_c_out,
       half_adder_6_c_out, half_adder_7_c_out, not_1_out, or_1_out, or_2_out, or_3_out, or_4_out, or_5_out,
       or_6_out, or_7_out, or_8_out;

  // Probe on In
  and and_1 (and_1_out, ~In[0], ~ADD_SUB);  // AND_Gate
  and and_2 (and_2_out, In[0], ADD_SUB);
  and and_3 (and_3_out, ~In[1], ~ADD_SUB);  // AND_Gate
  and and_4 (and_4_out, In[1], ADD_SUB);
  and and_5 (and_5_out, ~In[2], ~ADD_SUB);  // AND_Gate
  and and_6 (and_6_out, In[2], ADD_SUB);
  and and_7 (and_7_out, ~In[3], ~ADD_SUB);  // AND_Gate
  and and_8 (and_8_out, In[3], ADD_SUB);
  and and_9 (and_9_out, ~In[4], ~ADD_SUB);  // AND_Gate
  and and_10 (and_10_out, In[4], ADD_SUB);
  and and_11 (and_11_out, ~In[5], ~ADD_SUB);  // AND_Gate
  and and_12 (and_12_out, In[5], ADD_SUB);
  and and_13 (and_13_out, ~In[6], ~ADD_SUB);  // AND_Gate
  and and_14 (and_14_out, In[6], ADD_SUB);
  and and_15 (and_15_out, ~In[7], ~ADD_SUB);  // AND_Gate
  and and_16 (and_16_out, In[7], ADD_SUB);
  or or_1 (or_1_out, and_1_out, and_2_out);
  or or_2 (or_2_out, and_3_out, and_4_out);
  or or_3 (or_3_out, and_5_out, and_6_out);
  or or_4 (or_4_out, and_7_out, and_8_out);
  or or_5 (or_5_out, and_9_out, and_10_out);
  or or_6 (or_6_out, and_11_out, and_12_out);
  or or_7 (or_7_out, and_13_out, and_14_out);
  or or_8 (or_8_out, and_15_out, and_16_out);
  Half_Adder half_adder_1 (.A(or_1_out), .B(not_1_out), .R(Out[0]), .C_Out(half_adder_1_c_out));
  not not_1 (not_1_out, ADD_SUB);
  Half_Adder half_adder_2 (.A(or_2_out), .B(half_adder_1_c_out), .R(Out[1]), .C_Out(half_adder_2_c_out));
  Half_Adder half_adder_3 (.A(or_3_out), .B(half_adder_2_c_out), .R(Out[2]), .C_Out(half_adder_3_c_out));
  Half_Adder half_adder_4 (.A(or_4_out), .B(half_adder_3_c_out), .R(Out[3]), .C_Out(half_adder_4_c_out));
  Half_Adder half_adder_5 (.A(or_5_out), .B(half_adder_4_c_out), .R(Out[4]), .C_Out(half_adder_5_c_out));
  Half_Adder half_adder_6 (.A(or_6_out), .B(half_adder_5_c_out), .R(Out[5]), .C_Out(half_adder_6_c_out));
  Half_Adder half_adder_7 (.A(or_7_out), .B(half_adder_6_c_out), .R(Out[6]), .C_Out(half_adder_7_c_out));
  Half_Adder half_adder_8 (.A(or_8_out), .B(half_adder_7_c_out), .R(Out[7]));  // open: C_Out
  // Probe on Out

  // Notes on the sheet:
  //   0 for sub, 1 for add
endmodule

module DISPLAY (
  input  [3:0] in_1,
  input  [3:0] in_2,
  input  [3:0] in_3
);

  wire [6:0] encode_display_1_out_2, encode_display_2_out_2, encode_display_3_out_2;

  ENCODE_DISPLAY encode_display_1 (.out_2(encode_display_1_out_2), .in_1(in_1));
  _7_Segment_Display u_7_segment_display_1 (
    .g(encode_display_1_out_2[0]), .f(encode_display_1_out_2[1]), .a(encode_display_1_out_2[2]),
    .b(encode_display_1_out_2[3]), .e(encode_display_1_out_2[4]), .d(encode_display_1_out_2[5]),
    .c(encode_display_1_out_2[6]));  // open: dp
  ENCODE_DISPLAY encode_display_2 (.out_2(encode_display_2_out_2), .in_1(in_2));
  _7_Segment_Display u_7_segment_display_2 (
    .g(encode_display_2_out_2[0]), .f(encode_display_2_out_2[1]), .a(encode_display_2_out_2[2]),
    .b(encode_display_2_out_2[3]), .e(encode_display_2_out_2[4]), .d(encode_display_2_out_2[5]),
    .c(encode_display_2_out_2[6]));  // open: dp
  _7_Segment_Display u_7_segment_display_3 (
    .g(encode_display_3_out_2[0]), .f(encode_display_3_out_2[1]), .a(encode_display_3_out_2[2]),
    .b(encode_display_3_out_2[3]), .e(encode_display_3_out_2[4]), .d(encode_display_3_out_2[5]),
    .c(encode_display_3_out_2[6]));  // open: dp
  ENCODE_DISPLAY encode_display_3 (.out_2(encode_display_3_out_2), .in_1(in_3));
endmodule

module ENCODE_DISPLAY (
  input  [3:0] in_1,
  output [6:0] out_2
);

  wire I0_out, I1_out, I2_out, I3_out, I4_out, I5_out, I6_out, I7_out, I8_out, I9_out;

  or O6 (out_2[6], I9_out, I8_out, I7_out, I6_out, I5_out, I4_out, I3_out, I1_out, I0_out);
  and I9 (I9_out, in_1[3], ~in_1[2], ~in_1[1], in_1[0]);  // AND_Gate
  or O5 (out_2[5], I8_out, I6_out, I5_out, I3_out, I2_out, I0_out);
  and I8 (I8_out, in_1[3], ~in_1[2], ~in_1[1], ~in_1[0]);  // AND_Gate
  and I7 (I7_out, ~in_1[3], in_1[2], in_1[1], in_1[0]);  // AND_Gate
  or O4 (out_2[4], I8_out, I6_out, I2_out, I0_out);
  and I6 (I6_out, ~in_1[3], in_1[2], in_1[1], ~in_1[0]);  // AND_Gate
  or O3 (out_2[3], I9_out, I8_out, I7_out, I4_out, I3_out, I2_out, I1_out, I0_out);
  and I5 (I5_out, ~in_1[3], in_1[2], ~in_1[1], in_1[0]);  // AND_Gate
  and I3 (I3_out, ~in_1[3], ~in_1[2], in_1[1], in_1[0]);  // AND_Gate
  and I4 (I4_out, ~in_1[3], in_1[2], ~in_1[1], ~in_1[0]);  // AND_Gate
  or O2 (out_2[2], I9_out, I8_out, I7_out, I6_out, I5_out, I3_out, I2_out, I0_out);
  and I2 (I2_out, ~in_1[3], ~in_1[2], in_1[1], ~in_1[0]);  // AND_Gate
  or O1 (out_2[1], I9_out, I8_out, I6_out, I5_out, I4_out, I0_out);
  and I1 (I1_out, ~in_1[3], ~in_1[2], ~in_1[1], in_1[0]);  // AND_Gate
  and I0 (I0_out, ~in_1[3], ~in_1[2], ~in_1[1], ~in_1[0]);  // AND_Gate
  or O0 (out_2[0], I9_out, I8_out, I6_out, I5_out, I4_out, I3_out, I2_out);
endmodule

module DOUBLE_DABBLE (
  input  [7:0] in_1,
  output [3:0] out_2,
  output [3:0] out_3,
  output [3:0] out_4
);

  wire dab_1_out_8, dab_2_out_6, dab_2_out_7, dab_2_out_8, dab_3_out_6, dab_3_out_7, dab_3_out_8,
       dab_4_out_6, dab_4_out_7, dab_4_out_8, dab_5_out_7, dab_5_out_8, dab_6_out_5, dab_6_out_6,
       dab_6_out_7, dab_6_out_8, dab_7_out_5, dab_7_out_6, dab_7_out_7, dab_7_out_8, dab_8_out_5,
       dab_8_out_6, dab_8_out_7, dab_8_out_8, dab_10_out_5, dab_10_out_6, dab_10_out_7, dab_10_out_8;

  DAB dab_1 (.in_2(1'b0), .in_4(in_1[7]), .in_1(1'b0), .in_3(1'b0), .out_8(dab_1_out_8));  // open: out_7, out_5, out_6
  DAB dab_2 (
    .out_7(dab_2_out_7), .in_4(dab_6_out_5), .out_5(out_2[3]), .out_6(dab_2_out_6), .out_8(dab_2_out_8));  // open: in_2, in_1, in_3
  DAB dab_3 (
    .out_7(dab_3_out_7), .in_2(dab_2_out_7), .in_4(dab_7_out_5), .out_5(out_2[2]), .in_1(dab_2_out_6),
    .out_6(dab_3_out_6), .in_3(dab_2_out_8), .out_8(dab_3_out_8));
  DAB dab_4 (
    .out_7(dab_4_out_7), .in_2(dab_3_out_7), .in_4(dab_8_out_5), .out_5(out_2[1]), .in_1(dab_3_out_6),
    .out_6(dab_4_out_6), .in_3(dab_3_out_8), .out_8(dab_4_out_8));
  DAB dab_5 (
    .out_7(dab_5_out_7), .in_4(in_1[6]), .in_3(dab_1_out_8), .out_8(dab_5_out_8));  // open: in_2, out_5, in_1, out_6
  DAB dab_6 (
    .out_7(dab_6_out_7), .in_2(dab_5_out_7), .in_4(in_1[5]), .out_5(dab_6_out_5), .out_6(dab_6_out_6),
    .in_3(dab_5_out_8), .out_8(dab_6_out_8));  // open: in_1
  DAB dab_7 (
    .out_7(dab_7_out_7), .in_2(dab_6_out_7), .in_4(in_1[4]), .out_5(dab_7_out_5), .in_1(dab_6_out_6),
    .out_6(dab_7_out_6), .in_3(dab_6_out_8), .out_8(dab_7_out_8));
  DAB dab_8 (
    .out_7(dab_8_out_7), .in_2(dab_7_out_7), .in_4(in_1[3]), .out_5(dab_8_out_5), .in_1(dab_7_out_6),
    .out_6(dab_8_out_6), .in_3(dab_7_out_8), .out_8(dab_8_out_8));
  DAB dab_9 (
    .out_7(out_3[2]), .in_2(dab_4_out_7), .in_4(dab_10_out_5), .out_5(out_2[0]), .in_1(dab_4_out_6),
    .out_6(out_3[3]), .in_3(dab_4_out_8), .out_8(out_3[1]));
  DAB dab_10 (
    .out_7(dab_10_out_7), .in_2(dab_8_out_7), .in_4(in_1[2]), .out_5(dab_10_out_5), .in_1(dab_8_out_6),
    .out_6(dab_10_out_6), .in_3(dab_8_out_8), .out_8(dab_10_out_8));
  DAB dab_11 (
    .out_7(out_4[2]), .in_2(dab_10_out_7), .in_4(in_1[1]), .out_5(out_3[0]), .in_1(dab_10_out_6),
    .out_6(out_4[3]), .in_3(dab_10_out_8), .out_8(out_4[1]));

  assign out_4[0] = in_1[0];
endmodule

module DAB (
  input  in_1,
  input  in_2,
  input  in_3,
  input  in_4,
  output out_5,
  output out_6,
  output out_7,
  output out_8
);

  wire and_1_out, and_2_out, and_3_out, and_4_out, and_5_out, and_6_out, or_1_out, or_2_out, or_3_out,
       or_4_out, xor_3_out;

  xor xor_1 (out_5, in_1, and_1_out);
  and and_1 (and_1_out, in_2, or_4_out);
  and and_2 (and_2_out, in_2, or_1_out);
  xor xor_2 (out_6, in_2, or_4_out);
  or or_1 (or_1_out, in_3, in_4);
  or or_2 (or_2_out, and_2_out, in_1);
  or or_3 (or_3_out, and_2_out, in_1);
  and and_3 (and_3_out, in_3, or_3_out);
  and and_4 (and_4_out, in_3, and_6_out);
  or or_4 (or_4_out, and_3_out, and_4_out, and_5_out);
  and and_5 (and_5_out, or_3_out, and_6_out);
  xor xor_3 (xor_3_out, or_3_out, and_6_out);
  xor xor_4 (out_7, in_3, xor_3_out);
  xor xor_5 (out_8, in_4, or_2_out);
  and and_6 (and_6_out, in_4, or_2_out);

  // Notes on the sheet:
  //   if 5, add 3
endmodule

module GEN_REGISTER (
  input  CLK_IN,
  input  On_Off_In,
  input  IN_OR_OUT,
  input  [7:0] DATA_IN,
  input  ADDR,
  output [7:0] DATA_OUT,
  output [7:0] CONTENTS
);

  wire and_1_out, and_2_out, and_3_out, and_4_out, and_5_out, and_6_out, and_7_out, and_8_out, and_10_out,
       and_11_out, and_12_out, and_13_out, and_14_out, and_15_out, and_16_out, and_17_out;

  and and_1 (and_1_out, DATA_IN[7], ~IN_OR_OUT, ADDR);  // AND_Gate
  S_R_Flip_Flop s_r_ff_1 (
    .S(and_1_out), .R(and_2_out), .clk(CLK_IN), .Q(CONTENTS[7]), .reset(On_Off_In));  // open: Qn, preset
  and and_2 (and_2_out, ~DATA_IN[7], ~IN_OR_OUT, ADDR);  // AND_Gate
  and and_3 (and_3_out, DATA_IN[6], ~IN_OR_OUT, ADDR);  // AND_Gate
  and and_4 (and_4_out, ~DATA_IN[6], ~IN_OR_OUT, ADDR);  // AND_Gate
  S_R_Flip_Flop s_r_ff_2 (
    .S(and_3_out), .R(and_4_out), .clk(CLK_IN), .Q(CONTENTS[6]), .reset(On_Off_In));  // open: Qn, preset
  and and_5 (and_5_out, DATA_IN[5], ~IN_OR_OUT, ADDR);  // AND_Gate
  S_R_Flip_Flop s_r_ff_3 (
    .S(and_5_out), .R(and_6_out), .clk(CLK_IN), .Q(CONTENTS[5]), .reset(On_Off_In));  // open: Qn, preset
  and and_6 (and_6_out, ~DATA_IN[5], ~IN_OR_OUT, ADDR);  // AND_Gate
  and and_7 (and_7_out, ~DATA_IN[4], ~IN_OR_OUT, ADDR);  // AND_Gate
  and and_8 (and_8_out, DATA_IN[4], ~IN_OR_OUT, ADDR);  // AND_Gate
  S_R_Flip_Flop s_r_ff_4 (
    .S(and_8_out), .R(and_7_out), .clk(CLK_IN), .Q(CONTENTS[4]), .reset(On_Off_In));  // open: Qn, preset
  assign DATA_OUT = {8{IN_OR_OUT}} & CONTENTS;  // AND_Gate and_9, 8 bits wide
  and and_10 (and_10_out, DATA_IN[3], ~IN_OR_OUT, ADDR);  // AND_Gate
  S_R_Flip_Flop s_r_ff_5 (
    .S(and_10_out), .R(and_11_out), .clk(CLK_IN), .Q(CONTENTS[3]), .reset(On_Off_In));  // open: Qn, preset
  and and_11 (and_11_out, ~DATA_IN[3], ~IN_OR_OUT, ADDR);  // AND_Gate
  and and_12 (and_12_out, DATA_IN[2], ~IN_OR_OUT, ADDR);  // AND_Gate
  S_R_Flip_Flop s_r_ff_6 (
    .S(and_12_out), .R(and_13_out), .clk(CLK_IN), .Q(CONTENTS[2]), .reset(On_Off_In));  // open: Qn, preset
  and and_13 (and_13_out, ~DATA_IN[2], ~IN_OR_OUT, ADDR);  // AND_Gate
  and and_14 (and_14_out, DATA_IN[1], ~IN_OR_OUT, ADDR);  // AND_Gate
  S_R_Flip_Flop s_r_ff_7 (
    .S(and_14_out), .R(and_15_out), .clk(CLK_IN), .Q(CONTENTS[1]), .reset(On_Off_In));  // open: Qn, preset
  and and_15 (and_15_out, ~DATA_IN[1], ~IN_OR_OUT, ADDR);  // AND_Gate
  and and_16 (and_16_out, DATA_IN[0], ~IN_OR_OUT, ADDR);  // AND_Gate
  S_R_Flip_Flop s_r_ff_8 (
    .S(and_16_out), .R(and_17_out), .clk(CLK_IN), .Q(CONTENTS[0]), .reset(On_Off_In));  // open: Qn, preset
  and and_17 (and_17_out, ~DATA_IN[0], ~IN_OR_OUT, ADDR);  // AND_Gate
endmodule

module KeyPad (
  input  Zero,
  input  One,
  input  Two,
  input  Three,
  input  Four,
  input  Five,
  input  Six,
  input  Seven,
  input  Eight,
  input  Nine,
  output [7:0] Output
);

  wire Active_out, and_1_out, nand_1_out, not_1_out, not_2_out, not_3_out, not_4_out, or_1_out, or_2_out,
       or_3_out, or_4_out, s_r_ff_2_q, s_r_ff_3_q, undriven, undriven_2, xnor_1_out;

  NotExactlyOne xnor_1 (
    .out(xnor_1_out), .in0(Zero), .in1(One), .in2(Two), .in3(Three), .in4(Four), .in5(Five), .in6(Six),
    .in7(Seven), .in8(Eight), .in9(Nine));
  nand nand_1 (nand_1_out, xnor_1_out, Active_out);
  or Active (Active_out, Nine, Eight, Seven, Six, Five, Four, Three, Two, One, Zero);
  buf and_1 (and_1_out, Active_out);  // AND_Gate
  or or_1 (or_1_out, One, Three, Five, Seven, Nine);
  not not_1 (not_1_out, or_1_out);
  and and_2 (Output[0], undriven, nand_1_out);
  and and_3 (Output[1], s_r_ff_2_q, nand_1_out);
  and and_4 (Output[2], s_r_ff_3_q, nand_1_out);
  and and_5 (Output[3], undriven_2, nand_1_out);
  S_R_Flip_Flop s_r_ff_1 (
    .S(or_1_out), .clk(or_1_out), .R(not_1_out), .preset(not_1_out), .reset(not_1_out));  // open: Q, Qn
  S_R_Flip_Flop s_r_ff_2 (.S(or_2_out), .R(not_2_out), .clk(and_1_out), .Q(s_r_ff_2_q));  // open: reset, Qn, preset
  or or_2 (or_2_out, Two, Three, Six, Seven);
  not not_2 (not_2_out, or_2_out);
  or or_3 (or_3_out, Four, Five, Six, Seven);
  not not_3 (not_3_out, or_3_out);
  S_R_Flip_Flop s_r_ff_3 (.S(or_3_out), .R(not_3_out), .clk(and_1_out), .Q(s_r_ff_3_q));  // open: reset, Qn, preset
  or or_4 (or_4_out, Eight, Nine);
  S_R_Flip_Flop s_r_ff_4 (
    .S(or_4_out), .clk(or_4_out), .R(not_4_out), .preset(not_4_out), .reset(not_4_out));  // open: Q, Qn
  not not_4 (not_4_out, or_4_out);

  assign Output[7:4] = 4'b0000;
endmodule

module DATA_BYTE (
  input  [7:0] Byte_In,
  input  CLK,
  input  NO_IN,
  output [7:0] Byte_Out
);

  wire and_1_out, and_2_out, and_3_out, and_4_out, and_5_out, and_6_out, and_7_out, and_8_out, and_9_out,
       and_10_out, and_11_out, and_12_out, and_13_out, and_14_out, and_15_out, and_16_out;

  S_R_Flip_Flop s_r_ff_1 (.S(and_1_out), .R(and_2_out), .clk(CLK), .Q(Byte_Out[0]));  // open: reset, Qn, preset
  and and_1 (and_1_out, ~NO_IN, Byte_In[0]);  // AND_Gate
  and and_2 (and_2_out, ~NO_IN, ~Byte_In[0]);  // AND_Gate
  and and_3 (and_3_out, ~NO_IN, Byte_In[1]);  // AND_Gate
  S_R_Flip_Flop s_r_ff_2 (.S(and_3_out), .R(and_4_out), .clk(CLK), .Q(Byte_Out[1]));  // open: reset, Qn, preset
  and and_4 (and_4_out, ~NO_IN, ~Byte_In[1]);  // AND_Gate
  S_R_Flip_Flop s_r_ff_3 (.S(and_5_out), .R(and_6_out), .clk(CLK), .Q(Byte_Out[2]));  // open: reset, Qn, preset
  and and_5 (and_5_out, ~NO_IN, Byte_In[2]);  // AND_Gate
  and and_6 (and_6_out, ~NO_IN, ~Byte_In[2]);  // AND_Gate
  and and_7 (and_7_out, ~NO_IN, Byte_In[3]);  // AND_Gate
  S_R_Flip_Flop s_r_ff_4 (.S(and_7_out), .R(and_8_out), .clk(CLK), .Q(Byte_Out[3]));  // open: reset, Qn, preset
  and and_8 (and_8_out, ~NO_IN, ~Byte_In[3]);  // AND_Gate
  S_R_Flip_Flop s_r_ff_5 (.S(and_9_out), .R(and_10_out), .clk(CLK), .Q(Byte_Out[4]));  // open: reset, Qn, preset
  and and_9 (and_9_out, ~NO_IN, Byte_In[4]);  // AND_Gate
  and and_10 (and_10_out, ~NO_IN, ~Byte_In[4]);  // AND_Gate
  and and_11 (and_11_out, ~NO_IN, Byte_In[5]);  // AND_Gate
  S_R_Flip_Flop s_r_ff_6 (.S(and_11_out), .R(and_12_out), .clk(CLK), .Q(Byte_Out[5]));  // open: reset, Qn, preset
  and and_12 (and_12_out, ~NO_IN, ~Byte_In[5]);  // AND_Gate
  S_R_Flip_Flop s_r_ff_7 (.S(and_13_out), .R(and_14_out), .clk(CLK), .Q(Byte_Out[6]));  // open: reset, Qn, preset
  and and_13 (and_13_out, ~NO_IN, Byte_In[6]);  // AND_Gate
  and and_14 (and_14_out, ~NO_IN, ~Byte_In[6]);  // AND_Gate
  and and_15 (and_15_out, ~NO_IN, Byte_In[7]);  // AND_Gate
  S_R_Flip_Flop s_r_ff_8 (.S(and_15_out), .R(and_16_out), .clk(CLK), .Q(Byte_Out[7]));  // open: reset, Qn, preset
  and and_16 (and_16_out, ~NO_IN, ~Byte_In[7]);  // AND_Gate
endmodule

module AR (
  input  CLK_IN,
  input  On_Off_In,
  input  IN_OR_OUT,
  input  [3:0] ADR_IN,
  output [3:0] ADR_OUT
);

  wire and_1_out, and_2_out, and_3_out, and_4_out, and_6_out, and_7_out, and_8_out, and_9_out;
  wire [3:0] s_r_ff_4_q;

  S_R_Flip_Flop s_r_ff_1 (
    .S(and_2_out), .R(and_1_out), .clk(CLK_IN), .Q(s_r_ff_4_q[3]), .reset(On_Off_In));  // open: Qn, preset
  and and_1 (and_1_out, ~IN_OR_OUT, ~ADR_IN[3]);  // AND_Gate
  and and_2 (and_2_out, ~IN_OR_OUT, ADR_IN[3]);  // AND_Gate
  S_R_Flip_Flop s_r_ff_2 (
    .S(and_3_out), .R(and_4_out), .clk(CLK_IN), .Q(s_r_ff_4_q[2]), .reset(On_Off_In));  // open: Qn, preset
  and and_3 (and_3_out, ~IN_OR_OUT, ADR_IN[2]);  // AND_Gate
  and and_4 (and_4_out, ~IN_OR_OUT, ~ADR_IN[2]);  // AND_Gate
  assign ADR_OUT = {4{IN_OR_OUT}} & s_r_ff_4_q;  // AND_Gate and_5, 4 bits wide
  and and_6 (and_6_out, ~IN_OR_OUT, ADR_IN[1]);  // AND_Gate
  S_R_Flip_Flop s_r_ff_3 (
    .S(and_6_out), .R(and_7_out), .clk(CLK_IN), .Q(s_r_ff_4_q[1]), .reset(On_Off_In));  // open: Qn, preset
  and and_7 (and_7_out, ~IN_OR_OUT, ~ADR_IN[1]);  // AND_Gate
  and and_8 (and_8_out, ~IN_OR_OUT, ADR_IN[0]);  // AND_Gate
  S_R_Flip_Flop s_r_ff_4 (
    .S(and_8_out), .R(and_9_out), .clk(CLK_IN), .Q(s_r_ff_4_q[0]), .reset(On_Off_In));  // open: Qn, preset
  and and_9 (and_9_out, ~IN_OR_OUT, ~ADR_IN[0]);  // AND_Gate

  // Notes on the sheet:
  //   in (receiving data) : 0
  //   out (outputting data) : 1
endmodule

module PC (
  input  IN_MODE,
  input  NO_IN,
  input  On_Off_In,
  input  CLK,
  input  [3:0] IN_1,
  input  [3:0] IN_0,
  output [3:0] OUT_0
);

  wire and_3_out, and_4_out, and_5_out, and_6_out, and_7_out, and_8_out, and_9_out, and_10_out;
  wire [3:0] and_1_out, and_2_out, or_1_out;

  assign and_1_out = {4{IN_MODE}} & IN_1;  // AND_Gate and_1, 4 bits wide
  assign or_1_out = and_1_out | and_2_out;  // OR_Gate or_1, 4 bits wide
  assign and_2_out = ~{4{IN_MODE}} & IN_0;  // AND_Gate and_2, 4 bits wide
  and and_3 (and_3_out, ~NO_IN, or_1_out[0]);  // AND_Gate
  and and_4 (and_4_out, ~or_1_out[0], ~NO_IN);  // AND_Gate
  and and_5 (and_5_out, ~NO_IN, or_1_out[1]);  // AND_Gate
  and and_6 (and_6_out, ~NO_IN, ~or_1_out[1]);  // AND_Gate
  and and_7 (and_7_out, ~NO_IN, or_1_out[2]);  // AND_Gate
  and and_8 (and_8_out, ~NO_IN, ~or_1_out[2]);  // AND_Gate
  and and_9 (and_9_out, ~NO_IN, or_1_out[3]);  // AND_Gate
  and and_10 (and_10_out, ~NO_IN, ~or_1_out[3]);  // AND_Gate
  S_R_Flip_Flop s_r_ff_1 (
    .S(and_3_out), .R(and_4_out), .clk(CLK), .Q(OUT_0[0]), .reset(On_Off_In));  // open: Qn, preset
  S_R_Flip_Flop s_r_ff_2 (
    .S(and_5_out), .R(and_6_out), .clk(CLK), .Q(OUT_0[1]), .reset(On_Off_In));  // open: Qn, preset
  S_R_Flip_Flop s_r_ff_3 (
    .S(and_7_out), .R(and_8_out), .clk(CLK), .Q(OUT_0[2]), .reset(On_Off_In));  // open: Qn, preset
  S_R_Flip_Flop s_r_ff_4 (
    .S(and_9_out), .R(and_10_out), .clk(CLK), .Q(OUT_0[3]), .reset(On_Off_In));  // open: Qn, preset

  // Notes on the sheet:
  //   Input from INC
  //   Input from IR
endmodule

module INC (
  input  ON_0,
  input  [3:0] IN_0,
  output [3:0] OUT_0
);

  wire half_adder_1_c_out, half_adder_2_c_out, half_adder_3_c_out;

  Half_Adder half_adder_1 (.A(IN_0[0]), .B(ON_0), .R(OUT_0[0]), .C_Out(half_adder_1_c_out));
  Half_Adder half_adder_2 (.A(IN_0[1]), .B(half_adder_1_c_out), .R(OUT_0[1]), .C_Out(half_adder_2_c_out));
  Half_Adder half_adder_3 (.A(IN_0[2]), .B(half_adder_2_c_out), .R(OUT_0[2]), .C_Out(half_adder_3_c_out));
  Half_Adder half_adder_4 (.A(IN_0[3]), .B(half_adder_3_c_out), .R(OUT_0[3]));  // open: C_Out
endmodule

module STATUS (
  input  [2:0] in_1,
  input  CLK,
  input  On_Off_In,
  output [2:0] out_4
);

  D_Flip_Flop d_ff_1 (.D(in_1[0]), .clk(CLK), .Q(out_4[0]), .reset(On_Off_In));  // open: Qn, preset
  D_Flip_Flop d_ff_2 (.D(in_1[1]), .clk(CLK), .Q(out_4[1]), .reset(On_Off_In));  // open: Qn, preset
  D_Flip_Flop d_ff_3 (.D(in_1[2]), .clk(CLK), .Q(out_4[2]), .reset(On_Off_In));  // open: Qn, preset
endmodule

module MBR (
  input  [7:0] IN_0,
  input  IN_MODE,
  input  CLK,
  input  On_Off_In,
  output [7:0] Contents,
  output [7:0] OUT_0
);

  wire and_1_out, and_2_out, and_3_out, and_4_out, and_5_out, and_6_out, and_7_out, and_8_out, and_9_out,
       and_10_out, and_11_out, and_12_out, and_14_out, and_15_out, and_16_out, and_17_out;

  and and_1 (and_1_out, IN_0[0], ~IN_MODE);  // AND_Gate
  and and_2 (and_2_out, ~IN_0[0], ~IN_MODE);  // AND_Gate
  S_R_Flip_Flop s_r_ff_1 (
    .S(and_1_out), .R(and_2_out), .clk(CLK), .Q(Contents[0]), .reset(On_Off_In));  // open: Qn, preset
  and and_3 (and_3_out, IN_0[1], ~IN_MODE);  // AND_Gate
  and and_4 (and_4_out, ~IN_0[1], ~IN_MODE);  // AND_Gate
  S_R_Flip_Flop s_r_ff_2 (
    .S(and_3_out), .R(and_4_out), .clk(CLK), .Q(Contents[1]), .reset(On_Off_In));  // open: Qn, preset
  and and_5 (and_5_out, IN_0[2], ~IN_MODE);  // AND_Gate
  and and_6 (and_6_out, ~IN_0[2], ~IN_MODE);  // AND_Gate
  S_R_Flip_Flop s_r_ff_3 (
    .S(and_5_out), .R(and_6_out), .clk(CLK), .Q(Contents[2]), .reset(On_Off_In));  // open: Qn, preset
  and and_7 (and_7_out, IN_0[3], ~IN_MODE);  // AND_Gate
  and and_8 (and_8_out, ~IN_0[3], ~IN_MODE);  // AND_Gate
  S_R_Flip_Flop s_r_ff_4 (
    .S(and_7_out), .R(and_8_out), .clk(CLK), .Q(Contents[3]), .reset(On_Off_In));  // open: Qn, preset
  and and_9 (and_9_out, IN_0[4], ~IN_MODE);  // AND_Gate
  S_R_Flip_Flop s_r_ff_5 (
    .S(and_9_out), .R(and_10_out), .clk(CLK), .Q(Contents[4]), .reset(On_Off_In));  // open: Qn, preset
  and and_10 (and_10_out, ~IN_0[4], ~IN_MODE);  // AND_Gate
  S_R_Flip_Flop s_r_ff_6 (
    .S(and_11_out), .R(and_12_out), .clk(CLK), .Q(Contents[5]), .reset(On_Off_In));  // open: Qn, preset
  and and_11 (and_11_out, IN_0[5], ~IN_MODE);  // AND_Gate
  and and_12 (and_12_out, ~IN_0[5], ~IN_MODE);  // AND_Gate
  assign OUT_0 = {8{IN_MODE}} & Contents;  // AND_Gate and_13, 8 bits wide
  and and_14 (and_14_out, IN_0[6], ~IN_MODE);  // AND_Gate
  S_R_Flip_Flop s_r_ff_7 (
    .S(and_14_out), .R(and_15_out), .clk(CLK), .Q(Contents[6]), .reset(On_Off_In));  // open: Qn, preset
  and and_15 (and_15_out, ~IN_0[6], ~IN_MODE);  // AND_Gate
  S_R_Flip_Flop s_r_ff_8 (
    .S(and_16_out), .R(and_17_out), .clk(CLK), .Q(Contents[7]), .reset(On_Off_In));  // open: Qn, preset
  and and_16 (and_16_out, IN_0[7], ~IN_MODE);  // AND_Gate
  and and_17 (and_17_out, ~IN_0[7], ~IN_MODE);  // AND_Gate

  // Notes on the sheet:
  //   0= IN
  //   1=OUT
endmodule

module COUNT (
  input  IN_MODE,
  input  NO_IN,
  input  CLK,
  input  [3:0] IN_1,
  input  [3:0] IN_0,
  output [3:0] OUT_0
);

  wire and_3_out, and_4_out, and_5_out, and_6_out, and_7_out, and_8_out, and_9_out, and_10_out;
  wire [3:0] and_1_out, and_2_out, or_1_out;

  assign and_1_out = {4{IN_MODE}} & IN_1;  // AND_Gate and_1, 4 bits wide
  assign or_1_out = and_1_out | and_2_out;  // OR_Gate or_1, 4 bits wide
  assign and_2_out = ~{4{IN_MODE}} & IN_0;  // AND_Gate and_2, 4 bits wide
  and and_3 (and_3_out, ~NO_IN, or_1_out[0]);  // AND_Gate
  and and_4 (and_4_out, ~or_1_out[0], ~NO_IN);  // AND_Gate
  and and_5 (and_5_out, ~NO_IN, or_1_out[1]);  // AND_Gate
  and and_6 (and_6_out, ~NO_IN, ~or_1_out[1]);  // AND_Gate
  and and_7 (and_7_out, ~NO_IN, or_1_out[2]);  // AND_Gate
  and and_8 (and_8_out, ~NO_IN, ~or_1_out[2]);  // AND_Gate
  and and_9 (and_9_out, ~NO_IN, or_1_out[3]);  // AND_Gate
  and and_10 (and_10_out, ~NO_IN, ~or_1_out[3]);  // AND_Gate
  S_R_Flip_Flop s_r_ff_1 (.S(and_3_out), .R(and_4_out), .clk(CLK), .Q(OUT_0[0]));  // open: reset, Qn, preset
  S_R_Flip_Flop s_r_ff_2 (.S(and_5_out), .R(and_6_out), .clk(CLK), .Q(OUT_0[1]));  // open: reset, Qn, preset
  S_R_Flip_Flop s_r_ff_3 (.S(and_7_out), .R(and_8_out), .clk(CLK), .Q(OUT_0[2]));  // open: reset, Qn, preset
  S_R_Flip_Flop s_r_ff_4 (.S(and_9_out), .R(and_10_out), .clk(CLK), .Q(OUT_0[3]));  // open: reset, Qn, preset

  // Notes on the sheet:
  //   Input from INC
  //   Input from IR
endmodule

module MAR (
  input  [3:0] InAdr,
  input  in_or_out,
  input  Clock,
  input  On_Off_In,
  output [7:0] OutAdr,
  output [7:0] Contents
);

  wire and_1_out, and_2_out, and_3_out, and_4_out, and_5_out, and_6_out, and_7_out, and_8_out;

  S_R_Flip_Flop s_r_ff_1 (
    .S(and_1_out), .R(and_2_out), .clk(Clock), .Q(Contents[0]), .reset(On_Off_In));  // open: Qn, preset
  and and_1 (and_1_out, InAdr[0], ~in_or_out);  // AND_Gate
  and and_2 (and_2_out, ~InAdr[0], ~in_or_out);  // AND_Gate
  S_R_Flip_Flop s_r_ff_2 (
    .S(and_3_out), .R(and_4_out), .clk(Clock), .Q(Contents[1]), .reset(On_Off_In));  // open: Qn, preset
  and and_3 (and_3_out, InAdr[1], ~in_or_out);  // AND_Gate
  and and_4 (and_4_out, ~InAdr[1], ~in_or_out);  // AND_Gate
  S_R_Flip_Flop s_r_ff_3 (
    .S(and_5_out), .R(and_6_out), .clk(Clock), .Q(Contents[2]), .reset(On_Off_In));  // open: Qn, preset
  and and_5 (and_5_out, InAdr[2], ~in_or_out);  // AND_Gate
  and and_6 (and_6_out, ~InAdr[2], ~in_or_out);  // AND_Gate
  S_R_Flip_Flop s_r_ff_4 (
    .S(and_7_out), .R(and_8_out), .clk(Clock), .Q(Contents[3]), .reset(On_Off_In));  // open: Qn, preset
  and and_7 (and_7_out, InAdr[3], ~in_or_out);  // AND_Gate
  and and_8 (and_8_out, ~InAdr[3], ~in_or_out);  // AND_Gate
  and and_9 (OutAdr[0], Contents[0], in_or_out);
  and and_10 (OutAdr[1], Contents[1], in_or_out);
  and and_11 (OutAdr[2], Contents[2], in_or_out);
  and and_12 (OutAdr[3], Contents[3], in_or_out);

  assign Contents[7:4] = 4'b0000;
  assign OutAdr[7:4] = 4'b0000;
endmodule

module EQ (
  input  [7:0] IN_1,
  input  [7:0] IN_0,
  output EQ
);

  wire and_1_out, and_2_out, and_3_out, and_4_out, and_5_out, and_6_out, and_7_out, and_8_out, and_9_out,
       and_10_out, and_11_out, and_12_out, and_13_out, and_14_out, and_15_out, and_16_out, or_1_out,
       or_2_out, or_3_out, or_4_out, or_5_out, or_6_out, or_7_out, or_8_out;

  and and_1 (and_1_out, IN_1[0], IN_0[0]);
  or or_1 (or_1_out, and_1_out, and_2_out);
  and and_2 (and_2_out, ~IN_1[0], ~IN_0[0]);  // AND_Gate
  and and_3 (and_3_out, IN_1[1], IN_0[1]);
  or or_2 (or_2_out, and_3_out, and_4_out);
  and and_4 (and_4_out, ~IN_1[1], ~IN_0[1]);  // AND_Gate
  and and_5 (and_5_out, IN_1[2], IN_0[2]);
  or or_3 (or_3_out, and_5_out, and_6_out);
  and and_6 (and_6_out, ~IN_1[2], ~IN_0[2]);  // AND_Gate
  and and_7 (and_7_out, IN_1[3], IN_0[3]);
  or or_4 (or_4_out, and_7_out, and_8_out);
  and and_8 (and_8_out, ~IN_1[3], ~IN_0[3]);  // AND_Gate
  and and_9 (and_9_out, IN_1[4], IN_0[4]);
  or or_5 (or_5_out, and_9_out, and_10_out);
  and and_10 (and_10_out, ~IN_1[4], ~IN_0[4]);  // AND_Gate
  and and_11 (and_11_out, IN_1[5], IN_0[5]);
  or or_6 (or_6_out, and_11_out, and_12_out);
  and and_12 (and_12_out, ~IN_1[5], ~IN_0[5]);  // AND_Gate
  and and_13 (and_13_out, IN_1[6], IN_0[6]);
  or or_7 (or_7_out, and_13_out, and_14_out);
  and and_14 (and_14_out, ~IN_1[6], ~IN_0[6]);  // AND_Gate
  and and_15 (and_15_out, IN_1[7], IN_0[7]);
  or or_8 (or_8_out, and_15_out, and_16_out);
  and and_16 (and_16_out, ~IN_1[7], ~IN_0[7]);  // AND_Gate
  and and_17 (EQ, or_1_out, or_2_out, or_3_out, or_4_out, or_5_out, or_6_out, or_7_out, or_8_out);
endmodule

module PROG_ROM (
  input  ROM_ON,
  input  [3:0] PROG,
  output [31:0] ROM_OUT_0000_0011,
  output [31:0] ROM_OUT_0100_0111,
  output [31:0] ROM_OUT_1000_1011,
  output [31:0] ROM_OUT_1100_1111
);

  wire [3:0] not_1_out;
  wire [3:3] and_1_out, and_2_out;
  wire [31:0] countdown_1_out_3, countdown_1_out_4, countdown_1_out_5, countdown_1_out_6, mult_input_1_out_3,
       mult_input_1_out_4, mult_input_1_out_5, mult_input_1_out_6, req_program_1_out_3, req_program_1_out_4,
       req_program_1_out_5, req_program_1_out_6;

  assign not_1_out = ~PROG;  // NOT_Gate not_1, 4 bits wide
  and and_1 (and_1_out[3], PROG[0], ~PROG[1], ~PROG[2], ~PROG[3]);  // AND_Gate
  and and_2 (and_2_out[3], ~PROG[0], PROG[1], ~PROG[2], ~PROG[3]);  // AND_Gate
  REQ_PROGRAM req_program_1 (
    .out_4(req_program_1_out_4), .out_5(req_program_1_out_5), .Address(not_1_out),
    .out_3(req_program_1_out_3), .out_6(req_program_1_out_6), .ON(ROM_ON));
  MULT_INPUT mult_input_1 (
    .out_6(mult_input_1_out_6), .Address({4{and_1_out[3]}}), .out_5(mult_input_1_out_5), .ON(ROM_ON),
    .out_4(mult_input_1_out_4), .out_3(mult_input_1_out_3));
  Countdown countdown_1 (
    .ON(ROM_ON), .Address({4{and_2_out[3]}}), .out_3(countdown_1_out_3), .out_4(countdown_1_out_4),
    .out_5(countdown_1_out_5), .out_6(countdown_1_out_6));
  assign ROM_OUT_0000_0011 = req_program_1_out_3 | mult_input_1_out_3 | countdown_1_out_3;  // OR_Gate or_1, 32 bits wide
  assign ROM_OUT_0100_0111 = req_program_1_out_4 | mult_input_1_out_4 | countdown_1_out_4;  // OR_Gate or_2, 32 bits wide
  assign ROM_OUT_1000_1011 = req_program_1_out_5 | mult_input_1_out_5 | countdown_1_out_5;  // OR_Gate or_3, 32 bits wide
  assign ROM_OUT_1100_1111 = req_program_1_out_6 | mult_input_1_out_6 | countdown_1_out_6;  // OR_Gate or_4, 32 bits wide

  // Notes on the sheet:
  //   Will output ROM vals
  //   Should be AND with CPU OFF
  //   Address of program we want to load
  //   0000
  //   0001
endmodule

module REQ_PROGRAM (
  input  ON,
  input  [3:0] Address,
  output [31:0] out_3,
  output [31:0] out_4,
  output [31:0] out_5,
  output [31:0] out_6
);

  wire ADDR_TRUE_out;
  wire [7:0] not_15_out;
  wire [22:0] not_1_out;
  wire [28:2] not_69_out;
  wire [30:0] not_23_out;
  wire [31:1] not_49_out;

  and ADDR_TRUE (ADDR_TRUE_out, Address[0], Address[1], Address[2], Address[3]);
  and ON_AND_ADDR (not_49_out[31], ON, ADDR_TRUE_out);
  not not_1 (not_1_out[0], not_49_out[31]);
  not not_2 (not_1_out[1], not_49_out[31]);
  not not_3 (not_1_out[2], not_49_out[31]);
  not not_4 (not_1_out[7], not_49_out[31]);
  not not_5 (not_1_out[11], not_49_out[31]);
  not not_6 (not_1_out[13], not_49_out[31]);
  not not_7 (not_1_out[15], not_49_out[31]);
  not not_8 (not_1_out[16], not_49_out[31]);
  not not_9 (not_1_out[17], not_49_out[31]);
  not not_10 (not_1_out[18], not_49_out[31]);
  not not_11 (not_1_out[19], not_49_out[31]);
  not not_12 (not_1_out[20], not_49_out[31]);
  not not_13 (not_1_out[21], not_49_out[31]);
  not not_14 (not_1_out[22], not_49_out[31]);
  not not_15 (not_15_out[0], not_49_out[31]);
  not not_16 (not_15_out[1], not_49_out[31]);
  not not_17 (not_15_out[2], not_49_out[31]);
  not not_18 (not_15_out[3], not_49_out[31]);
  not not_19 (not_15_out[4], not_49_out[31]);
  not not_20 (not_15_out[5], not_49_out[31]);
  not not_21 (not_15_out[6], not_49_out[31]);
  not not_22 (not_15_out[7], not_49_out[31]);
  not not_23 (not_23_out[0], not_49_out[31]);
  not not_24 (not_23_out[1], not_49_out[31]);
  not not_25 (not_23_out[2], not_49_out[31]);
  not not_26 (not_23_out[3], not_49_out[31]);
  not not_27 (not_23_out[4], not_49_out[31]);
  not not_28 (not_23_out[5], not_49_out[31]);
  not not_29 (not_23_out[6], not_49_out[31]);
  not not_30 (not_23_out[7], not_49_out[31]);
  not not_31 (not_23_out[8], not_49_out[31]);
  not not_32 (not_23_out[11], not_49_out[31]);
  not not_33 (not_23_out[12], not_49_out[31]);
  not not_34 (not_23_out[13], not_49_out[31]);
  not not_35 (not_23_out[14], not_49_out[31]);
  not not_36 (not_23_out[15], not_49_out[31]);
  not not_37 (not_23_out[17], not_49_out[31]);
  not not_38 (not_23_out[18], not_49_out[31]);
  not not_39 (not_23_out[19], not_49_out[31]);
  not not_40 (not_23_out[20], not_49_out[31]);
  not not_41 (not_23_out[21], not_49_out[31]);
  not not_42 (not_23_out[22], not_49_out[31]);
  not not_43 (not_23_out[23], not_49_out[31]);
  not not_44 (not_23_out[24], not_49_out[31]);
  not not_45 (not_23_out[25], not_49_out[31]);
  not not_46 (not_23_out[27], not_49_out[31]);
  not not_47 (not_23_out[28], not_49_out[31]);
  not not_48 (not_23_out[30], not_49_out[31]);
  not not_49 (not_49_out[1], not_49_out[31]);
  not not_50 (not_49_out[3], not_49_out[31]);
  not not_51 (not_49_out[6], not_49_out[31]);
  not not_52 (not_49_out[8], not_49_out[31]);
  not not_53 (not_49_out[9], not_49_out[31]);
  not not_54 (not_49_out[10], not_49_out[31]);
  not not_55 (not_49_out[11], not_49_out[31]);
  not not_56 (not_49_out[12], not_49_out[31]);
  not not_57 (not_49_out[14], not_49_out[31]);
  not not_58 (not_49_out[15], not_49_out[31]);
  not not_59 (not_49_out[16], not_49_out[31]);
  not not_60 (not_49_out[17], not_49_out[31]);
  not not_61 (not_49_out[18], not_49_out[31]);
  not not_62 (not_49_out[19], not_49_out[31]);
  not not_63 (not_49_out[20], not_49_out[31]);
  not not_64 (not_49_out[23], not_49_out[31]);
  not not_65 (not_49_out[24], not_49_out[31]);
  not not_66 (not_49_out[25], not_49_out[31]);
  not not_67 (not_49_out[27], not_49_out[31]);
  not not_68 (not_49_out[28], not_49_out[31]);
  not not_69 (not_69_out[2], not_49_out[31]);
  not not_70 (not_69_out[3], not_49_out[31]);
  not not_71 (not_69_out[4], not_49_out[31]);
  not not_72 (not_69_out[6], not_49_out[31]);
  not not_73 (not_69_out[8], not_49_out[31]);
  not not_74 (not_69_out[11], not_49_out[31]);
  not not_75 (not_69_out[14], not_49_out[31]);
  not not_76 (not_69_out[16], not_49_out[31]);
  not not_77 (not_69_out[17], not_49_out[31]);
  not not_78 (not_69_out[18], not_49_out[31]);
  not not_79 (not_69_out[19], not_49_out[31]);
  not not_80 (not_69_out[20], not_49_out[31]);
  not not_81 (not_69_out[22], not_49_out[31]);
  not not_82 (not_69_out[23], not_49_out[31]);
  not not_83 (not_69_out[26], not_49_out[31]);
  not not_84 (not_69_out[27], not_49_out[31]);
  not not_85 (not_69_out[28], not_49_out[31]);
  assign out_3 = {not_15_out, not_49_out[31], not_1_out[22:15], not_49_out[31], not_1_out[13], not_49_out[31], not_1_out[11], {3{not_49_out[31]}}, not_1_out[7], {4{not_49_out[31]}}, not_1_out[2:0]} & {32{not_49_out[31]}};  // AND_Gate and_1, 32 bits wide
  assign out_4 = {not_49_out[31], not_23_out[30], not_49_out[31], not_23_out[28:27], not_49_out[31], not_23_out[25:17], not_49_out[31], not_23_out[15:11], {2{not_49_out[31]}}, not_23_out[8:0]} & {32{not_49_out[31]}};  // AND_Gate and_2, 32 bits wide
  assign out_5 = {{3{not_49_out[31]}}, not_49_out[28:27], not_49_out[31], not_49_out[25:23], {2{not_49_out[31]}}, not_49_out[20:14], not_49_out[31], not_49_out[12:8], not_49_out[31], not_49_out[6], {2{not_49_out[31]}}, not_49_out[3], not_49_out[31], not_49_out[1], not_49_out[31]} & {32{not_49_out[31]}};  // AND_Gate and_3, 32 bits wide
  assign out_6 = {{3{not_49_out[31]}}, not_69_out[28:26], {2{not_49_out[31]}}, not_69_out[23:22], not_49_out[31], not_69_out[20:16], not_49_out[31], not_69_out[14], {2{not_49_out[31]}}, not_69_out[11], {2{not_49_out[31]}}, not_69_out[8], not_49_out[31], not_69_out[6], not_49_out[31], not_69_out[4:2], {2{not_49_out[31]}}} & {32{not_49_out[31]}};  // AND_Gate and_4, 32 bits wide
endmodule

module MULT (
  input  [7:0] IN_0,
  input  [7:0] IN_1,
  output [7:0] ANS,
  output OVERFLOW
);

  wire A0_c_out, A1_0_c_out, A1_0_r, A1_1_c_out, A1_C_c_out, A1_C_r, A2_0_c_out, A2_0_r, A2_1_c_out,
       A2_C_c_out, A2_C_r, A3_0_c_out, A3_0_r, A3_1_c_out, A3_1_r, A3_2_c_out, A3_C_0_c_out, A3_C_0_r,
       A3_C_1_c_out, A3_C_1_r, A4_0_c_out, A4_0_r, A4_1_c_out, A4_1_r, A4_2_c_out, A4_C_0_c_out, A4_C_0_r,
       A4_C_1_c_out, A4_C_1_r, A5_0_c_out, A5_0_r, A5_1_c_out, A5_1_r, A5_2_c_out, A5_2_r, A5_3_c_out,
       A5_C_0_c_out, A5_C_0_r, A5_C_1_c_out, A5_C_1_r, A5_C_2_c_out, A5_C_2_r, A6_0_c_out, A6_0_r,
       A6_1_c_out, A6_1_r, A6_2_c_out, A6_2_r, A6_3_c_out, OVERFLOW_out;
  wire [7:0] M1_out, M2_out, M3_out, M4_out, M5_out, M6_out, M7_out;
  wire [7:1] M0_out;

  assign {M0_out, ANS[0]} = IN_0 & {8{IN_1[0]}};  // AND_Gate M0, 8 bits wide
  assign M1_out = IN_0 & {8{IN_1[1]}};  // AND_Gate M1, 8 bits wide
  assign M2_out = IN_0 & {8{IN_1[2]}};  // AND_Gate M2, 8 bits wide
  assign M3_out = IN_0 & {8{IN_1[3]}};  // AND_Gate M3, 8 bits wide
  assign M4_out = IN_0 & {8{IN_1[4]}};  // AND_Gate M4, 8 bits wide
  assign M5_out = IN_0 & {8{IN_1[5]}};  // AND_Gate M5, 8 bits wide
  assign M6_out = IN_0 & {8{IN_1[6]}};  // AND_Gate M6, 8 bits wide
  assign M7_out = IN_0 & {8{IN_1[7]}};  // AND_Gate M7, 8 bits wide
  or u_OVERFLOW (OVERFLOW_out, M1_out[7], M2_out[7], M2_out[6], M3_out[7], M3_out[6], M3_out[5], M4_out[7], M4_out[6], M4_out[5], M4_out[4], M5_out[7], M5_out[6], M5_out[5], M5_out[4], M5_out[3], M6_out[7], M6_out[6], M6_out[5], M6_out[4], M6_out[3], M6_out[2], M7_out[7], M7_out[6], M7_out[5], M7_out[4], M7_out[3], M7_out[2], M7_out[1], A6_0_c_out, A6_1_c_out, A6_3_c_out, A5_C_1_c_out);
  or or_1 (OVERFLOW, OVERFLOW_out, A6_2_c_out, A5_C_0_c_out, A5_C_2_c_out);
  Half_Adder A0 (.A(M0_out[1]), .B(M1_out[0]), .R(ANS[1]), .C_Out(A0_c_out));
  Full_Adder A1_0 (.A(M0_out[2]), .B(M1_out[1]), .C_In(A0_c_out), .R(A1_0_r), .C_Out(A1_0_c_out));
  Half_Adder A1_1 (.A(A1_0_r), .B(M2_out[0]), .R(ANS[2]), .C_Out(A1_1_c_out));
  Half_Adder A1_C (.A(A1_1_c_out), .B(A1_0_c_out), .R(A1_C_r), .C_Out(A1_C_c_out));
  Full_Adder A2_0 (.A(M0_out[3]), .B(M1_out[2]), .C_In(A1_C_r), .R(A2_0_r), .C_Out(A2_0_c_out));
  Full_Adder A2_1 (.A(A2_0_r), .B(M2_out[1]), .C_In(M3_out[0]), .R(ANS[3]), .C_Out(A2_1_c_out));
  Full_Adder A3_0 (.A(M0_out[4]), .B(M1_out[3]), .C_In(M2_out[2]), .R(A3_0_r), .C_Out(A3_0_c_out));
  Full_Adder A2_C (.A(A1_C_c_out), .B(A2_0_c_out), .C_In(A2_1_c_out), .R(A2_C_r), .C_Out(A2_C_c_out));
  Full_Adder A3_1 (.A(M3_out[1]), .B(M4_out[0]), .C_In(A2_C_r), .R(A3_1_r), .C_Out(A3_1_c_out));
  Half_Adder A3_2 (.A(A3_0_r), .B(A3_1_r), .R(ANS[4]), .C_Out(A3_2_c_out));
  Full_Adder A3_C_0 (.A(A3_0_c_out), .B(A2_C_c_out), .C_In(A3_2_c_out), .R(A3_C_0_r), .C_Out(A3_C_0_c_out));
  Half_Adder A3_C_1 (.A(A3_C_0_r), .B(A3_1_c_out), .R(A3_C_1_r), .C_Out(A3_C_1_c_out));
  Full_Adder A4_0 (.A(M0_out[5]), .B(M1_out[4]), .C_In(M2_out[3]), .R(A4_0_r), .C_Out(A4_0_c_out));
  Full_Adder A4_1 (.A(A4_0_r), .B(M3_out[2]), .C_In(M4_out[1]), .R(A4_1_r), .C_Out(A4_1_c_out));
  Full_Adder A4_C_0 (.A(A3_C_0_c_out), .B(A3_C_1_c_out), .C_In(A4_0_c_out), .R(A4_C_0_r), .C_Out(A4_C_0_c_out));
  Full_Adder A4_2 (.A(A4_1_r), .B(A3_C_1_r), .C_In(M5_out[0]), .R(ANS[5]), .C_Out(A4_2_c_out));
  Full_Adder A4_C_1 (.A(A4_C_0_r), .B(A4_1_c_out), .C_In(A4_2_c_out), .R(A4_C_1_r), .C_Out(A4_C_1_c_out));
  Full_Adder A5_0 (.A(M0_out[6]), .B(M1_out[5]), .C_In(M2_out[4]), .R(A5_0_r), .C_Out(A5_0_c_out));
  Full_Adder A5_1 (.A(M3_out[3]), .B(M4_out[2]), .C_In(M5_out[1]), .R(A5_1_r), .C_Out(A5_1_c_out));
  Full_Adder A5_2 (.A(A5_0_r), .B(A5_1_r), .C_In(M6_out[0]), .R(A5_2_r), .C_Out(A5_2_c_out));
  Full_Adder A5_C_0 (.A(A4_C_1_c_out), .B(A4_C_0_c_out), .C_In(A5_1_c_out), .R(A5_C_0_r), .C_Out(A5_C_0_c_out));
  Full_Adder A6_0 (.A(M0_out[7]), .B(M1_out[6]), .C_In(M2_out[5]), .R(A6_0_r), .C_Out(A6_0_c_out));
  Half_Adder A5_3 (.A(A5_2_r), .B(A4_C_1_r), .R(ANS[6]), .C_Out(A5_3_c_out));
  Full_Adder A6_1 (.A(A6_0_r), .B(M3_out[4]), .C_In(M4_out[3]), .R(A6_1_r), .C_Out(A6_1_c_out));
  Full_Adder A5_C_1 (.A(A5_2_c_out), .B(A5_3_c_out), .C_In(A5_C_0_r), .R(A5_C_1_r), .C_Out(A5_C_1_c_out));
  Half_Adder A5_C_2 (.A(A5_0_c_out), .B(A5_C_1_r), .R(A5_C_2_r), .C_Out(A5_C_2_c_out));
  Full_Adder A6_2 (.A(M5_out[2]), .B(M6_out[1]), .C_In(A6_1_r), .R(A6_2_r), .C_Out(A6_2_c_out));
  Full_Adder A6_3 (.A(A6_2_r), .B(M7_out[0]), .C_In(A5_C_2_r), .R(ANS[7]), .C_Out(A6_3_c_out));
endmodule

module DATA_BYTE_ONOFF (
  input  [7:0] Byte_In,
  input  CLK,
  input  NO_IN,
  input  On_Off_In,
  output [7:0] Byte_Out
);

  wire and_1_out, and_2_out, and_3_out, and_4_out, and_5_out, and_6_out, and_7_out, and_8_out, and_9_out,
       and_10_out, and_11_out, and_12_out, and_13_out, and_14_out, and_15_out, and_16_out;

  and and_1 (and_1_out, ~NO_IN, Byte_In[0]);  // AND_Gate
  S_R_Flip_Flop s_r_ff_1 (
    .S(and_1_out), .R(and_2_out), .clk(CLK), .Q(Byte_Out[0]), .reset(On_Off_In));  // open: Qn, preset
  and and_2 (and_2_out, ~NO_IN, ~Byte_In[0]);  // AND_Gate
  S_R_Flip_Flop s_r_ff_2 (
    .S(and_3_out), .R(and_4_out), .clk(CLK), .Q(Byte_Out[1]), .reset(On_Off_In));  // open: Qn, preset
  and and_3 (and_3_out, ~NO_IN, Byte_In[1]);  // AND_Gate
  and and_4 (and_4_out, ~NO_IN, ~Byte_In[1]);  // AND_Gate
  S_R_Flip_Flop s_r_ff_3 (
    .S(and_5_out), .R(and_6_out), .clk(CLK), .Q(Byte_Out[2]), .reset(On_Off_In));  // open: Qn, preset
  and and_5 (and_5_out, ~NO_IN, Byte_In[2]);  // AND_Gate
  and and_6 (and_6_out, ~NO_IN, ~Byte_In[2]);  // AND_Gate
  and and_7 (and_7_out, ~NO_IN, Byte_In[3]);  // AND_Gate
  S_R_Flip_Flop s_r_ff_4 (
    .S(and_7_out), .R(and_8_out), .clk(CLK), .Q(Byte_Out[3]), .reset(On_Off_In));  // open: Qn, preset
  and and_8 (and_8_out, ~NO_IN, ~Byte_In[3]);  // AND_Gate
  S_R_Flip_Flop s_r_ff_5 (
    .S(and_9_out), .R(and_10_out), .clk(CLK), .Q(Byte_Out[4]), .reset(On_Off_In));  // open: Qn, preset
  and and_9 (and_9_out, ~NO_IN, Byte_In[4]);  // AND_Gate
  and and_10 (and_10_out, ~NO_IN, ~Byte_In[4]);  // AND_Gate
  S_R_Flip_Flop s_r_ff_6 (
    .S(and_11_out), .R(and_12_out), .clk(CLK), .Q(Byte_Out[5]), .reset(On_Off_In));  // open: Qn, preset
  and and_11 (and_11_out, ~NO_IN, Byte_In[5]);  // AND_Gate
  and and_12 (and_12_out, ~NO_IN, ~Byte_In[5]);  // AND_Gate
  and and_13 (and_13_out, ~NO_IN, Byte_In[6]);  // AND_Gate
  S_R_Flip_Flop s_r_ff_7 (
    .S(and_13_out), .R(and_14_out), .clk(CLK), .Q(Byte_Out[6]), .reset(On_Off_In));  // open: Qn, preset
  and and_14 (and_14_out, ~NO_IN, ~Byte_In[6]);  // AND_Gate
  S_R_Flip_Flop s_r_ff_8 (
    .S(and_15_out), .R(and_16_out), .clk(CLK), .Q(Byte_Out[7]), .reset(On_Off_In));  // open: Qn, preset
  and and_15 (and_15_out, ~NO_IN, Byte_In[7]);  // AND_Gate
  and and_16 (and_16_out, ~NO_IN, ~Byte_In[7]);  // AND_Gate
endmodule

module MULT_INPUT (
  input  ON,
  input  [3:0] Address,
  output [31:0] out_3,
  output [31:0] out_4,
  output [31:0] out_5,
  output [31:0] out_6
);

  wire ADDR_TRUE_out;
  wire [7:0] not_13_out;
  wire [23:0] not_1_out;
  wire [31:0] not_20_out, not_52_out, not_84_out;

  and ADDR_TRUE (ADDR_TRUE_out, Address[0], Address[1], Address[2], Address[3]);
  and ON_AND_ADDR (not_13_out[7], ON, ADDR_TRUE_out);
  not not_1 (not_1_out[0], not_13_out[7]);
  not not_2 (not_1_out[1], not_13_out[7]);
  not not_3 (not_1_out[2], not_13_out[7]);
  not not_4 (not_1_out[7], not_13_out[7]);
  not not_5 (not_1_out[8], not_13_out[7]);
  not not_6 (not_1_out[13], not_13_out[7]);
  not not_7 (not_1_out[14], not_13_out[7]);
  not not_8 (not_1_out[16], not_13_out[7]);
  not not_9 (not_1_out[17], not_13_out[7]);
  not not_10 (not_1_out[18], not_13_out[7]);
  not not_11 (not_1_out[20], not_13_out[7]);
  not not_12 (not_1_out[23], not_13_out[7]);
  not not_13 (not_13_out[0], not_13_out[7]);
  not not_14 (not_13_out[1], not_13_out[7]);
  not not_15 (not_13_out[2], not_13_out[7]);
  not not_16 (not_13_out[3], not_13_out[7]);
  not not_17 (not_13_out[4], not_13_out[7]);
  not not_18 (not_13_out[5], not_13_out[7]);
  not not_19 (not_13_out[6], not_13_out[7]);
  not not_20 (not_20_out[0], not_13_out[7]);
  not not_21 (not_20_out[1], not_13_out[7]);
  not not_22 (not_20_out[2], not_13_out[7]);
  not not_23 (not_20_out[3], not_13_out[7]);
  not not_24 (not_20_out[4], not_13_out[7]);
  not not_25 (not_20_out[5], not_13_out[7]);
  not not_26 (not_20_out[6], not_13_out[7]);
  not not_27 (not_20_out[7], not_13_out[7]);
  not not_28 (not_20_out[8], not_13_out[7]);
  not not_29 (not_20_out[9], not_13_out[7]);
  not not_30 (not_20_out[10], not_13_out[7]);
  not not_31 (not_20_out[11], not_13_out[7]);
  not not_32 (not_20_out[12], not_13_out[7]);
  not not_33 (not_20_out[13], not_13_out[7]);
  not not_34 (not_20_out[14], not_13_out[7]);
  not not_35 (not_20_out[15], not_13_out[7]);
  not not_36 (not_20_out[16], not_13_out[7]);
  not not_37 (not_20_out[17], not_13_out[7]);
  not not_38 (not_20_out[18], not_13_out[7]);
  not not_39 (not_20_out[19], not_13_out[7]);
  not not_40 (not_20_out[20], not_13_out[7]);
  not not_41 (not_20_out[21], not_13_out[7]);
  not not_42 (not_20_out[22], not_13_out[7]);
  not not_43 (not_20_out[23], not_13_out[7]);
  not not_44 (not_20_out[24], not_13_out[7]);
  not not_45 (not_20_out[25], not_13_out[7]);
  not not_46 (not_20_out[26], not_13_out[7]);
  not not_47 (not_20_out[27], not_13_out[7]);
  not not_48 (not_20_out[28], not_13_out[7]);
  not not_49 (not_20_out[29], not_13_out[7]);
  not not_50 (not_20_out[30], not_13_out[7]);
  not not_51 (not_20_out[31], not_13_out[7]);
  not not_52 (not_52_out[0], not_13_out[7]);
  not not_53 (not_52_out[1], not_13_out[7]);
  not not_54 (not_52_out[2], not_13_out[7]);
  not not_55 (not_52_out[3], not_13_out[7]);
  not not_56 (not_52_out[4], not_13_out[7]);
  not not_57 (not_52_out[5], not_13_out[7]);
  not not_58 (not_52_out[6], not_13_out[7]);
  not not_59 (not_52_out[7], not_13_out[7]);
  not not_60 (not_52_out[8], not_13_out[7]);
  not not_61 (not_52_out[9], not_13_out[7]);
  not not_62 (not_52_out[10], not_13_out[7]);
  not not_63 (not_52_out[11], not_13_out[7]);
  not not_64 (not_52_out[12], not_13_out[7]);
  not not_65 (not_52_out[13], not_13_out[7]);
  not not_66 (not_52_out[14], not_13_out[7]);
  not not_67 (not_52_out[15], not_13_out[7]);
  not not_68 (not_52_out[16], not_13_out[7]);
  not not_69 (not_52_out[17], not_13_out[7]);
  not not_70 (not_52_out[18], not_13_out[7]);
  not not_71 (not_52_out[19], not_13_out[7]);
  not not_72 (not_52_out[20], not_13_out[7]);
  not not_73 (not_52_out[21], not_13_out[7]);
  not not_74 (not_52_out[22], not_13_out[7]);
  not not_75 (not_52_out[23], not_13_out[7]);
  not not_76 (not_52_out[24], not_13_out[7]);
  not not_77 (not_52_out[25], not_13_out[7]);
  not not_78 (not_52_out[26], not_13_out[7]);
  not not_79 (not_52_out[27], not_13_out[7]);
  not not_80 (not_52_out[28], not_13_out[7]);
  not not_81 (not_52_out[29], not_13_out[7]);
  not not_82 (not_52_out[30], not_13_out[7]);
  not not_83 (not_52_out[31], not_13_out[7]);
  not not_84 (not_84_out[0], not_13_out[7]);
  not not_85 (not_84_out[1], not_13_out[7]);
  not not_86 (not_84_out[2], not_13_out[7]);
  not not_87 (not_84_out[3], not_13_out[7]);
  not not_88 (not_84_out[4], not_13_out[7]);
  not not_89 (not_84_out[5], not_13_out[7]);
  not not_90 (not_84_out[6], not_13_out[7]);
  not not_91 (not_84_out[7], not_13_out[7]);
  not not_92 (not_84_out[8], not_13_out[7]);
  not not_93 (not_84_out[9], not_13_out[7]);
  not not_94 (not_84_out[10], not_13_out[7]);
  not not_95 (not_84_out[11], not_13_out[7]);
  not not_96 (not_84_out[12], not_13_out[7]);
  not not_97 (not_84_out[13], not_13_out[7]);
  not not_98 (not_84_out[14], not_13_out[7]);
  not not_99 (not_84_out[15], not_13_out[7]);
  not not_100 (not_84_out[16], not_13_out[7]);
  not not_101 (not_84_out[17], not_13_out[7]);
  not not_102 (not_84_out[18], not_13_out[7]);
  not not_103 (not_84_out[19], not_13_out[7]);
  not not_104 (not_84_out[20], not_13_out[7]);
  not not_105 (not_84_out[21], not_13_out[7]);
  not not_106 (not_84_out[22], not_13_out[7]);
  not not_107 (not_84_out[23], not_13_out[7]);
  not not_108 (not_84_out[24], not_13_out[7]);
  not not_109 (not_84_out[25], not_13_out[7]);
  not not_110 (not_84_out[26], not_13_out[7]);
  not not_111 (not_84_out[27], not_13_out[7]);
  not not_112 (not_84_out[28], not_13_out[7]);
  not not_113 (not_84_out[29], not_13_out[7]);
  not not_114 (not_84_out[30], not_13_out[7]);
  not not_115 (not_84_out[31], not_13_out[7]);
  assign out_3 = {not_13_out, not_1_out[23], {2{not_13_out[7]}}, not_1_out[20], not_13_out[7], not_1_out[18:16], not_13_out[7], not_1_out[14:13], {4{not_13_out[7]}}, not_1_out[8:7], {4{not_13_out[7]}}, not_1_out[2:0]} & {32{not_13_out[7]}};  // AND_Gate and_1, 32 bits wide
  assign out_4 = not_20_out & {32{not_13_out[7]}};  // AND_Gate and_2, 32 bits wide
  assign out_5 = not_52_out & {32{not_13_out[7]}};  // AND_Gate and_3, 32 bits wide
  assign out_6 = not_84_out & {32{not_13_out[7]}};  // AND_Gate and_4, 32 bits wide
endmodule

module Countdown (
  input  ON,
  input  [3:0] Address,
  output [31:0] out_3,
  output [31:0] out_4,
  output [31:0] out_5,
  output [31:0] out_6
);

  wire ADDR_TRUE_out;
  wire [7:3] not_15_out;
  wire [22:0] not_1_out;
  wire [30:0] not_19_out;
  wire [31:0] not_63_out;
  wire [31:9] not_40_out;

  and ADDR_TRUE (ADDR_TRUE_out, Address[0], Address[1], Address[2], Address[3]);
  and ON_AND_ADDR (not_15_out[6], ON, ADDR_TRUE_out);
  not not_1 (not_1_out[0], not_15_out[6]);
  not not_2 (not_1_out[1], not_15_out[6]);
  not not_3 (not_1_out[2], not_15_out[6]);
  not not_4 (not_1_out[4], not_15_out[6]);
  not not_5 (not_1_out[6], not_15_out[6]);
  not not_6 (not_1_out[8], not_15_out[6]);
  not not_7 (not_1_out[9], not_15_out[6]);
  not not_8 (not_1_out[10], not_15_out[6]);
  not not_9 (not_1_out[11], not_15_out[6]);
  not not_10 (not_1_out[12], not_15_out[6]);
  not not_11 (not_1_out[15], not_15_out[6]);
  not not_12 (not_1_out[17], not_15_out[6]);
  not not_13 (not_1_out[18], not_15_out[6]);
  not not_14 (not_1_out[22], not_15_out[6]);
  not not_15 (not_15_out[3], not_15_out[6]);
  not not_16 (not_15_out[4], not_15_out[6]);
  not not_17 (not_15_out[5], not_15_out[6]);
  not not_18 (not_15_out[7], not_15_out[6]);
  not not_19 (not_19_out[0], not_15_out[6]);
  not not_20 (not_19_out[1], not_15_out[6]);
  not not_21 (not_19_out[2], not_15_out[6]);
  not not_22 (not_19_out[3], not_15_out[6]);
  not not_23 (not_19_out[6], not_15_out[6]);
  not not_24 (not_19_out[7], not_15_out[6]);
  not not_25 (not_19_out[8], not_15_out[6]);
  not not_26 (not_19_out[10], not_15_out[6]);
  not not_27 (not_19_out[14], not_15_out[6]);
  not not_28 (not_19_out[17], not_15_out[6]);
  not not_29 (not_19_out[18], not_15_out[6]);
  not not_30 (not_19_out[19], not_15_out[6]);
  not not_31 (not_19_out[21], not_15_out[6]);
  not not_32 (not_19_out[23], not_15_out[6]);
  not not_33 (not_19_out[24], not_15_out[6]);
  not not_34 (not_19_out[25], not_15_out[6]);
  not not_35 (not_19_out[26], not_15_out[6]);
  not not_36 (not_19_out[27], not_15_out[6]);
  not not_37 (not_19_out[28], not_15_out[6]);
  not not_38 (not_19_out[29], not_15_out[6]);
  not not_39 (not_19_out[30], not_15_out[6]);
  not not_40 (not_40_out[9], not_15_out[6]);
  not not_41 (not_40_out[10], not_15_out[6]);
  not not_42 (not_40_out[11], not_15_out[6]);
  not not_43 (not_40_out[12], not_15_out[6]);
  not not_44 (not_40_out[13], not_15_out[6]);
  not not_45 (not_40_out[14], not_15_out[6]);
  not not_46 (not_40_out[15], not_15_out[6]);
  not not_47 (not_40_out[16], not_15_out[6]);
  not not_48 (not_40_out[17], not_15_out[6]);
  not not_49 (not_40_out[18], not_15_out[6]);
  not not_50 (not_40_out[19], not_15_out[6]);
  not not_51 (not_40_out[20], not_15_out[6]);
  not not_52 (not_40_out[21], not_15_out[6]);
  not not_53 (not_40_out[22], not_15_out[6]);
  not not_54 (not_40_out[23], not_15_out[6]);
  not not_55 (not_40_out[24], not_15_out[6]);
  not not_56 (not_40_out[25], not_15_out[6]);
  not not_57 (not_40_out[26], not_15_out[6]);
  not not_58 (not_40_out[27], not_15_out[6]);
  not not_59 (not_40_out[28], not_15_out[6]);
  not not_60 (not_40_out[29], not_15_out[6]);
  not not_61 (not_40_out[30], not_15_out[6]);
  not not_62 (not_40_out[31], not_15_out[6]);
  not not_63 (not_63_out[0], not_15_out[6]);
  not not_64 (not_63_out[1], not_15_out[6]);
  not not_65 (not_63_out[2], not_15_out[6]);
  not not_66 (not_63_out[3], not_15_out[6]);
  not not_67 (not_63_out[4], not_15_out[6]);
  not not_68 (not_63_out[5], not_15_out[6]);
  not not_69 (not_63_out[6], not_15_out[6]);
  not not_70 (not_63_out[7], not_15_out[6]);
  not not_71 (not_63_out[8], not_15_out[6]);
  not not_72 (not_63_out[9], not_15_out[6]);
  not not_73 (not_63_out[10], not_15_out[6]);
  not not_74 (not_63_out[11], not_15_out[6]);
  not not_75 (not_63_out[12], not_15_out[6]);
  not not_76 (not_63_out[13], not_15_out[6]);
  not not_77 (not_63_out[14], not_15_out[6]);
  not not_78 (not_63_out[15], not_15_out[6]);
  not not_79 (not_63_out[16], not_15_out[6]);
  not not_80 (not_63_out[17], not_15_out[6]);
  not not_81 (not_63_out[18], not_15_out[6]);
  not not_82 (not_63_out[19], not_15_out[6]);
  not not_83 (not_63_out[20], not_15_out[6]);
  not not_84 (not_63_out[21], not_15_out[6]);
  not not_85 (not_63_out[22], not_15_out[6]);
  not not_86 (not_63_out[23], not_15_out[6]);
  not not_87 (not_63_out[24], not_15_out[6]);
  not not_88 (not_63_out[25], not_15_out[6]);
  not not_89 (not_63_out[26], not_15_out[6]);
  not not_90 (not_63_out[27], not_15_out[6]);
  not not_91 (not_63_out[28], not_15_out[6]);
  not not_92 (not_63_out[29], not_15_out[6]);
  not not_93 (not_63_out[30], not_15_out[6]);
  not not_94 (not_63_out[31], not_15_out[6]);
  assign out_3 = {not_15_out, {4{not_15_out[6]}}, not_1_out[22], {3{not_15_out[6]}}, not_1_out[18:17], not_15_out[6], not_1_out[15], {2{not_15_out[6]}}, not_1_out[12:8], not_15_out[6], not_1_out[6], not_15_out[6], not_1_out[4], not_15_out[6], not_1_out[2:0]} & {32{not_15_out[6]}};  // AND_Gate and_1, 32 bits wide
  assign out_4 = {not_15_out[6], not_19_out[30:23], not_15_out[6], not_19_out[21], not_15_out[6], not_19_out[19:17], {2{not_15_out[6]}}, not_19_out[14], {3{not_15_out[6]}}, not_19_out[10], not_15_out[6], not_19_out[8:6], {2{not_15_out[6]}}, not_19_out[3:0]} & {32{not_15_out[6]}};  // AND_Gate and_2, 32 bits wide
  assign out_5 = {not_40_out, {9{not_15_out[6]}}} & {32{not_15_out[6]}};  // AND_Gate and_3, 32 bits wide
  assign out_6 = not_63_out & {32{not_15_out[6]}};  // AND_Gate and_4, 32 bits wide
endmodule
