// Logisim project ALU.circ as structural Verilog: 4 circuits, main circuit ALU
module ALU (
  input  [7:0] L_Input_Register,
  input  [7:0] R_Input_Register,
  input  [1:0] Op_Code,
  output [7:0] A,
  output [2:0] Status
);

  wire and_1_out, and_2_out, full_adder_1_c_out, full_adder_2_c_out, full_adder_3_c_out, full_adder_4_c_out,
       full_adder_5_c_out, full_adder_6_c_out, half_adder_1_c_out;
  wire [7:0] twos_comp_1_out;

  and and_1 (and_1_out, twos_comp_1_out[7], ~A[7], R_Input_Register[7]);  // AND_Gate
  // Probe on L_Input_Register
  Twos_Comp twos_comp_1 (.In(L_Input_Register), .Out(twos_comp_1_out), .ADD_SUB(Op_Code[0]));
  and and_2 (and_2_out, ~twos_comp_1_out[7], A[7], ~R_Input_Register[7]);  // AND_Gate
  or or_1 (Status[2], and_2_out, and_1_out);
  // Probe on R_Input_Register
  Half_Adder half_adder_1 (.A(R_Input_Register[0]), .B(twos_comp_1_out[0]), .R(A[0]), .C_Out(half_adder_1_c_out));
  Full_Adder full_adder_1 (
    .A(twos_comp_1_out[1]), .B(R_Input_Register[1]), .C_In(half_adder_1_c_out), .R(A[1]),
    .C_Out(full_adder_1_c_out));
  Full_Adder full_adder_2 (
    .A(twos_comp_1_out[2]), .B(R_Input_Register[2]), .C_In(full_adder_1_c_out), .R(A[2]),
    .C_Out(full_adder_2_c_out));
  Full_Adder full_adder_3 (
    .A(twos_comp_1_out[3]), .B(R_Input_Register[3]), .C_In(full_adder_2_c_out), .R(A[3]),
    .C_Out(full_adder_3_c_out));
  Full_Adder full_adder_4 (
    .A(twos_comp_1_out[4]), .B(R_Input_Register[4]), .C_In(full_adder_3_c_out), .R(A[4]),
    .C_Out(full_adder_4_c_out));
  Full_Adder full_adder_5 (
    .A(twos_comp_1_out[5]), .B(R_Input_Register[5]), .C_In(full_adder_4_c_out), .R(A[5]),
    .C_Out(full_adder_5_c_out));
  Full_Adder full_adder_6 (
    .A(twos_comp_1_out[6]), .B(R_Input_Register[6]), .C_In(full_adder_5_c_out), .R(A[6]),
    .C_Out(full_adder_6_c_out));
  Full_Adder full_adder_7 (
    .A(twos_comp_1_out[7]), .B(R_Input_Register[7]), .C_In(full_adder_6_c_out), .R(A[7]));  // open: C_Out
  and Zero (Status[0], ~A[0], ~A[1], ~A[2], ~A[3], ~A[4], ~A[5], ~A[6], ~A[7]);  // AND_Gate
  // Probe on A

  assign Status[1] = A[7];

  // Notes on the sheet:
  //   00 Sub
  //   01 Add
  //   001 zero result
  //   010 negative result
  //   100 overflow
endmodule

module Half_Adder (
  input  A,
  input  B,
  output R,
  output C_Out
);

  wire or_1_out;

  and and_1 (C_Out, A, B);
  or or_1 (or_1_out, A, B);
  and and_2 (R, ~C_Out, or_1_out);  // AND_Gate
endmodule

module Full_Adder (
  input  A,
  input  B,
  input  C_In,
  output R,
  output C_Out
);

  wire A_B_out, A_C_out, and_1_out, and_2_out, and_3_out, B_C_out, or_1_out;

  and A_B (A_B_out, A, B);
  and A_C (A_C_out, A, C_In);
  and B_C (B_C_out, B, C_In);
  and and_1 (and_1_out, A, B, C_In);
  or or_1 (or_1_out, A, B, C_In);
  and and_2 (and_2_out, ~A_B_out, ~A_C_out, ~B_C_out);  // AND_Gate
  and and_3 (and_3_out, or_1_out, and_2_out);
  or or_2 (C_Out, A_B_out, A_C_out, B_C_out);
  or or_3 (R, and_1_out, and_3_out);
endmodule

module Twos_Comp (
  input  ADD_SUB,
  input  [7:0] In,
  output [7:0] Out
);

  wire and_1_out, and_2_out, and_3_out, and_4_out, and_5_out, and_6_out, and_7_out, and_8_out, and_9_out,
       and_10_out, and_11_out, and_12_out, and_13_out, and_14_out, and_15_out, and_16_out,
       half_adder_1_c_out, half_adder_2_c_out, half_adder_3_c_out, half_adder_4_c_out, half_adder_5_c_out,
       half_adder_6_c_out, half_adder_7_c_out, not_1_out, or_1_out, or_2_out, or_3_out, or_4_out, or_5_out,
       or_6_out, or_7_out, or_8_out;

  // Probe on In
  and and_1 (and_1_out, ~In[0], ~ADD_SUB);  // AND_Gate
  and and_2 (and_2_out, In[0], ADD_SUB);
  and and_3 (and_3_out, ~In[1], ~ADD_SUB);  // AND_Gate
  and and_4 (and_4_out, In[1], ADD_SUB);
  and and_5 (and_5_out, ~In[2], ~ADD_SUB);  // AND_Gate
  and and_6 (and_6_out, In[2], ADD_SUB);
  and and_7 (and_7_out, ~In[3], ~ADD_SUB);  // AND_Gate
  and and_8 (and_8_out, In[3], ADD_SUB);
  and and_9 (and_9_out, ~In[4], ~ADD_SUB);  // AND_Gate
  and and_10 (and_10_out, In[4], ADD_SUB);
  and and_11 (and_11_out, ~In[5], ~ADD_SUB);  // AND_Gate
  and and_12 (and_12_out, In[5], ADD_SUB);
  and and_13 (and_13_out, ~In[6], ~ADD_SUB);  // AND_Gate
  and and_14 (and_14_out, In[6], ADD_SUB);
  and and_15 (and_15_out, ~In[7], ~ADD_SUB);  // AND_Gate
  and and_16 (and_16_out, In[7], ADD_SUB);
  or or_1 (or_1_out, and_1_out, and_2_out);
  or or_2 (or_2_out, and_3_out, and_4_out);
  or or_3 (or_3_out, and_5_out, and_6_out);
  or or_4 (or_4_out, and_7_out, and_8_out);
  or or_5 (or_5_out, and_9_out, and_10_out);
  or or_6 (or_6_out, and_11_out, and_12_out);
  or or_7 (or_7_out, and_13_out, and_14_out);
  or or_8 (or_8_out, and_15_out, and_16_out);
  Half_Adder half_adder_1 (.A(or_1_out), .B(not_1_out), .R(Out[0]), .C_Out(half_adder_1_c_out));
  not not_1 (not_1_out, ADD_SUB);
  Half_Adder half_adder_2 (.A(or_2_out), .B(half_adder_1_c_out), .R(Out[1]), .C_Out(half_adder_2_c_out));
  Half_Adder half_adder_3 (.A(or_3_out), .B(half_adder_2_c_out), .R(Out[2]), .C_Out(half_adder_3_c_out));
  Half_Adder half_adder_4 (.A(or_4_out), .B(half_adder_3_c_out), .R(Out[3]), .C_Out(half_adder_4_c_out));
  Half_Adder half_adder_5 (.A(or_5_out), .B(half_adder_4_c_out), .R(Out[4]), .C_Out(half_adder_5_c_out));
  Half_Adder half_adder_6 (.A(or_6_out), .B(half_adder_5_c_out), .R(Out[5]), .C_Out(half_adder_6_c_out));
  Half_Adder half_adder_7 (.A(or_7_out), .B(half_adder_6_c_out), .R(Out[6]), .C_Out(half_adder_7_c_out));
  Half_Adder half_adder_8 (.A(or_8_out), .B(half_adder_7_c_out), .R(Out[7]));  // open: C_Out
  // Probe on Out

  // Notes on the sheet:
  //   0 for sub, 1 for add
endmodule
