// Logisim project DISPLAY.circ as structural Verilog: 2 circuits, main circuit DISPLAY
module DISPLAY (
  input  [3:0] in_1,
  input  [3:0] in_2,
  input  [3:0] in_3
);

  wire [6:0] encode_display_1_out_2, encode_display_2_out_2, encode_display_3_out_2;

  ENCODE_DISPLAY encode_display_1 (.out_2(encode_display_1_out_2), .in_1(in_1));
  _7_Segment_Display u_7_segment_display_1 (
    .g(encode_display_1_out_2[0]), .f(encode_display_1_out_2[1]), .a(encode_display_1_out_2[2]),
    .b(encode_display_1_out_2[3]), .e(encode_display_1_out_2[4]), .d(encode_display_1_out_2[5]),
    .c(encode_display_1_out_2[6]));  // open: dp
  ENCODE_DISPLAY encode_display_2 (.out_2(encode_display_2_out_2), .in_1(in_2));
  _7_Segment_Display u_7_segment_display_2 (
    .g(encode_display_2_out_2[0]), .f(encode_display_2_out_2[1]), .a(encode_display_2_out_2[2]),
    .b(encode_display_2_out_2[3]), .e(encode_display_2_out_2[4]), .d(encode_display_2_out_2[5]),
    .c(encode_display_2_out_2[6]));  // open: dp
  _7_Segment_Display u_7_segment_display_3 (
    .g(encode_display_3_out_2[0]), .f(encode_display_3_out_2[1]), .a(encode_display_3_out_2[2]),
    .b(encode_display_3_out_2[3]), .e(encode_display_3_out_2[4]), .d(encode_display_3_out_2[5]),
    .c(encode_display_3_out_2[6]));  // open: dp
  ENCODE_DISPLAY encode_display_3 (.out_2(encode_display_3_out_2), .in_1(in_3));
endmodule

module ENCODE_DISPLAY (
  input  [3:0] in_1,
  output [6:0] out_2
);

  wire I0_out, I1_out, I2_out, I3_out, I4_out, I5_out, I6_out, I7_out, I8_out, I9_out;

  or O6 (out_2[6], I9_out, I8_out, I7_out, I6_out, I5_out, I4_out, I3_out, I1_out, I0_out);
  and I9 (I9_out, in_1[3], ~in_1[2], ~in_1[1], in_1[0]);  // AND_Gate
  or O5 (out_2[5], I8_out, I6_out, I5_out, I3_out, I2_out, I0_out);
  and I8 (I8_out, in_1[3], ~in_1[2], ~in_1[1], ~in_1[0]);  // AND_Gate
  and I7 (I7_out, ~in_1[3], in_1[2], in_1[1], in_1[0]);  // AND_Gate
  or O4 (out_2[4], I8_out, I6_out, I2_out, I0_out);
  and I6 (I6_out, ~in_1[3], in_1[2], in_1[1], ~in_1[0]);  // AND_Gate
  or O3 (out_2[3], I9_out, I8_out, I7_out, I4_out, I3_out, I2_out, I1_out, I0_out);
  and I5 (I5_out, ~in_1[3], in_1[2], ~in_1[1], in_1[0]);  // AND_Gate
  and I4 (I4_out, ~in_1[3], in_1[2], ~in_1[1], ~in_1[0]);  // AND_Gate
  and I3 (I3_out, ~in_1[3], ~in_1[2], in_1[1], in_1[0]);  // AND_Gate
  or O2 (out_2[2], I9_out, I8_out, I7_out, I6_out, I5_out, I3_out, I2_out, I0_out);
  and I2 (I2_out, ~in_1[3], ~in_1[2], in_1[1], ~in_1[0]);  // AND_Gate
  or O1 (out_2[1], I9_out, I8_out, I6_out, I5_out, I4_out, I0_out);
  and I1 (I1_out, ~in_1[3], ~in_1[2], ~in_1[1], in_1[0]);  // AND_Gate
  and I0 (I0_out, ~in_1[3], ~in_1[2], ~in_1[1], ~in_1[0]);  // AND_Gate
  or O0 (out_2[0], I9_out, I8_out, I6_out, I5_out, I4_out, I3_out, I2_out);
endmodule
