// Logisim project GENREG.circ as structural Verilog: 1 circuit, main circuit GEN_REGISTER
module GEN_REGISTER (
  input  CLK_IN,
  input  IN_OR_OUT,
  input  [7:0] DATA_IN,
  input  ADDR,
  output [7:0] DATA_OUT,
  output [7:0] CONTENTS
);

  wire and_1_out, and_2_out, and_3_out, and_4_out, and_5_out, and_6_out, and_7_out, and_8_out, and_10_out,
       and_11_out, and_12_out, and_13_out, and_14_out, and_15_out, and_16_out, and_17_out;

  and and_1 (and_1_out, DATA_IN[7], ~IN_OR_OUT, ADDR);  // AND_Gate
  S_R_Flip_Flop s_r_ff_1 (.S(and_1_out), .R(and_2_out), .clk(CLK_IN), .Q(CONTENTS[7]));  // open: reset, Qn, preset
  and and_2 (and_2_out, ~DATA_IN[7], ~IN_OR_OUT, ADDR);  // AND_Gate
  and and_3 (and_3_out, DATA_IN[6], ~IN_OR_OUT, ADDR);  // AND_Gate
  and and_4 (and_4_out, ~DATA_IN[6], ~IN_OR_OUT, ADDR);  // AND_Gate
  S_R_Flip_Flop s_r_ff_2 (.S(and_3_out), .R(and_4_out), .clk(CLK_IN), .Q(CONTENTS[6]));  // open: reset, Qn, preset
  and and_5 (and_5_out, DATA_IN[5], ~IN_OR_OUT, ADDR);  // AND_Gate
  S_R_Flip_Flop s_r_ff_3 (.S(and_5_out), .R(and_6_out), .clk(CLK_IN), .Q(CONTENTS[5]));  // open: reset, Qn, preset
  and and_6 (and_6_out, ~DATA_IN[5], ~IN_OR_OUT, ADDR);  // AND_Gate
  and and_7 (and_7_out, ~DATA_IN[4], ~IN_OR_OUT, ADDR);  // AND_Gate
  and and_8 (and_8_out, DATA_IN[4], ~IN_OR_OUT, ADDR);  // AND_Gate
  S_R_Flip_Flop s_r_ff_4 (.S(and_8_out), .R(and_7_out), .clk(CLK_IN), .Q(CONTENTS[4]));  // open: reset, Qn, preset
  assign DATA_OUT = {8{IN_OR_OUT}} & CONTENTS;  // AND_Gate and_9, 8 bits wide
  and and_10 (and_10_out, DATA_IN[3], ~IN_OR_OUT, ADDR);  // AND_Gate
  S_R_Flip_Flop s_r_ff_5 (.S(and_10_out), .R(and_11_out), .clk(CLK_IN), .Q(CONTENTS[3]));  // open: reset, Qn, preset
  and and_11 (and_11_out, ~DATA_IN[3], ~IN_OR_OUT, ADDR);  // AND_Gate
  and and_12 (and_12_out, DATA_IN[2], ~IN_OR_OUT, ADDR);  // AND_Gate
  S_R_Flip_Flop s_r_ff_6 (.S(and_12_out), .R(and_13_out), .clk(CLK_IN), .Q(CONTENTS[2]));  // open: reset, Qn, preset
  and and_13 (and_13_out, ~DATA_IN[2], ~IN_OR_OUT, ADDR);  // AND_Gate
  and and_14 (and_14_out, DATA_IN[1], ~IN_OR_OUT, ADDR);  // AND_Gate
  S_R_Flip_Flop s_r_ff_7 (.S(and_14_out), .R(and_15_out), .clk(CLK_IN), .Q(CONTENTS[1]));  // open: reset, Qn, preset
  and and_15 (and_15_out, ~DATA_IN[1], ~IN_OR_OUT, ADDR);  // AND_Gate
  and and_16 (and_16_out, DATA_IN[0], ~IN_OR_OUT, ADDR);  // AND_Gate
  S_R_Flip_Flop s_r_ff_8 (.S(and_16_out), .R(and_17_out), .clk(CLK_IN), .Q(CONTENTS[0]));  // open: reset, Qn, preset
  and and_17 (and_17_out, ~DATA_IN[0], ~IN_OR_OUT, ADDR);  // AND_Gate
endmodule
