// Logisim project JL_Instr_Prototypes.circ as structural Verilog: 2 circuits, main circuit STORE
module STORE (
);

  wire [7:0] D0_byte_out, D1_byte_out;

  DATA_BYTE RAM_TARGET (.Byte_In(D0_byte_out));  // open: Byte_Out, CLK
  DATA_BYTE D0 (.Byte_Out(D0_byte_out));  // open: Byte_In, CLK
  DATA_BYTE D1 (.Byte_Out(D1_byte_out));  // open: Byte_In, CLK
  DATA_BYTE IR ();  // open: Byte_In, Byte_Out, CLK

  // Notes on the sheet:
  //   OP-D0/D1-ADDR
  //   GATES
endmodule

module DATA_BYTE (
  input  [7:0] Byte_In,
  input  CLK,
  output [7:0] Byte_Out
);

  wire undriven;

  D_Flip_Flop L_0 (.D(Byte_In[0]), .clk(CLK), .Q(Byte_Out[0]));  // open: Qn, preset, reset
  D_Flip_Flop L_1 (.D(Byte_In[1]), .clk(CLK), .Q(Byte_Out[1]), .reset(undriven));  // open: Qn, preset
  D_Flip_Flop L_2 (.D(Byte_In[2]), .clk(CLK), .Q(Byte_Out[2]), .preset(undriven));  // open: Qn, reset
  D_Flip_Flop L_3 (.D(Byte_In[3]), .clk(CLK), .Q(Byte_Out[3]));  // open: Qn, preset, reset
  D_Flip_Flop L_4 (.D(Byte_In[4]), .clk(CLK), .Q(Byte_Out[4]));  // open: Qn, preset, reset
  D_Flip_Flop L_5 (.D(Byte_In[5]), .clk(CLK), .Q(Byte_Out[5]));  // open: Qn, preset, reset
  D_Flip_Flop L_6 (.D(Byte_In[6]), .clk(CLK), .Q(Byte_Out[6]));  // open: Qn, preset, reset
  D_Flip_Flop L_7 (.D(Byte_In[7]), .clk(CLK), .Q(Byte_Out[7]));  // open: Qn, preset, reset
endmodule
