// Logisim project JV_Instr_Prototype.circ as structural Verilog: 10 circuits, main circuit ALU
module ALU (
  input  [7:0] L_In,
  input  [7:0] R_In,
  input  [1:0] Op,
  output [7:0] A_Out,
  output [2:0] Status
);

  wire and_1_out, and_2_out, full_adder_1_c_out, full_adder_2_c_out, full_adder_3_c_out, full_adder_4_c_out,
       full_adder_5_c_out, full_adder_6_c_out, half_adder_1_c_out;
  wire [7:0] twos_comp_1_out;

  and and_1 (and_1_out, twos_comp_1_out[7], ~A_Out[7], R_In[7]);  // AND_Gate
  // Probe on L_In
  Twos_Comp twos_comp_1 (.In(L_In), .Out(twos_comp_1_out), .ADD_SUB(Op[0]));
  and and_2 (and_2_out, ~twos_comp_1_out[7], A_Out[7], ~R_In[7]);  // AND_Gate
  or or_1 (Status[2], and_2_out, and_1_out);
  // Probe on R_In
  Half_Adder half_adder_1 (.A(R_In[0]), .B(twos_comp_1_out[0]), .R(A_Out[0]), .C_Out(half_adder_1_c_out));
  Full_Adder full_adder_1 (
    .A(twos_comp_1_out[1]), .B(R_In[1]), .C_In(half_adder_1_c_out), .R(A_Out[1]), .C_Out(full_adder_1_c_out));
  Full_Adder full_adder_2 (
    .A(twos_comp_1_out[2]), .B(R_In[2]), .C_In(full_adder_1_c_out), .R(A_Out[2]), .C_Out(full_adder_2_c_out));
  Full_Adder full_adder_3 (
    .A(twos_comp_1_out[3]), .B(R_In[3]), .C_In(full_adder_2_c_out), .R(A_Out[3]), .C_Out(full_adder_3_c_out));
  Full_Adder full_adder_4 (
    .A(twos_comp_1_out[4]), .B(R_In[4]), .C_In(full_adder_3_c_out), .R(A_Out[4]), .C_Out(full_adder_4_c_out));
  Full_Adder full_adder_5 (
    .A(twos_comp_1_out[5]), .B(R_In[5]), .C_In(full_adder_4_c_out), .R(A_Out[5]), .C_Out(full_adder_5_c_out));
  Full_Adder full_adder_6 (
    .A(twos_comp_1_out[6]), .B(R_In[6]), .C_In(full_adder_5_c_out), .R(A_Out[6]), .C_Out(full_adder_6_c_out));
  Full_Adder full_adder_7 (
    .A(twos_comp_1_out[7]), .B(R_In[7]), .C_In(full_adder_6_c_out), .R(A_Out[7]));  // open: C_Out
  and Zero (Status[0], ~A_Out[0], ~A_Out[1], ~A_Out[2], ~A_Out[3], ~A_Out[4], ~A_Out[5], ~A_Out[6], ~A_Out[7]);  // AND_Gate
  // Probe on A_Out

  assign Status[1] = A_Out[7];

  // Notes on the sheet:
  //   00 Sub
  //   01 Add
  //   001 zero result
  //   010 negative result
  //   100 overflow
endmodule

module Half_Adder (
  input  A,
  input  B,
  output R,
  output C_Out
);

  wire or_1_out;

  and and_1 (C_Out, A, B);
  or or_1 (or_1_out, A, B);
  and and_2 (R, ~C_Out, or_1_out);  // AND_Gate
endmodule

module Full_Adder (
  input  A,
  input  B,
  input  C_In,
  output R,
  output C_Out
);

  wire A_B_out, A_C_out, and_1_out, and_2_out, and_3_out, B_C_out, or_1_out;

  and A_B (A_B_out, A, B);
  and A_C (A_C_out, A, C_In);
  and B_C (B_C_out, B, C_In);
  and and_1 (and_1_out, A, B, C_In);
  or or_1 (or_1_out, A, B, C_In);
  and and_2 (and_2_out, ~A_B_out, ~A_C_out, ~B_C_out);  // AND_Gate
  and and_3 (and_3_out, or_1_out, and_2_out);
  or or_2 (C_Out, A_B_out, A_C_out, B_C_out);
  or or_3 (R, and_1_out, and_3_out);
endmodule

module Twos_Comp (
  input  ADD_SUB,
  input  [7:0] In,
  output [7:0] Out
);

  wire and_1_out, and_2_out, and_3_out, and_4_out, and_5_out, and_6_out, and_7_out, and_8_out, and_9_out,
       and_10_out, and_11_out, and_12_out, and_13_out, and_14_out, and_15_out, and_16_out,
       half_adder_1_c_out, half_adder_2_c_out, half_adder_3_c_out, half_adder_4_c_out, half_adder_5_c_out,
       half_adder_6_c_out, half_adder_7_c_out, not_1_out, or_1_out, or_2_out, or_3_out, or_4_out, or_5_out,
       or_6_out, or_7_out, or_8_out;

  // Probe on In
  and and_1 (and_1_out, ~In[0], ~ADD_SUB);  // AND_Gate
  and and_2 (and_2_out, In[0], ADD_SUB);
  and and_3 (and_3_out, ~In[1], ~ADD_SUB);  // AND_Gate
  and and_4 (and_4_out, In[1], ADD_SUB);
  and and_5 (and_5_out, ~In[2], ~ADD_SUB);  // AND_Gate
  and and_6 (and_6_out, In[2], ADD_SUB);
  and and_7 (and_7_out, ~In[3], ~ADD_SUB);  // AND_Gate
  and and_8 (and_8_out, In[3], ADD_SUB);
  and and_9 (and_9_out, ~In[4], ~ADD_SUB);  // AND_Gate
  and and_10 (and_10_out, In[4], ADD_SUB);
  and and_11 (and_11_out, ~In[5], ~ADD_SUB);  // AND_Gate
  and and_12 (and_12_out, In[5], ADD_SUB);
  and and_13 (and_13_out, ~In[6], ~ADD_SUB);  // AND_Gate
  and and_14 (and_14_out, In[6], ADD_SUB);
  and and_15 (and_15_out, ~In[7], ~ADD_SUB);  // AND_Gate
  and and_16 (and_16_out, In[7], ADD_SUB);
  or or_1 (or_1_out, and_1_out, and_2_out);
  or or_2 (or_2_out, and_3_out, and_4_out);
  or or_3 (or_3_out, and_5_out, and_6_out);
  or or_4 (or_4_out, and_7_out, and_8_out);
  or or_5 (or_5_out, and_9_out, and_10_out);
  or or_6 (or_6_out, and_11_out, and_12_out);
  or or_7 (or_7_out, and_13_out, and_14_out);
  or or_8 (or_8_out, and_15_out, and_16_out);
  Half_Adder half_adder_1 (.A(or_1_out), .B(not_1_out), .R(Out[0]), .C_Out(half_adder_1_c_out));
  not not_1 (not_1_out, ADD_SUB);
  Half_Adder half_adder_2 (.A(or_2_out), .B(half_adder_1_c_out), .R(Out[1]), .C_Out(half_adder_2_c_out));
  Half_Adder half_adder_3 (.A(or_3_out), .B(half_adder_2_c_out), .R(Out[2]), .C_Out(half_adder_3_c_out));
  Half_Adder half_adder_4 (.A(or_4_out), .B(half_adder_3_c_out), .R(Out[3]), .C_Out(half_adder_4_c_out));
  Half_Adder half_adder_5 (.A(or_5_out), .B(half_adder_4_c_out), .R(Out[4]), .C_Out(half_adder_5_c_out));
  Half_Adder half_adder_6 (.A(or_6_out), .B(half_adder_5_c_out), .R(Out[5]), .C_Out(half_adder_6_c_out));
  Half_Adder half_adder_7 (.A(or_7_out), .B(half_adder_6_c_out), .R(Out[6]), .C_Out(half_adder_7_c_out));
  Half_Adder half_adder_8 (.A(or_8_out), .B(half_adder_7_c_out), .R(Out[7]));  // open: C_Out
  // Probe on Out

  // Notes on the sheet:
  //   0 for sub, 1 for add
endmodule

module GEN_REGISTER (
  input  CLK_IN,
  input  IN_OR_OUT,
  input  [7:0] DATA_IN,
  input  ADDR,
  output [7:0] DATA_OUT,
  output [7:0] CONTENTS
);

  wire and_1_out, and_2_out, and_3_out, and_4_out, and_5_out, and_6_out, and_7_out, and_8_out, and_10_out,
       and_11_out, and_12_out, and_13_out, and_14_out, and_15_out, and_16_out, and_17_out;

  and and_1 (and_1_out, DATA_IN[7], ~IN_OR_OUT, ADDR);  // AND_Gate
  S_R_Flip_Flop s_r_ff_1 (.S(and_1_out), .R(and_2_out), .clk(CLK_IN), .Q(CONTENTS[7]));  // open: reset, Qn, preset
  and and_2 (and_2_out, ~DATA_IN[7], ~IN_OR_OUT, ADDR);  // AND_Gate
  and and_3 (and_3_out, DATA_IN[6], ~IN_OR_OUT, ADDR);  // AND_Gate
  and and_4 (and_4_out, ~DATA_IN[6], ~IN_OR_OUT, ADDR);  // AND_Gate
  S_R_Flip_Flop s_r_ff_2 (.S(and_3_out), .R(and_4_out), .clk(CLK_IN), .Q(CONTENTS[6]));  // open: reset, Qn, preset
  and and_5 (and_5_out, DATA_IN[5], ~IN_OR_OUT, ADDR);  // AND_Gate
  S_R_Flip_Flop s_r_ff_3 (.S(and_5_out), .R(and_6_out), .clk(CLK_IN), .Q(CONTENTS[5]));  // open: reset, Qn, preset
  and and_6 (and_6_out, ~DATA_IN[5], ~IN_OR_OUT, ADDR);  // AND_Gate
  and and_7 (and_7_out, ~DATA_IN[4], ~IN_OR_OUT, ADDR);  // AND_Gate
  and and_8 (and_8_out, DATA_IN[4], ~IN_OR_OUT, ADDR);  // AND_Gate
  S_R_Flip_Flop s_r_ff_4 (.S(and_8_out), .R(and_7_out), .clk(CLK_IN), .Q(CONTENTS[4]));  // open: reset, Qn, preset
  assign DATA_OUT = {8{IN_OR_OUT}} & CONTENTS;  // AND_Gate and_9, 8 bits wide
  and and_10 (and_10_out, DATA_IN[3], ~IN_OR_OUT, ADDR);  // AND_Gate
  S_R_Flip_Flop s_r_ff_5 (.S(and_10_out), .R(and_11_out), .clk(CLK_IN), .Q(CONTENTS[3]));  // open: reset, Qn, preset
  and and_11 (and_11_out, ~DATA_IN[3], ~IN_OR_OUT, ADDR);  // AND_Gate
  and and_12 (and_12_out, DATA_IN[2], ~IN_OR_OUT, ADDR);  // AND_Gate
  S_R_Flip_Flop s_r_ff_6 (.S(and_12_out), .R(and_13_out), .clk(CLK_IN), .Q(CONTENTS[2]));  // open: reset, Qn, preset
  and and_13 (and_13_out, ~DATA_IN[2], ~IN_OR_OUT, ADDR);  // AND_Gate
  and and_14 (and_14_out, DATA_IN[1], ~IN_OR_OUT, ADDR);  // AND_Gate
  S_R_Flip_Flop s_r_ff_7 (.S(and_14_out), .R(and_15_out), .clk(CLK_IN), .Q(CONTENTS[1]));  // open: reset, Qn, preset
  and and_15 (and_15_out, ~DATA_IN[1], ~IN_OR_OUT, ADDR);  // AND_Gate
  and and_16 (and_16_out, DATA_IN[0], ~IN_OR_OUT, ADDR);  // AND_Gate
  S_R_Flip_Flop s_r_ff_8 (.S(and_16_out), .R(and_17_out), .clk(CLK_IN), .Q(CONTENTS[0]));  // open: reset, Qn, preset
  and and_17 (and_17_out, ~DATA_IN[0], ~IN_OR_OUT, ADDR);  // AND_Gate
endmodule

module DATA_BYTE (
  input  [7:0] Byte_In,
  input  CLK,
  input  NO_IN,
  output [7:0] Byte_Out
);

  wire and_1_out, and_2_out, and_3_out, and_4_out, and_5_out, and_6_out, and_7_out, and_8_out, and_9_out,
       and_10_out, and_11_out, and_12_out, and_13_out, and_14_out, and_15_out, and_16_out;

  and and_1 (and_1_out, ~NO_IN, Byte_In[0]);  // AND_Gate
  S_R_Flip_Flop s_r_ff_1 (.S(and_1_out), .R(and_2_out), .clk(CLK), .Q(Byte_Out[0]));  // open: reset, Qn, preset
  and and_2 (and_2_out, ~NO_IN, ~Byte_In[0]);  // AND_Gate
  S_R_Flip_Flop s_r_ff_2 (.S(and_3_out), .R(and_4_out), .clk(CLK), .Q(Byte_Out[1]));  // open: reset, Qn, preset
  and and_3 (and_3_out, ~NO_IN, Byte_In[1]);  // AND_Gate
  and and_4 (and_4_out, ~NO_IN, ~Byte_In[1]);  // AND_Gate
  and and_5 (and_5_out, ~NO_IN, Byte_In[2]);  // AND_Gate
  S_R_Flip_Flop s_r_ff_3 (.S(and_5_out), .R(and_6_out), .clk(CLK), .Q(Byte_Out[2]));  // open: reset, Qn, preset
  and and_6 (and_6_out, ~NO_IN, ~Byte_In[2]);  // AND_Gate
  and and_7 (and_7_out, ~NO_IN, Byte_In[3]);  // AND_Gate
  S_R_Flip_Flop s_r_ff_4 (.S(and_7_out), .R(and_8_out), .clk(CLK), .Q(Byte_Out[3]));  // open: reset, Qn, preset
  and and_8 (and_8_out, ~NO_IN, ~Byte_In[3]);  // AND_Gate
  and and_9 (and_9_out, ~NO_IN, Byte_In[4]);  // AND_Gate
  S_R_Flip_Flop s_r_ff_5 (.S(and_9_out), .R(and_10_out), .clk(CLK), .Q(Byte_Out[4]));  // open: reset, Qn, preset
  and and_10 (and_10_out, ~NO_IN, ~Byte_In[4]);  // AND_Gate
  and and_11 (and_11_out, ~NO_IN, Byte_In[5]);  // AND_Gate
  S_R_Flip_Flop s_r_ff_6 (.S(and_11_out), .R(and_12_out), .clk(CLK), .Q(Byte_Out[5]));  // open: reset, Qn, preset
  and and_12 (and_12_out, ~NO_IN, ~Byte_In[5]);  // AND_Gate
  S_R_Flip_Flop s_r_ff_7 (.S(and_13_out), .R(and_14_out), .clk(CLK), .Q(Byte_Out[6]));  // open: reset, Qn, preset
  and and_13 (and_13_out, ~NO_IN, Byte_In[6]);  // AND_Gate
  and and_14 (and_14_out, ~NO_IN, ~Byte_In[6]);  // AND_Gate
  and and_15 (and_15_out, ~NO_IN, Byte_In[7]);  // AND_Gate
  S_R_Flip_Flop s_r_ff_8 (.S(and_15_out), .R(and_16_out), .clk(CLK), .Q(Byte_Out[7]));  // open: reset, Qn, preset
  and and_16 (and_16_out, ~NO_IN, ~Byte_In[7]);  // AND_Gate
endmodule

module ADD (
  input  [7:0] R1In,
  input  [7:0] R2In,
  input  Activate
);

  wire clock_1_out;

  Clock clock_1 (.out(clock_1_out));
  S_R_Flip_Flop s_r_ff_1 (.S(Activate), .clk(clock_1_out));  // open: R, Q, reset, Qn, preset
endmodule

module ADDTest (
  input  [7:0] in_1,
  input  [7:0] in_2,
  input  in_3,
  input  in_4,
  input  in_5,
  input  in_6,
  input  AddOn,
  input  [3:0] in_8
);

  wire clock_1_out;
  wire [1:1] undriven;
  wire [3:0] inc_1_out_0, pc_1_out_0;
  wire [7:0] alu_1_a_out, R1_contents, R1_data_out, R2_contents, R2_data_out;

  Clock clock_1 (.out(clock_1_out));
  GEN_REGISTER R1 (
    .DATA_IN(in_1), .CONTENTS(R1_contents), .ADDR(in_3), .IN_OR_OUT(in_4), .CLK_IN(clock_1_out),
    .DATA_OUT(R1_data_out));
  INC inc_1 (.ON_0(in_5), .IN_0(pc_1_out_0), .OUT_0(inc_1_out_0));
  PC pc_1 (.IN_MODE(in_6), .CLK(clock_1_out), .IN_1(inc_1_out_0), .IN_0(in_8), .OUT_0(pc_1_out_0));  // open: NO_IN
  // Probe on pc_1_out_0
  // Probe on R1_contents
  ALU alu_1 (.A_Out(alu_1_a_out), .L_In(R1_data_out), .R_In(R2_data_out), .Op({undriven[1], AddOn}));  // open: Status
  GEN_REGISTER R2 (
    .DATA_IN(in_2), .CONTENTS(R2_contents), .ADDR(in_3), .IN_OR_OUT(in_4), .CLK_IN(clock_1_out),
    .DATA_OUT(R2_data_out));
  // Probe on alu_1_a_out
  // Probe on R2_contents
endmodule

module PC (
  input  IN_MODE,
  input  NO_IN,
  input  CLK,
  input  [3:0] IN_1,
  input  [3:0] IN_0,
  output [3:0] OUT_0
);

  wire and_3_out, and_4_out, and_5_out, and_6_out, and_7_out, and_8_out, and_9_out, and_10_out;
  wire [3:0] and_1_out, and_2_out, or_1_out;

  assign and_1_out = {4{IN_MODE}} & IN_1;  // AND_Gate and_1, 4 bits wide
  assign or_1_out = and_1_out | and_2_out;  // OR_Gate or_1, 4 bits wide
  assign and_2_out = ~{4{IN_MODE}} & IN_0;  // AND_Gate and_2, 4 bits wide
  and and_3 (and_3_out, ~NO_IN, or_1_out[0]);  // AND_Gate
  and and_4 (and_4_out, ~or_1_out[0], ~NO_IN);  // AND_Gate
  and and_5 (and_5_out, ~NO_IN, or_1_out[1]);  // AND_Gate
  and and_6 (and_6_out, ~NO_IN, ~or_1_out[1]);  // AND_Gate
  and and_7 (and_7_out, ~NO_IN, or_1_out[2]);  // AND_Gate
  and and_8 (and_8_out, ~NO_IN, ~or_1_out[2]);  // AND_Gate
  and and_9 (and_9_out, ~NO_IN, or_1_out[3]);  // AND_Gate
  and and_10 (and_10_out, ~NO_IN, ~or_1_out[3]);  // AND_Gate
  S_R_Flip_Flop s_r_ff_1 (.S(and_3_out), .R(and_4_out), .clk(CLK), .Q(OUT_0[0]));  // open: reset, Qn, preset
  S_R_Flip_Flop s_r_ff_2 (.S(and_5_out), .R(and_6_out), .clk(CLK), .Q(OUT_0[1]));  // open: reset, Qn, preset
  S_R_Flip_Flop s_r_ff_3 (.S(and_7_out), .R(and_8_out), .clk(CLK), .Q(OUT_0[2]));  // open: reset, Qn, preset
  S_R_Flip_Flop s_r_ff_4 (.S(and_9_out), .R(and_10_out), .clk(CLK), .Q(OUT_0[3]));  // open: reset, Qn, preset

  // Notes on the sheet:
  //   Input from INC
  //   Input from IR
endmodule

module INC (
  input  ON_0,
  input  [3:0] IN_0,
  output [3:0] OUT_0
);

  wire half_adder_1_c_out, half_adder_2_c_out, half_adder_3_c_out;

  Half_Adder half_adder_1 (.A(IN_0[0]), .B(ON_0), .R(OUT_0[0]), .C_Out(half_adder_1_c_out));
  Half_Adder half_adder_2 (.A(IN_0[1]), .B(half_adder_1_c_out), .R(OUT_0[1]), .C_Out(half_adder_2_c_out));
  Half_Adder half_adder_3 (.A(IN_0[2]), .B(half_adder_2_c_out), .R(OUT_0[2]), .C_Out(half_adder_3_c_out));
  Half_Adder half_adder_4 (.A(IN_0[3]), .B(half_adder_3_c_out), .R(OUT_0[3]));  // open: C_Out
endmodule
