// Logisim project KeypadEvo.circ as structural Verilog: 2 circuits, main circuit main
module KeyPad (
  input  Zero,
  input  One,
  input  Two,
  input  Three,
  input  Four,
  input  Five,
  input  Six,
  input  Seven,
  input  Eight,
  input  Nine,
  input  Clock,
  output [7:0] Output
);

  wire Active_out, and_1_out, nand_1_out, not_1_out, not_2_out, not_3_out, not_4_out, or_1_out, or_2_out,
       or_3_out, or_4_out, s_r_ff_2_q, s_r_ff_3_q, undriven, undriven_2, xnor_1_out;

  NotExactlyOne xnor_1 (
    .out(xnor_1_out), .in0(Zero), .in1(One), .in2(Two), .in3(Three), .in4(Four), .in5(Five), .in6(Six),
    .in7(Seven), .in8(Eight), .in9(Nine));
  nand nand_1 (nand_1_out, xnor_1_out, Active_out);
  or Active (Active_out, Nine, Eight, Seven, Six, Five, Four, Three, Two, One, Zero);
  or or_1 (or_1_out, One, Three, Five, Seven, Nine);
  not not_1 (not_1_out, or_1_out);
  and and_1 (and_1_out, Active_out, Clock);
  and and_2 (Output[0], undriven, nand_1_out);
  and and_3 (Output[1], s_r_ff_2_q, nand_1_out);
  and and_4 (Output[2], s_r_ff_3_q, nand_1_out);
  and and_5 (Output[3], undriven_2, nand_1_out);
  S_R_Flip_Flop s_r_ff_1 (
    .S(or_1_out), .clk(or_1_out), .R(not_1_out), .preset(not_1_out), .reset(not_1_out));  // open: Q, Qn
  or or_2 (or_2_out, Two, Three, Six, Seven);
  S_R_Flip_Flop s_r_ff_2 (.S(or_2_out), .R(not_2_out), .clk(and_1_out), .Q(s_r_ff_2_q));  // open: reset, Qn, preset
  not not_2 (not_2_out, or_2_out);
  or or_3 (or_3_out, Four, Five, Six, Seven);
  not not_3 (not_3_out, or_3_out);
  S_R_Flip_Flop s_r_ff_3 (.S(or_3_out), .R(not_3_out), .clk(and_1_out), .Q(s_r_ff_3_q));  // open: reset, Qn, preset
  or or_4 (or_4_out, Eight, Nine);
  S_R_Flip_Flop s_r_ff_4 (
    .S(or_4_out), .clk(or_4_out), .R(not_4_out), .preset(not_4_out), .reset(not_4_out));  // open: Q, Qn
  not not_4 (not_4_out, or_4_out);

  assign Output[7:4] = 4'b0000;
endmodule

module main (
  input  Zero,
  input  One,
  input  Two,
  input  Three,
  input  Four,
  input  Five,
  input  Six,
  input  Seven,
  input  Eight,
  input  Nine,
  output [7:0] out_11
);

  wire clock_1_out;

  KeyPad keypad_1 (
    .Zero(Zero), .One(One), .Two(Two), .Three(Three), .Four(Four), .Five(Five), .Six(Six), .Seven(Seven),
    .Eight(Eight), .Nine(Nine), .Clock(clock_1_out), .Output(out_11));
  Clock clock_1 (.out(clock_1_out));
  // Probe on out_11

  // Notes on the sheet:
  //   Demo to show it works as a box
endmodule
