// Logisim project MAREvo.circ as structural Verilog: 2 circuits, main circuit MAR
module MAR (
  input  [7:0] InAdr,
  input  InOn,
  input  OutOn,
  input  Clock,
  output [7:0] OutAdr,
  output [7:0] Contents
);

  wire and_1_out, not_1_out, not_2_out, not_3_out, not_4_out, not_5_out, not_6_out, not_7_out, not_8_out;

  and and_1 (and_1_out, InOn, Clock);
  S_R_Flip_Flop s_r_ff_1 (.S(InAdr[0]), .R(not_1_out), .clk(and_1_out), .Q(Contents[0]));  // open: reset, Qn, preset
  not not_1 (not_1_out, InAdr[0]);
  S_R_Flip_Flop s_r_ff_2 (.S(InAdr[1]), .R(not_2_out), .clk(and_1_out), .Q(Contents[1]));  // open: reset, Qn, preset
  not not_2 (not_2_out, InAdr[1]);
  S_R_Flip_Flop s_r_ff_3 (.S(InAdr[2]), .R(not_3_out), .clk(and_1_out), .Q(Contents[2]));  // open: reset, Qn, preset
  not not_3 (not_3_out, InAdr[2]);
  S_R_Flip_Flop s_r_ff_4 (.S(InAdr[3]), .R(not_4_out), .clk(and_1_out), .Q(Contents[3]));  // open: reset, Qn, preset
  not not_4 (not_4_out, InAdr[3]);
  S_R_Flip_Flop s_r_ff_5 (.S(InAdr[4]), .R(not_5_out), .clk(and_1_out), .Q(Contents[4]));  // open: reset, Qn, preset
  not not_5 (not_5_out, InAdr[4]);
  S_R_Flip_Flop s_r_ff_6 (.S(InAdr[5]), .R(not_6_out), .clk(and_1_out), .Q(Contents[5]));  // open: reset, Qn, preset
  not not_6 (not_6_out, InAdr[5]);
  S_R_Flip_Flop s_r_ff_7 (.S(InAdr[6]), .R(not_7_out), .clk(and_1_out), .Q(Contents[6]));  // open: reset, Qn, preset
  not not_7 (not_7_out, InAdr[6]);
  S_R_Flip_Flop s_r_ff_8 (.S(InAdr[7]), .R(not_8_out), .clk(and_1_out), .Q(Contents[7]));  // open: reset, Qn, preset
  not not_8 (not_8_out, InAdr[7]);
  and and_2 (OutAdr[0], Contents[0], OutOn);
  and and_3 (OutAdr[1], Contents[1], OutOn);
  and and_4 (OutAdr[2], Contents[2], OutOn);
  and and_5 (OutAdr[3], Contents[3], OutOn);
  and and_6 (OutAdr[4], Contents[4], OutOn);
  and and_7 (OutAdr[5], Contents[5], OutOn);
  and and_8 (OutAdr[6], Contents[6], OutOn);
  and and_9 (OutAdr[7], Contents[7], OutOn);
endmodule

module main (
  input  [7:0] in_1,
  input  in_2,
  input  in_3,
  output [7:0] out_4,
  output [7:0] out_5
);

  wire clock_1_out;

  Clock clock_1 (.out(clock_1_out));
  MAR mar_1 (.Clock(clock_1_out), .InOn(in_3), .Contents(out_4), .InAdr(in_1), .OutOn(in_2), .OutAdr(out_5));
endmodule
