// Logisim project MBREvo.circ as structural Verilog: 2 circuits, main circuit MBR
module MBR (
  input  [1:0] InMode,
  input  [7:0] In_00,
  input  [7:0] In_11,
  input  [7:0] In_10,
  input  InOn,
  input  OutOn,
  input  Clock,
  output [7:0] Out_00,
  output [7:0] Out_11,
  output [7:0] Contents,
  output [7:0] Out_10
);

  wire and_1_out, and_2_out, and_3_out, and_4_out, and_5_out, and_6_out, and_7_out, and_8_out, and_9_out,
       and_10_out, and_11_out, and_12_out, and_13_out, and_14_out, and_15_out, and_16_out, and_17_out,
       and_18_out, and_19_out, and_20_out, and_21_out, and_22_out, and_23_out, and_24_out, and_25_out,
       and_26_out, and_27_out, and_28_out, not_1_out, not_2_out, not_3_out, not_4_out, not_5_out, not_6_out,
       not_7_out, not_8_out, or_1_out, or_2_out, or_3_out, or_4_out, or_5_out, or_6_out, or_7_out, or_8_out;

  and and_1 (and_1_out, ~InMode[0], InMode[1]);  // AND_Gate
  and and_2 (and_2_out, InOn, Clock);
  and and_3 (and_3_out, ~InMode[0], ~InMode[1]);  // AND_Gate
  and and_4 (and_4_out, InMode[0], InMode[1]);
  and and_5 (and_5_out, In_00[0], and_3_out);
  and and_6 (and_6_out, In_00[1], and_3_out);
  and and_7 (and_7_out, In_00[2], and_3_out);
  and and_8 (and_8_out, In_00[3], and_3_out);
  and and_9 (and_9_out, In_00[4], and_3_out);
  and and_10 (and_10_out, In_00[5], and_3_out);
  and and_11 (and_11_out, In_00[6], and_3_out);
  and and_12 (and_12_out, In_00[7], and_3_out);
  and and_13 (and_13_out, In_11[0], and_4_out);
  and and_14 (and_14_out, In_11[1], and_4_out);
  and and_15 (and_15_out, In_11[2], and_4_out);
  and and_16 (and_16_out, In_11[3], and_4_out);
  and and_17 (and_17_out, In_11[4], and_4_out);
  and and_18 (and_18_out, In_11[5], and_4_out);
  and and_19 (and_19_out, In_11[6], and_4_out);
  and and_20 (and_20_out, In_11[7], and_4_out);
  and and_21 (and_21_out, In_10[0], and_1_out);
  and and_22 (and_22_out, In_10[1], and_1_out);
  and and_23 (and_23_out, In_10[2], and_1_out);
  and and_24 (and_24_out, In_10[3], and_1_out);
  and and_25 (and_25_out, In_10[4], and_1_out);
  and and_26 (and_26_out, In_10[5], and_1_out);
  and and_27 (and_27_out, In_10[6], and_1_out);
  and and_28 (and_28_out, In_10[7], and_1_out);
  or or_1 (or_1_out, and_5_out, and_21_out, and_13_out);
  not not_1 (not_1_out, or_1_out);
  S_R_Flip_Flop s_r_ff_1 (.S(or_1_out), .R(not_1_out), .clk(and_2_out), .Q(Contents[0]));  // open: reset, Qn, preset
  S_R_Flip_Flop s_r_ff_2 (.S(or_2_out), .R(not_2_out), .clk(and_2_out), .Q(Contents[1]));  // open: reset, Qn, preset
  or or_2 (or_2_out, and_6_out, and_22_out, and_14_out);
  not not_2 (not_2_out, or_2_out);
  or or_3 (or_3_out, and_7_out, and_23_out, and_15_out);
  S_R_Flip_Flop s_r_ff_3 (.S(or_3_out), .R(not_3_out), .clk(and_2_out), .Q(Contents[2]));  // open: reset, Qn, preset
  not not_3 (not_3_out, or_3_out);
  S_R_Flip_Flop s_r_ff_4 (.S(or_4_out), .R(not_4_out), .clk(and_2_out), .Q(Contents[3]));  // open: reset, Qn, preset
  or or_4 (or_4_out, and_8_out, and_24_out, and_16_out);
  not not_4 (not_4_out, or_4_out);
  or or_5 (or_5_out, and_9_out, and_25_out, and_17_out);
  S_R_Flip_Flop s_r_ff_5 (.S(or_5_out), .R(not_5_out), .clk(and_2_out), .Q(Contents[4]));  // open: reset, Qn, preset
  not not_5 (not_5_out, or_5_out);
  S_R_Flip_Flop s_r_ff_6 (.S(or_6_out), .R(not_6_out), .clk(and_2_out), .Q(Contents[5]));  // open: reset, Qn, preset
  or or_6 (or_6_out, and_10_out, and_26_out, and_18_out);
  not not_6 (not_6_out, or_6_out);
  or or_7 (or_7_out, and_11_out, and_27_out, and_19_out);
  S_R_Flip_Flop s_r_ff_7 (.S(or_7_out), .R(not_7_out), .clk(and_2_out), .Q(Contents[6]));  // open: reset, Qn, preset
  not not_7 (not_7_out, or_7_out);
  S_R_Flip_Flop s_r_ff_8 (.S(or_8_out), .R(not_8_out), .clk(and_2_out), .Q(Contents[7]));  // open: reset, Qn, preset
  or or_8 (or_8_out, and_12_out, and_28_out, and_20_out);
  not not_8 (not_8_out, or_8_out);
  and and_29 (Out_00[0], Contents[0], OutOn, and_3_out);
  and and_30 (Out_00[1], Contents[1], OutOn, and_3_out);
  and and_31 (Out_00[2], Contents[2], OutOn, and_3_out);
  and and_32 (Out_00[3], Contents[3], OutOn, and_3_out);
  and and_33 (Out_00[4], Contents[4], OutOn, and_3_out);
  and and_34 (Out_00[5], Contents[5], OutOn, and_3_out);
  and and_35 (Out_00[6], Contents[6], OutOn, and_3_out);
  and and_36 (Out_00[7], Contents[7], OutOn, and_3_out);
  and and_37 (Out_11[0], Contents[0], OutOn, and_4_out);
  and and_38 (Out_11[1], Contents[1], OutOn, and_4_out);
  and and_39 (Out_11[2], Contents[2], OutOn, and_4_out);
  and and_40 (Out_11[3], Contents[3], OutOn, and_4_out);
  and and_41 (Out_11[4], Contents[4], OutOn, and_4_out);
  and and_42 (Out_11[5], Contents[5], OutOn, and_4_out);
  and and_43 (Out_11[6], Contents[6], OutOn, and_4_out);
  and and_44 (Out_11[7], Contents[7], OutOn, and_4_out);
  and and_45 (Out_10[0], Contents[0], OutOn, and_1_out);
  and and_46 (Out_10[1], Contents[1], OutOn, and_1_out);
  and and_47 (Out_10[2], Contents[2], OutOn, and_1_out);
  and and_48 (Out_10[3], Contents[3], OutOn, and_1_out);
  and and_49 (Out_10[4], Contents[4], OutOn, and_1_out);
  and and_50 (Out_10[5], Contents[5], OutOn, and_1_out);
  and and_51 (Out_10[6], Contents[6], OutOn, and_1_out);
  and and_52 (Out_10[7], Contents[7], OutOn, and_1_out);
endmodule

module main (
  input  [7:0] in_1,
  input  [7:0] in_2,
  input  in_3,
  input  in_4,
  input  in_5,
  output [7:0] out_6,
  output [7:0] out_7,
  output [7:0] out_8
);

  wire clock_1_out;

  Clock clock_1 (.out(clock_1_out));
  // MBR mbr_1: pin names not known; wires that end beside it: in_1, in_2, in_3, in_4, in_5, clock_1_out, out_6, out_7, out_8
endmodule
