// Logisim project MULTsign.circ as structural Verilog: 3 circuits, main circuit Half_Adder
module MULT (
  input  [7:0] IN_0,
  input  [7:0] IN_1,
  output [7:0] ANS,
  output OVERFLOW
);

  wire A0_c_out, A1_0_c_out, A1_0_r, A1_1_c_out, A1_C_c_out, A1_C_r, A2_0_c_out, A2_0_r, A2_1_c_out,
       A2_C_c_out, A2_C_r, A3_0_c_out, A3_0_r, A3_1_c_out, A3_1_r, A3_2_c_out, A3_C_0_c_out, A3_C_0_r,
       A3_C_1_c_out, A3_C_1_r, A4_0_c_out, A4_0_r, A4_1_c_out, A4_1_r, A4_2_c_out, A4_C_0_c_out, A4_C_0_r,
       A4_C_1_c_out, A4_C_1_r, A5_0_c_out, A5_0_r, A5_1_c_out, A5_1_r, A5_2_c_out, A5_2_r, A5_3_c_out,
       A5_C_0_c_out, A5_C_0_r, A5_C_1_c_out, A5_C_1_r, A5_C_2_c_out, A5_C_2_r, A6_0_c_out, A6_0_r,
       A6_1_c_out, A6_1_r, A6_2_c_out, A6_2_r, A6_3_c_out, OVERFLOW_out;
  wire [7:0] M1_out, M2_out, M3_out, M4_out, M5_out, M6_out, M7_out;
  wire [7:1] M0_out;

  // Probe on IN_0
  // Probe on IN_1
  assign {M0_out, ANS[0]} = IN_0 & {8{IN_1[0]}};  // AND_Gate M0, 8 bits wide
  assign M1_out = IN_0 & {8{IN_1[1]}};  // AND_Gate M1, 8 bits wide
  assign M2_out = IN_0 & {8{IN_1[2]}};  // AND_Gate M2, 8 bits wide
  assign M3_out = IN_0 & {8{IN_1[3]}};  // AND_Gate M3, 8 bits wide
  assign M4_out = IN_0 & {8{IN_1[4]}};  // AND_Gate M4, 8 bits wide
  assign M5_out = IN_0 & {8{IN_1[5]}};  // AND_Gate M5, 8 bits wide
  assign M6_out = IN_0 & {8{IN_1[6]}};  // AND_Gate M6, 8 bits wide
  assign M7_out = IN_0 & {8{IN_1[7]}};  // AND_Gate M7, 8 bits wide
  or u_OVERFLOW (OVERFLOW_out, M1_out[7], M2_out[7], M2_out[6], M3_out[7], M3_out[6], M3_out[5], M4_out[7], M4_out[6], M4_out[5], M4_out[4], M5_out[7], M5_out[6], M5_out[5], M5_out[4], M5_out[3], M6_out[7], M6_out[6], M6_out[5], M6_out[4], M6_out[3], M6_out[2], M7_out[7], M7_out[6], M7_out[5], M7_out[4], M7_out[3], M7_out[2], M7_out[1], A6_0_c_out, A6_1_c_out, A6_3_c_out, A5_C_1_c_out);
  or or_1 (OVERFLOW, OVERFLOW_out, A6_2_c_out, A5_C_0_c_out, A5_C_2_c_out);
  Half_Adder A0 (.A(M0_out[1]), .B(M1_out[0]), .R(ANS[1]), .C_Out(A0_c_out));
  // Probe on ANS
  Full_Adder A1_0 (.A(M0_out[2]), .B(M1_out[1]), .C_In(A0_c_out), .R(A1_0_r), .C_Out(A1_0_c_out));
  Half_Adder A1_1 (.A(A1_0_r), .B(M2_out[0]), .R(ANS[2]), .C_Out(A1_1_c_out));
  Half_Adder A1_C (.A(A1_1_c_out), .B(A1_0_c_out), .R(A1_C_r), .C_Out(A1_C_c_out));
  Full_Adder A2_0 (.A(M0_out[3]), .B(M1_out[2]), .C_In(A1_C_r), .R(A2_0_r), .C_Out(A2_0_c_out));
  Full_Adder A2_1 (.A(A2_0_r), .B(M2_out[1]), .C_In(M3_out[0]), .R(ANS[3]), .C_Out(A2_1_c_out));
  Full_Adder A3_0 (.A(M0_out[4]), .B(M1_out[3]), .C_In(M2_out[2]), .R(A3_0_r), .C_Out(A3_0_c_out));
  Full_Adder A2_C (.A(A1_C_c_out), .B(A2_0_c_out), .C_In(A2_1_c_out), .R(A2_C_r), .C_Out(A2_C_c_out));
  Full_Adder A3_1 (.A(M3_out[1]), .B(M4_out[0]), .C_In(A2_C_r), .R(A3_1_r), .C_Out(A3_1_c_out));
  Half_Adder A3_2 (.A(A3_0_r), .B(A3_1_r), .R(ANS[4]), .C_Out(A3_2_c_out));
  Full_Adder A3_C_0 (.A(A3_0_c_out), .B(A2_C_c_out), .C_In(A3_2_c_out), .R(A3_C_0_r), .C_Out(A3_C_0_c_out));
  Half_Adder A3_C_1 (.A(A3_C_0_r), .B(A3_1_c_out), .R(A3_C_1_r), .C_Out(A3_C_1_c_out));
  Full_Adder A4_0 (.A(M0_out[5]), .B(M1_out[4]), .C_In(M2_out[3]), .R(A4_0_r), .C_Out(A4_0_c_out));
  Full_Adder A4_1 (.A(A4_0_r), .B(M3_out[2]), .C_In(M4_out[1]), .R(A4_1_r), .C_Out(A4_1_c_out));
  Full_Adder A4_C_0 (.A(A3_C_0_c_out), .B(A3_C_1_c_out), .C_In(A4_0_c_out), .R(A4_C_0_r), .C_Out(A4_C_0_c_out));
  Full_Adder A4_2 (.A(A4_1_r), .B(A3_C_1_r), .C_In(M5_out[0]), .R(ANS[5]), .C_Out(A4_2_c_out));
  Full_Adder A4_C_1 (.A(A4_C_0_r), .B(A4_1_c_out), .C_In(A4_2_c_out), .R(A4_C_1_r), .C_Out(A4_C_1_c_out));
  Full_Adder A5_0 (.A(M0_out[6]), .B(M1_out[5]), .C_In(M2_out[4]), .R(A5_0_r), .C_Out(A5_0_c_out));
  Full_Adder A5_1 (.A(M3_out[3]), .B(M4_out[2]), .C_In(M5_out[1]), .R(A5_1_r), .C_Out(A5_1_c_out));
  Full_Adder A5_2 (.A(A5_0_r), .B(A5_1_r), .C_In(M6_out[0]), .R(A5_2_r), .C_Out(A5_2_c_out));
  Full_Adder A5_C_0 (.A(A4_C_1_c_out), .B(A4_C_0_c_out), .C_In(A5_1_c_out), .R(A5_C_0_r), .C_Out(A5_C_0_c_out));
  Full_Adder A6_0 (.A(M0_out[7]), .B(M1_out[6]), .C_In(M2_out[5]), .R(A6_0_r), .C_Out(A6_0_c_out));
  Half_Adder A5_3 (.A(A5_2_r), .B(A4_C_1_r), .R(ANS[6]), .C_Out(A5_3_c_out));
  Full_Adder A6_1 (.A(A6_0_r), .B(M3_out[4]), .C_In(M4_out[3]), .R(A6_1_r), .C_Out(A6_1_c_out));
  Full_Adder A5_C_1 (.A(A5_2_c_out), .B(A5_3_c_out), .C_In(A5_C_0_r), .R(A5_C_1_r), .C_Out(A5_C_1_c_out));
  Half_Adder A5_C_2 (.A(A5_0_c_out), .B(A5_C_1_r), .R(A5_C_2_r), .C_Out(A5_C_2_c_out));
  Full_Adder A6_2 (.A(M5_out[2]), .B(M6_out[1]), .C_In(A6_1_r), .R(A6_2_r), .C_Out(A6_2_c_out));
  Full_Adder A6_3 (.A(A6_2_r), .B(M7_out[0]), .C_In(A5_C_2_r), .R(ANS[7]), .C_Out(A6_3_c_out));
endmodule

module Half_Adder (
  input  A,
  input  B,
  output R,
  output C_Out
);

  wire or_1_out;

  and and_1 (C_Out, A, B);
  or or_1 (or_1_out, A, B);
  and and_2 (R, ~C_Out, or_1_out);  // AND_Gate
endmodule

module Full_Adder (
  input  A,
  input  B,
  input  C_In,
  output R,
  output C_Out
);

  wire A_B_out, A_C_out, and_1_out, and_2_out, and_3_out, B_C_out, or_1_out;

  and A_B (A_B_out, A, B);
  and A_C (A_C_out, A, C_In);
  and B_C (B_C_out, B, C_In);
  and and_1 (and_1_out, A, B, C_In);
  or or_1 (or_1_out, A, B, C_In);
  and and_2 (and_2_out, ~A_B_out, ~A_C_out, ~B_C_out);  // AND_Gate
  and and_3 (and_3_out, or_1_out, and_2_out);
  or or_2 (C_Out, A_B_out, A_C_out, B_C_out);
  or or_3 (R, and_1_out, and_3_out);
endmodule
