// Logisim project RAM.circ as structural Verilog: 2 circuits, main circuit RAM
module RAM (
  input  READ_WRITE_f67e6d73,
  input  [3:0] ADDR
);

  wire B7_q, B9_q, B9_qn, L_2_81409bbd_qn, L_3_14cdc8b2_qn;
  wire [0:0] not_28_out;
  wire [1:0] not_11_out;
  wire [1:1] not_20_out;
  wire [2:0] not_8_out, not_26_out;
  wire [2:1] not_18_out;
  wire [2:2] not_32_out;
  wire [3:0] not_1_out, not_5_out, not_21_out, not_24_out;
  wire [3:1] not_13_out, not_16_out;
  wire [3:2] not_29_out;
  wire [3:3] not_31_out;
  wire [7:0] _0000_data_out, _0001_data_out, _0010_data_out, _0011_data_out, _0100_data_out, _0101_data_out,
       _0110_data_out, _0111_data_out, _1000_data_out, _1001_data_out, _1010_data_out, _1011_data_out,
       _1100_data_out, _1101_data_out, _1110_data_out, _1111_data_out, or_1_out, undriven, undriven_2;

  Clock CLK (.out(undriven_2[5]));
  RAM_BYTE _0000 (
    .CLK_IN(undriven_2[5]), .MODE(READ_WRITE_f67e6d73), .ADDR(not_1_out), .DATA_OUT(_0000_data_out),
    .DATA_IN({undriven_2[7:5], {3{undriven_2[5]}}, undriven_2[1:0]}));
  RAM_BYTE _0100 (
    .CLK_IN(undriven_2[5]), .MODE(READ_WRITE_f67e6d73), .ADDR({not_5_out[3], ADDR[2], not_5_out[1:0]}),
    .DATA_OUT(_0100_data_out), .DATA_IN(undriven));
  RAM_BYTE _1000 (
    .CLK_IN(undriven_2[5]), .MODE(READ_WRITE_f67e6d73), .ADDR({ADDR[3], not_8_out}),
    .DATA_OUT(_1000_data_out), .DATA_IN({undriven_2[7:5], {3{undriven_2[5]}}, undriven_2[1:0]}));
  RAM_BYTE _1100 (
    .CLK_IN(undriven_2[5]), .MODE(READ_WRITE_f67e6d73), .ADDR({ADDR[3:2], not_11_out}),
    .DATA_OUT(_1100_data_out), .DATA_IN({undriven_2[7:5], {3{undriven_2[5]}}, undriven_2[1:0]}));
  not not_1 (not_1_out[0], ADDR[0]);
  not not_2 (not_1_out[1], ADDR[1]);
  not not_3 (not_1_out[2], ADDR[2]);
  not not_4 (not_1_out[3], ADDR[3]);
  not not_5 (not_5_out[0], ADDR[0]);
  not not_6 (not_5_out[1], ADDR[1]);
  not not_7 (not_5_out[3], ADDR[3]);
  not not_8 (not_8_out[0], ADDR[0]);
  not not_9 (not_8_out[1], ADDR[1]);
  not not_10 (not_8_out[2], ADDR[2]);
  not not_11 (not_11_out[0], ADDR[0]);
  not not_12 (not_11_out[1], ADDR[1]);
  D_Flip_Flop B9 (.clk(or_1_out[7]), .Q(B9_q), .Qn(B9_qn), .preset(undriven_2[5]), .reset(or_1_out[6]));  // open: D
  RAM_BYTE _0001 (
    .CLK_IN(undriven_2[5]), .MODE(READ_WRITE_f67e6d73), .ADDR({not_13_out, ADDR[0]}),
    .DATA_OUT(_0001_data_out), .DATA_IN({undriven_2[7:5], {3{undriven_2[5]}}, undriven_2[1:0]}));
  RAM_BYTE _0101 (
    .CLK_IN(undriven_2[5]), .MODE(READ_WRITE_f67e6d73),
    .ADDR({not_16_out[3], ADDR[2], not_16_out[1], ADDR[0]}), .DATA_OUT(_0101_data_out), .DATA_IN(undriven));
  RAM_BYTE _1001 (
    .CLK_IN(undriven_2[5]), .MODE(READ_WRITE_f67e6d73), .ADDR({ADDR[3], not_18_out, ADDR[0]}),
    .DATA_OUT(_1001_data_out), .DATA_IN({undriven_2[7:5], {3{undriven_2[5]}}, undriven_2[1:0]}));
  RAM_BYTE _1101 (
    .CLK_IN(undriven_2[5]), .MODE(READ_WRITE_f67e6d73), .ADDR({ADDR[3:2], not_20_out[1], ADDR[0]}),
    .DATA_OUT(_1101_data_out), .DATA_IN({undriven_2[7:5], {3{undriven_2[5]}}, undriven_2[1:0]}));
  D_Flip_Flop B7 (.D(B9_q), .clk(B9_qn), .Q(B7_q), .Qn(or_1_out[5]), .preset(undriven_2[5]), .reset(or_1_out[6]));
  not not_13 (not_13_out[1], ADDR[1]);
  not not_14 (not_13_out[2], ADDR[2]);
  not not_15 (not_13_out[3], ADDR[3]);
  not not_16 (not_16_out[1], ADDR[1]);
  not not_17 (not_16_out[3], ADDR[3]);
  not not_18 (not_18_out[1], ADDR[1]);
  not not_19 (not_18_out[2], ADDR[2]);
  not not_20 (not_20_out[1], ADDR[1]);
  D_Flip_Flop L_4_4e7a8a8b (
    .D(undriven_2[5]), .clk(or_1_out[5]), .Q(undriven_2[5]), .preset(undriven_2[5]), .reset(or_1_out[3]));  // open: Qn
  D_Flip_Flop L_5_6949ef7c (
    .D(B7_q), .clk(or_1_out[5]), .Q(undriven_2[5]), .Qn(or_1_out[5]), .preset(undriven_2[5]),
    .reset(or_1_out[6]));
  D_Flip_Flop L_3_14cdc8b2 (
    .D(undriven_2[5]), .Q(undriven_2[5]), .Qn(L_3_14cdc8b2_qn), .preset(undriven_2[5]), .reset(or_1_out[2]));  // open: clk
  assign or_1_out = _1100_data_out | _1000_data_out | _0100_data_out | _0000_data_out | _1101_data_out | _1001_data_out | _0101_data_out | _0001_data_out | _1110_data_out | _1010_data_out | _0110_data_out | _0010_data_out | _1111_data_out | _1011_data_out | _0111_data_out | _0011_data_out;  // OR_Gate or_1, 8 bits wide
  RAM_BYTE _0010 (
    .CLK_IN(undriven_2[5]), .MODE(READ_WRITE_f67e6d73), .ADDR({not_21_out[3:2], ADDR[1], not_21_out[0]}),
    .DATA_OUT(_0010_data_out), .DATA_IN({undriven_2[7:5], {3{undriven_2[5]}}, undriven_2[1:0]}));
  not not_21 (not_21_out[0], ADDR[0]);
  not not_22 (not_21_out[2], ADDR[2]);
  not not_23 (not_21_out[3], ADDR[3]);
  RAM_BYTE _0110 (
    .CLK_IN(undriven_2[5]), .MODE(READ_WRITE_f67e6d73), .ADDR({not_24_out[3], ADDR[2:1], not_24_out[0]}),
    .DATA_OUT(_0110_data_out), .DATA_IN(undriven));
  not not_24 (not_24_out[0], ADDR[0]);
  not not_25 (not_24_out[3], ADDR[3]);
  RAM_BYTE _1010 (
    .CLK_IN(undriven_2[5]), .MODE(READ_WRITE_f67e6d73),
    .ADDR({ADDR[3], not_26_out[2], ADDR[1], not_26_out[0]}), .DATA_OUT(_1010_data_out),
    .DATA_IN({undriven_2[7:5], {3{undriven_2[5]}}, undriven_2[1:0]}));
  not not_26 (not_26_out[0], ADDR[0]);
  not not_27 (not_26_out[2], ADDR[2]);
  RAM_BYTE _1110 (
    .CLK_IN(undriven_2[5]), .MODE(READ_WRITE_f67e6d73), .ADDR({ADDR[3:1], not_28_out[0]}),
    .DATA_OUT(_1110_data_out), .DATA_IN({undriven_2[7:5], {3{undriven_2[5]}}, undriven_2[1:0]}));
  not not_28 (not_28_out[0], ADDR[0]);
  D_Flip_Flop L_2_81409bbd (
    .D(undriven_2[5]), .clk(L_3_14cdc8b2_qn), .Q(undriven_2[5]), .Qn(L_2_81409bbd_qn),
    .preset(undriven_2[5]), .reset(or_1_out[1]));
  D_Flip_Flop d_ff_1 (
    .D(undriven_2[5]), .clk(L_2_81409bbd_qn), .preset(undriven_2[5]), .reset(or_1_out[0]));  // open: Q, Qn
  D_Flip_Flop d_ff_2 (.clk(undriven_2[5]), .D(or_1_out[0]));  // open: Q, Qn, preset, reset
  RAM_BYTE _0011 (
    .CLK_IN(undriven_2[5]), .MODE(READ_WRITE_f67e6d73), .ADDR({not_29_out, ADDR[1:0]}),
    .DATA_OUT(_0011_data_out), .DATA_IN({undriven_2[7:5], {3{undriven_2[5]}}, undriven_2[1:0]}));
  RAM_BYTE _0111 (
    .CLK_IN(undriven_2[5]), .MODE(READ_WRITE_f67e6d73), .ADDR({not_31_out[3], ADDR[2:0]}),
    .DATA_OUT(_0111_data_out), .DATA_IN(undriven));
  RAM_BYTE _1011 (
    .CLK_IN(undriven_2[5]), .MODE(READ_WRITE_f67e6d73), .ADDR({ADDR[3], not_32_out[2], ADDR[1:0]}),
    .DATA_OUT(_1011_data_out), .DATA_IN({undriven_2[7:5], {3{undriven_2[5]}}, undriven_2[1:0]}));
  RAM_BYTE _1111 (
    .CLK_IN(undriven_2[5]), .MODE(READ_WRITE_f67e6d73), .ADDR(ADDR), .DATA_OUT(_1111_data_out),
    .DATA_IN({undriven_2[7:5], {3{undriven_2[5]}}, undriven_2[1:0]}));
  not not_29 (not_29_out[2], ADDR[2]);
  not not_30 (not_29_out[3], ADDR[3]);
  not not_31 (not_31_out[3], ADDR[3]);
  not not_32 (not_32_out[2], ADDR[2]);

  // Notes on the sheet:
  //   read = 0, write = 1
endmodule

module RAM_BYTE (
  input  CLK_IN,
  input  [3:0] ADDR,
  input  MODE,
  input  [7:0] DATA_IN,
  output [7:0] DATA_OUT
);

  wire and_1_out, and_3_out, and_4_out, and_6_out, and_7_out, and_9_out, and_10_out, and_12_out, and_13_out,
       and_15_out, and_16_out, and_18_out, and_19_out, and_21_out, and_22_out, and_24_out, s_r_ff_1_q,
       s_r_ff_2_q, s_r_ff_3_q, s_r_ff_4_q, s_r_ff_5_q, s_r_ff_6_q, s_r_ff_7_q, s_r_ff_8_q;

  and and_1 (and_1_out, DATA_IN[7], ADDR[3], ADDR[2], ADDR[1], ADDR[2], MODE);
  and and_2 (DATA_OUT[7], s_r_ff_1_q, ADDR[3], ADDR[2], ADDR[1], ADDR[2], ~MODE);  // AND_Gate
  S_R_Flip_Flop s_r_ff_1 (.S(and_1_out), .R(and_3_out), .clk(CLK_IN), .Q(s_r_ff_1_q));  // open: reset, Qn, preset
  and and_3 (and_3_out, ~DATA_IN[7], ADDR[3], ADDR[2], ADDR[1], ADDR[2], MODE);  // AND_Gate
  and and_4 (and_4_out, DATA_IN[6], ADDR[3], ADDR[2], ADDR[1], ADDR[2], MODE);
  and and_5 (DATA_OUT[6], s_r_ff_2_q, ADDR[3], ADDR[2], ADDR[1], ADDR[2], ~MODE);  // AND_Gate
  S_R_Flip_Flop s_r_ff_2 (.S(and_4_out), .R(and_6_out), .clk(CLK_IN), .Q(s_r_ff_2_q));  // open: reset, Qn, preset
  and and_6 (and_6_out, ~DATA_IN[6], ADDR[3], ADDR[2], ADDR[1], ADDR[2], MODE);  // AND_Gate
  S_R_Flip_Flop s_r_ff_3 (.S(and_7_out), .R(and_9_out), .clk(CLK_IN), .Q(s_r_ff_3_q));  // open: reset, Qn, preset
  and and_7 (and_7_out, DATA_IN[5], ADDR[3], ADDR[2], ADDR[1], ADDR[2], MODE);
  and and_8 (DATA_OUT[5], s_r_ff_3_q, ADDR[3], ADDR[2], ADDR[1], ADDR[2], ~MODE);  // AND_Gate
  and and_9 (and_9_out, ~DATA_IN[5], ADDR[3], ADDR[2], ADDR[1], ADDR[2], MODE);  // AND_Gate
  and and_10 (and_10_out, DATA_IN[4], ADDR[3], ADDR[2], ADDR[1], ADDR[2], MODE);
  S_R_Flip_Flop s_r_ff_4 (.S(and_10_out), .R(and_12_out), .clk(CLK_IN), .Q(s_r_ff_4_q));  // open: reset, Qn, preset
  and and_11 (DATA_OUT[4], s_r_ff_4_q, ADDR[3], ADDR[2], ADDR[1], ADDR[2], ~MODE);  // AND_Gate
  and and_12 (and_12_out, ~DATA_IN[4], ADDR[3], ADDR[2], ADDR[1], ADDR[2], MODE);  // AND_Gate
  and and_13 (and_13_out, DATA_IN[3], ADDR[3], ADDR[2], ADDR[1], ADDR[2], MODE);
  and and_14 (DATA_OUT[3], s_r_ff_5_q, ADDR[3], ADDR[2], ADDR[1], ADDR[2], ~MODE);  // AND_Gate
  S_R_Flip_Flop s_r_ff_5 (.S(and_13_out), .R(and_15_out), .clk(CLK_IN), .Q(s_r_ff_5_q));  // open: reset, Qn, preset
  and and_15 (and_15_out, ~DATA_IN[3], ADDR[3], ADDR[2], ADDR[1], ADDR[2], MODE);  // AND_Gate
  and and_16 (and_16_out, DATA_IN[2], ADDR[3], ADDR[2], ADDR[1], ADDR[2], MODE);
  and and_17 (DATA_OUT[2], s_r_ff_6_q, ADDR[3], ADDR[2], ADDR[1], ADDR[2], ~MODE);  // AND_Gate
  S_R_Flip_Flop s_r_ff_6 (.S(and_16_out), .R(and_18_out), .clk(CLK_IN), .Q(s_r_ff_6_q));  // open: reset, Qn, preset
  and and_18 (and_18_out, ~DATA_IN[2], ADDR[3], ADDR[2], ADDR[1], ADDR[2], MODE);  // AND_Gate
  S_R_Flip_Flop s_r_ff_7 (.S(and_19_out), .R(and_21_out), .clk(CLK_IN), .Q(s_r_ff_7_q));  // open: reset, Qn, preset
  and and_19 (and_19_out, DATA_IN[1], ADDR[3], ADDR[2], ADDR[1], ADDR[2], MODE);
  and and_20 (DATA_OUT[1], s_r_ff_7_q, ADDR[3], ADDR[2], ADDR[1], ADDR[2], ~MODE);  // AND_Gate
  and and_21 (and_21_out, ~DATA_IN[1], ADDR[3], ADDR[2], ADDR[1], ADDR[2], MODE);  // AND_Gate
  and and_22 (and_22_out, DATA_IN[0], ADDR[3], ADDR[2], ADDR[1], ADDR[2], MODE);
  S_R_Flip_Flop s_r_ff_8 (.S(and_22_out), .R(and_24_out), .clk(CLK_IN), .Q(s_r_ff_8_q));  // open: reset, Qn, preset
  and and_23 (DATA_OUT[0], s_r_ff_8_q, ADDR[3], ADDR[2], ADDR[1], ADDR[2], ~MODE);  // AND_Gate
  and and_24 (and_24_out, ~DATA_IN[0], ADDR[3], ADDR[2], ADDR[1], ADDR[2], MODE);  // AND_Gate

  assign ADDR[0] = ADDR[2];
endmodule
