// Logisim project DABBY.circ as structural Verilog: 2 circuits, main circuit LIL_DABBLER
module DABBLER (
  input  [7:0] in_1,
  output [3:0] out_2,
  output [3:0] out_3,
  output [3:0] out_4
);

  wire lil_dabbler_1_out_5, lil_dabbler_1_out_6, lil_dabbler_1_out_7, lil_dabbler_2_out_5,
       lil_dabbler_2_out_6, lil_dabbler_2_out_7, lil_dabbler_3_out_5, lil_dabbler_4_out_5,
       lil_dabbler_4_out_6, lil_dabbler_5_out_5, lil_dabbler_5_out_6, lil_dabbler_5_out_7,
       lil_dabbler_5_out_8, lil_dabbler_6_out_5, lil_dabbler_6_out_6, lil_dabbler_6_out_7,
       lil_dabbler_6_out_8, lil_dabbler_7_out_5, lil_dabbler_7_out_6, lil_dabbler_7_out_7,
       lil_dabbler_9_out_5, lil_dabbler_9_out_6, lil_dabbler_9_out_7, lil_dabbler_9_out_8,
       lil_dabbler_10_out_5, lil_dabbler_10_out_6, lil_dabbler_10_out_7, lil_dabbler_10_out_8;

  LIL_DABBLER lil_dabbler_1 (
    .out_7(lil_dabbler_1_out_7), .out_6(lil_dabbler_1_out_6), .out_8(out_2[3]), .in_1(lil_dabbler_5_out_8),
    .out_5(lil_dabbler_1_out_5));  // open: in_3, in_2, in_4
  LIL_DABBLER lil_dabbler_2 (
    .out_7(lil_dabbler_2_out_7), .in_3(lil_dabbler_1_out_6), .in_2(lil_dabbler_1_out_5),
    .out_6(lil_dabbler_2_out_6), .in_4(lil_dabbler_1_out_7), .out_8(out_2[2]), .in_1(lil_dabbler_6_out_8),
    .out_5(lil_dabbler_2_out_5));
  LIL_DABBLER lil_dabbler_3 (
    .in_3(1'b0), .in_2(1'b0), .in_4(1'b0), .in_1(in_1[7]), .out_5(lil_dabbler_3_out_5));  // open: out_7, out_6, out_8
  LIL_DABBLER lil_dabbler_4 (
    .in_2(lil_dabbler_3_out_5), .out_6(lil_dabbler_4_out_6), .in_1(in_1[6]), .out_5(lil_dabbler_4_out_5));  // open: out_7, in_3, in_4, out_8
  LIL_DABBLER lil_dabbler_5 (
    .out_7(lil_dabbler_5_out_7), .in_3(lil_dabbler_4_out_6), .in_2(lil_dabbler_4_out_5),
    .out_6(lil_dabbler_5_out_6), .out_8(lil_dabbler_5_out_8), .in_1(in_1[5]), .out_5(lil_dabbler_5_out_5));  // open: in_4
  LIL_DABBLER lil_dabbler_6 (
    .out_7(lil_dabbler_6_out_7), .in_3(lil_dabbler_5_out_6), .in_2(lil_dabbler_5_out_5),
    .out_6(lil_dabbler_6_out_6), .in_4(lil_dabbler_5_out_7), .out_8(lil_dabbler_6_out_8), .in_1(in_1[4]),
    .out_5(lil_dabbler_6_out_5));
  LIL_DABBLER lil_dabbler_7 (
    .out_7(lil_dabbler_7_out_7), .in_3(lil_dabbler_2_out_6), .in_2(lil_dabbler_2_out_5),
    .out_6(lil_dabbler_7_out_6), .in_4(lil_dabbler_2_out_7), .out_8(out_2[1]), .in_1(lil_dabbler_9_out_8),
    .out_5(lil_dabbler_7_out_5));
  LIL_DABBLER lil_dabbler_8 (
    .out_7(out_3[3]), .in_3(lil_dabbler_7_out_6), .in_2(lil_dabbler_7_out_5), .out_6(out_3[2]),
    .in_4(lil_dabbler_7_out_7), .out_8(out_2[0]), .in_1(lil_dabbler_10_out_8), .out_5(out_3[1]));
  LIL_DABBLER lil_dabbler_9 (
    .out_7(lil_dabbler_9_out_7), .in_3(lil_dabbler_6_out_6), .in_2(lil_dabbler_6_out_5),
    .out_6(lil_dabbler_9_out_6), .in_4(lil_dabbler_6_out_7), .out_8(lil_dabbler_9_out_8), .in_1(in_1[3]),
    .out_5(lil_dabbler_9_out_5));
  LIL_DABBLER lil_dabbler_10 (
    .out_7(lil_dabbler_10_out_7), .in_3(lil_dabbler_9_out_6), .in_2(lil_dabbler_9_out_5),
    .out_6(lil_dabbler_10_out_6), .in_4(lil_dabbler_9_out_7), .out_8(lil_dabbler_10_out_8), .in_1(in_1[2]),
    .out_5(lil_dabbler_10_out_5));
  LIL_DABBLER lil_dabbler_11 (
    .out_7(out_4[3]), .in_3(lil_dabbler_10_out_6), .in_2(lil_dabbler_10_out_5), .out_6(out_4[2]),
    .in_4(lil_dabbler_10_out_7), .out_8(out_3[0]), .in_1(in_1[1]), .out_5(out_4[1]));

  assign out_4[0] = in_1[0];
endmodule

module LIL_DABBLER (
  input  in_1,
  input  in_2,
  input  in_3,
  input  in_4,
  output out_5,
  output out_6,
  output out_7,
  output out_8
);

  wire and_1_out, and_2_out, and_3_out, and_4_out, and_5_out, and_6_out, or_1_out, or_2_out, or_3_out,
       or_4_out, xor_3_out;

  xor xor_1 (out_5, in_1, and_1_out);
  and and_1 (and_1_out, in_2, or_4_out);
  and and_2 (and_2_out, in_2, or_1_out);
  xor xor_2 (out_6, in_2, or_4_out);
  or or_1 (or_1_out, in_3, in_4);
  or or_2 (or_2_out, and_2_out, in_1);
  or or_3 (or_3_out, and_2_out, in_1);
  and and_3 (and_3_out, in_3, or_3_out);
  and and_4 (and_4_out, in_3, and_6_out);
  or or_4 (or_4_out, and_3_out, and_4_out, and_5_out);
  and and_5 (and_5_out, or_3_out, and_6_out);
  xor xor_3 (xor_3_out, or_3_out, and_6_out);
  xor xor_4 (out_7, in_3, xor_3_out);
  xor xor_5 (out_8, in_4, or_2_out);
  and and_6 (and_6_out, in_4, or_2_out);

  // Notes on the sheet:
  //   if 5, add 3
endmodule
