// Logisim project SM_Dabbler_Prototype.circ as structural Verilog: 4 circuits, main circuit LIL_DABBLER
module LIL_DABBLER (
  input  in_1,
  input  in_2,
  input  in_3,
  input  in_4,
  output out_5,
  output out_6,
  output out_7,
  output out_8
);

  wire add_1bit_2_cout, add_1bit_3_cout, add_1bit_4_cout, and_1_out, or_1_out, or_2_out, or_3_out;

  Add_1Bit add_1bit_1 (.Sum(out_5), .B(in_1), .Cin(add_1bit_2_cout));  // open: Cout, A
  and and_1 (and_1_out, in_2, or_1_out);
  Add_1Bit add_1bit_2 (.Cout(add_1bit_2_cout), .Sum(out_6), .B(in_2), .Cin(add_1bit_3_cout));  // open: A
  or or_1 (or_1_out, in_3, in_4);
  or or_2 (or_2_out, and_1_out, in_1);
  or or_3 (or_3_out, and_1_out, in_1);
  Add_1Bit add_1bit_3 (.Cout(add_1bit_3_cout), .Sum(out_7), .B(in_3), .A(or_3_out), .Cin(add_1bit_4_cout));
  Add_1Bit add_1bit_4 (.Cout(add_1bit_4_cout), .Sum(out_8), .B(in_4), .A(or_2_out));  // open: Cin

  // Notes on the sheet:
  //   if 5, add 3
  //   can be replaced if causes issues with nesting
endmodule

module Add_1Bit (
  input  Cin,
  input  A,
  input  B,
  output Sum,
  output Cout
);

  wire and_1_out, and_2_out, and_3_out, xor_1_out;

  xor xor_1 (xor_1_out, Cin, A);
  xor xor_2 (Sum, xor_1_out, B);
  and and_1 (and_1_out, Cin, A);
  and and_2 (and_2_out, Cin, B);
  and and_3 (and_3_out, A, B);
  or or_1 (Cout, and_1_out, and_2_out, and_3_out);
endmodule

module DOUBLE_DABBLE (
  input  [7:0] in_1,
  output [3:0] HUNDREDS,
  output [3:0] TENS,
  output [3:0] ONES
);

  wire lil_dabbler_1_out_8, lil_dabbler_2_out_6, lil_dabbler_2_out_7, lil_dabbler_2_out_8,
       lil_dabbler_3_out_6, lil_dabbler_3_out_7, lil_dabbler_3_out_8, lil_dabbler_4_out_6,
       lil_dabbler_4_out_7, lil_dabbler_4_out_8, lil_dabbler_5_out_7, lil_dabbler_5_out_8,
       lil_dabbler_6_out_5, lil_dabbler_6_out_6, lil_dabbler_6_out_7, lil_dabbler_6_out_8,
       lil_dabbler_7_out_5, lil_dabbler_7_out_6, lil_dabbler_7_out_7, lil_dabbler_7_out_8,
       lil_dabbler_8_out_5, lil_dabbler_8_out_6, lil_dabbler_8_out_7, lil_dabbler_8_out_8,
       lil_dabbler_10_out_5, lil_dabbler_10_out_6, lil_dabbler_10_out_7, lil_dabbler_10_out_8;

  LIL_DABBLER lil_dabbler_1 (
    .in_4(in_1[7]), .in_3(1'b0), .in_2(1'b0), .in_1(1'b0), .out_8(lil_dabbler_1_out_8));  // open: out_7, out_6, out_5
  LIL_DABBLER lil_dabbler_2 (
    .out_7(lil_dabbler_2_out_7), .out_6(lil_dabbler_2_out_6), .out_5(HUNDREDS[3]),
    .in_4(lil_dabbler_6_out_5), .out_8(lil_dabbler_2_out_8));  // open: in_3, in_2, in_1
  LIL_DABBLER lil_dabbler_3 (
    .out_7(lil_dabbler_3_out_7), .out_6(lil_dabbler_3_out_6), .out_5(HUNDREDS[2]),
    .in_4(lil_dabbler_7_out_5), .in_3(lil_dabbler_2_out_8), .in_2(lil_dabbler_2_out_7),
    .in_1(lil_dabbler_2_out_6), .out_8(lil_dabbler_3_out_8));
  LIL_DABBLER lil_dabbler_4 (
    .out_7(lil_dabbler_4_out_7), .out_6(lil_dabbler_4_out_6), .out_5(HUNDREDS[1]),
    .in_4(lil_dabbler_8_out_5), .in_3(lil_dabbler_3_out_8), .in_2(lil_dabbler_3_out_7),
    .in_1(lil_dabbler_3_out_6), .out_8(lil_dabbler_4_out_8));
  LIL_DABBLER lil_dabbler_5 (
    .out_7(lil_dabbler_5_out_7), .in_4(in_1[6]), .in_3(lil_dabbler_1_out_8), .out_8(lil_dabbler_5_out_8));  // open: out_6, out_5, in_2, in_1
  LIL_DABBLER lil_dabbler_6 (
    .out_7(lil_dabbler_6_out_7), .out_6(lil_dabbler_6_out_6), .out_5(lil_dabbler_6_out_5), .in_4(in_1[5]),
    .in_3(lil_dabbler_5_out_8), .in_2(lil_dabbler_5_out_7), .out_8(lil_dabbler_6_out_8));  // open: in_1
  LIL_DABBLER lil_dabbler_7 (
    .out_7(lil_dabbler_7_out_7), .out_6(lil_dabbler_7_out_6), .out_5(lil_dabbler_7_out_5), .in_4(in_1[4]),
    .in_3(lil_dabbler_6_out_8), .in_2(lil_dabbler_6_out_7), .in_1(lil_dabbler_6_out_6),
    .out_8(lil_dabbler_7_out_8));
  LIL_DABBLER lil_dabbler_8 (
    .out_7(lil_dabbler_8_out_7), .out_6(lil_dabbler_8_out_6), .out_5(lil_dabbler_8_out_5), .in_4(in_1[3]),
    .in_3(lil_dabbler_7_out_8), .in_2(lil_dabbler_7_out_7), .in_1(lil_dabbler_7_out_6),
    .out_8(lil_dabbler_8_out_8));
  LIL_DABBLER lil_dabbler_9 (
    .out_7(TENS[2]), .out_6(TENS[3]), .out_5(HUNDREDS[0]), .in_4(lil_dabbler_10_out_5),
    .in_3(lil_dabbler_4_out_8), .in_2(lil_dabbler_4_out_7), .in_1(lil_dabbler_4_out_6), .out_8(TENS[1]));
  LIL_DABBLER lil_dabbler_10 (
    .out_7(lil_dabbler_10_out_7), .out_6(lil_dabbler_10_out_6), .out_5(lil_dabbler_10_out_5), .in_4(in_1[2]),
    .in_3(lil_dabbler_8_out_8), .in_2(lil_dabbler_8_out_7), .in_1(lil_dabbler_8_out_6),
    .out_8(lil_dabbler_10_out_8));
  LIL_DABBLER lil_dabbler_11 (
    .out_7(ONES[2]), .out_6(ONES[3]), .out_5(TENS[0]), .in_4(in_1[1]), .in_3(lil_dabbler_10_out_8),
    .in_2(lil_dabbler_10_out_7), .in_1(lil_dabbler_10_out_6), .out_8(ONES[1]));

  assign ONES[0] = in_1[0];

  // Notes on the sheet:
  //   only one wire connected because output at most 1
  //   only one wire connected, because output at most 3
  //   two lil dabblers and four wires connected, because output at most 8
endmodule

module test (
  input  [7:0] in_1
);

  wire [3:0] double_dabble_1_hundreds, double_dabble_1_ones, double_dabble_1_tens;

  DOUBLE_DABBLE double_dabble_1 (
    .ONES(double_dabble_1_ones), .TENS(double_dabble_1_tens), .HUNDREDS(double_dabble_1_hundreds), .in_1(in_1));
  Hex_Digit_Display hex_digit_display_1 (.value(double_dabble_1_tens));  // open: dp
  Hex_Digit_Display hex_digit_display_2 (.value(double_dabble_1_hundreds));  // open: dp
  Hex_Digit_Display hex_digit_display_3 (.value(double_dabble_1_ones));  // open: dp
endmodule
