// Logisim project SM_Instr_Main.circ as structural Verilog: 23 circuits, main circuit RAM_BYTE
module main (
  input  [7:0] in_1,
  input  [7:0] in_2,
  input  K8,
  input  K9,
  input  K7,
  input  K5,
  input  K6,
  input  K4,
  input  K2,
  input  K3,
  input  K1,
  input  ON_0,
  input  K0,
  input  [3:0] in_14,
  input  [3:0] in_15,
  input  [3:0] in_16,
  output [7:0] R0000,
  output [7:0] R0001,
  output [7:0] R0010,
  output [7:0] R0011,
  output [7:0] R0100,
  output [7:0] R0101,
  output [7:0] R0110,
  output [7:0] R0111,
  output [3:0] out_25,
  output [7:0] R1000,
  output [7:0] R1001,
  output [7:0] R1010,
  output [7:0] R1011,
  output [7:0] out_30,
  output [7:0] R1100,
  output [7:0] R1101,
  output [7:0] R1110,
  output [7:0] R1111,
  output [7:0] out_35,
  output [3:0] out_36,
  output [3:0] out_37,
  output [7:0] D0,
  output [2:0] out_39,
  output [7:0] D1
);

  wire All_0_out, and_5_out, C_14_out, C_15_out, CLK_out, clock_1_out, D_0_out, D_1_out, INP_D_out, MODE_q,
       not_1_out, not_2_out, or_1_out, or_4_out, or_6_out, STR_1_out, STR_D_out;
  wire [0:0] not_3_out;
  wire [2:0] alu_1_status;
  wire [3:0] and_4_out, and_6_out, and_7_out, BEQ_IN_out, inc_1_out_0, inc_2_out_0, mar_1_outadr, or_3_out,
       or_7_out, pc_1_out_0, STR_ADR_out;
  wire [3:3] BEQ_0_out, BEQ_out, eq_1_eq, INP_out, STR_0_out, STR_out;
  wire [6:0] encode_display_1_out_2, encode_display_2_out_2, encode_display_3_out_2;
  wire [7:0] A_Out_byte_out, alu_1_a_out, and_1_out, and_2_out, and_3_out, gen_register_1_data_out,
       gen_register_2_data_out, Input_Buffer_byte_out, keypad_1_output, mbr_1_out_0, or_2_out, or_5_out,
       ram_1_dr_out;
  wire [7:7] ADDR_out, INP_0_out;

  D_Flip_Flop MODE (.D(or_1_out), .clk(CLK_out), .Q(MODE_q));  // open: Qn, preset, reset
  or or_1 (or_1_out, STR_0_out[3], STR_1_out);
  ENCODE_DISPLAY encode_display_1 (.out_2(encode_display_1_out_2), .in_1(in_14));
  AR ar_1 (.IN_OR_OUT(not_1_out), .ADR_IN(mar_1_outadr), .CLK_IN(CLK_out), .ADR_OUT(out_36));
  not not_1 (not_1_out, STR_1_out);
  _7_Segment_Display u_7_segment_display_1 (
    .g(encode_display_1_out_2[0]), .f(encode_display_1_out_2[1]), .a(encode_display_1_out_2[2]),
    .b(encode_display_1_out_2[3]), .e(encode_display_1_out_2[4]), .d(encode_display_1_out_2[5]),
    .c(encode_display_1_out_2[6]));  // open: dp
  RAM ram_1 (
    .CLK(CLK_out), .READ_WRITE(MODE_q), .ADDR(out_36), .DR_IN(mbr_1_out_0), .DR_OUT(ram_1_dr_out),
    .out_5(R0000), .out_6(R0001), .out_7(R0010), .out_8(R0011), .out_9(R0100), .out_10(R0101),
    .out_11(R0110), .out_12(R0111), .out_13(R1000), .out_14(R1001), .out_15(R1010), .out_16(R1011),
    .out_17(R1100), .out_18(R1101), .out_19(R1110), .out_20(R1111));  // open: out_21
  KeyPad keypad_1 (
    .Zero(K0), .One(K1), .Two(K2), .Three(K3), .Four(K4), .Five(K5), .Six(K6), .Seven(K7), .Eight(K8),
    .Nine(K9), .Output(keypad_1_output));
  ENCODE_DISPLAY encode_display_2 (.out_2(encode_display_2_out_2), .in_1(in_15));
  DATA_BYTE Input_Buffer (.Byte_In(keypad_1_output), .Byte_Out(Input_Buffer_byte_out), .CLK(CLK_out));  // open: NO_IN
  _7_Segment_Display u_7_segment_display_2 (
    .g(encode_display_2_out_2[0]), .f(encode_display_2_out_2[1]), .a(encode_display_2_out_2[2]),
    .b(encode_display_2_out_2[3]), .e(encode_display_2_out_2[4]), .d(encode_display_2_out_2[5]),
    .c(encode_display_2_out_2[6]));  // open: dp
  _7_Segment_Display u_7_segment_display_3 (
    .g(encode_display_3_out_2[0]), .f(encode_display_3_out_2[1]), .a(encode_display_3_out_2[2]),
    .b(encode_display_3_out_2[3]), .e(encode_display_3_out_2[4]), .d(encode_display_3_out_2[5]),
    .c(encode_display_3_out_2[6]));  // open: dp
  ENCODE_DISPLAY encode_display_3 (.out_2(encode_display_3_out_2), .in_1(in_16));
  assign or_2_out = and_2_out | and_1_out;  // OR_Gate or_2, 8 bits wide
  assign and_1_out = ~{8{ADDR_out[7]}} & gen_register_1_data_out;  // AND_Gate and_1, 8 bits wide
  assign and_2_out = {8{ADDR_out[7]}} & gen_register_2_data_out;  // AND_Gate and_2, 8 bits wide
  or ADDR (ADDR_out[7], INP_D_out, STR_D_out);
  and INP_D (INP_D_out, out_30[3], INP_0_out[7]);
  MAR mar_1 (.OutAdr(mar_1_outadr), .InAdr(STR_ADR_out), .Contents(out_25), .Clock(CLK_out), .In_Out(or_4_out));
  GEN_REGISTER gen_register_1 (
    .ADDR(D_0_out), .DATA_OUT(gen_register_1_data_out), .IN_OR_OUT(STR_out[3]), .DATA_IN(or_5_out),
    .CONTENTS(D0), .CLK_IN(clock_1_out));
  GEN_REGISTER gen_register_2 (
    .ADDR(D_1_out), .DATA_OUT(gen_register_2_data_out), .IN_OR_OUT(STR_out[3]), .DATA_IN(or_5_out),
    .CONTENTS(D1), .CLK_IN(clock_1_out));
  and STR_D (STR_D_out, out_30[4], STR_out[3]);
  MBR mbr_1 (.OUT_0(mbr_1_out_0), .CLK(CLK_out), .Contents(out_35), .IN_0(or_2_out), .IN_MODE(or_6_out));
  buf D_0 (D_0_out, ~ADDR_out[7]);  // OR_Gate OR_Gate
  buf D_1 (D_1_out, ADDR_out[7]);  // OR_Gate
  assign or_3_out = STR_ADR_out | STR_ADR_out | pc_1_out_0;  // OR_Gate or_3, 4 bits wide
  buf or_4 (or_4_out, ~STR_0_out[3]);  // OR_Gate OR_Gate
  assign STR_ADR_out = out_30[3:0] & {4{STR_0_out[3]}};  // AND_Gate STR_ADR, 4 bits wide
  assign or_5_out = in_2 | and_3_out | A_Out_byte_out;  // OR_Gate or_5, 8 bits wide
  assign and_3_out = Input_Buffer_byte_out & {8{INP_0_out[7]}};  // AND_Gate and_3, 8 bits wide
  buf or_6 (or_6_out, STR_1_out);  // OR_Gate
  DATA_BYTE A_Out (.Byte_In(alu_1_a_out), .Byte_Out(A_Out_byte_out), .CLK(clock_1_out));  // open: NO_IN
  PC pc_1 (
    .OUT_0(pc_1_out_0), .CLK(CLK_out), .IN_1(inc_1_out_0), .IN_MODE(and_5_out), .IN_0(BEQ_IN_out));  // open: NO_IN
  ALU alu_1 (.A_Out(alu_1_a_out), .Status(alu_1_status));  // open: R_In, Op, L_In
  EQ eq_1 (.EQ(eq_1_eq[3]), .IN_0(gen_register_2_data_out), .IN_1(gen_register_1_data_out));
  INC inc_1 (.OUT_0(inc_1_out_0), .IN_0(pc_1_out_0));  // open: ON_0
  Clock clock_1 (.out(clock_1_out));
  STATUS status_1 (.in_1(alu_1_status), .CLK(clock_1_out), .out_3(out_39));
  DATA_BYTE IR (.Byte_In(in_1), .Byte_Out(out_30), .CLK(CLK_out));  // open: NO_IN
  COUNT count_1 (
    .NO_IN(not_2_out), .IN_MODE(All_0_out), .CLK(CLK_out), .IN_1(or_7_out), .IN_0(inc_2_out_0), .OUT_0(out_37));
  not not_2 (not_2_out, ON_0);
  and All_0 (All_0_out, ~out_37[3], ~out_37[2], ~out_37[1], ~out_37[0]);  // AND_Gate
  INC inc_2 (.OUT_0(inc_2_out_0), .ON_0(ON_0), .IN_0(out_37));
  Clock CLK (.out(CLK_out));
  assign and_4_out = {4{STR_out[3]}} & {{3{STR_out[3]}}, not_3_out[0]};  // AND_Gate and_4, 4 bits wide
  assign or_7_out = and_4_out | and_6_out | and_7_out;  // OR_Gate or_7, 4 bits wide
  // AND_Gate C_13 has open pins: in0=out_37[0], in1=out_37[1], in2=out_37[2], in3=out_37[3], out=open
  and C_14 (C_14_out, ~out_37[0], out_37[1], out_37[2], out_37[3]);  // AND_Gate
  and C_15 (C_15_out, out_37[0], out_37[1], out_37[2], out_37[3]);
  and STR_1 (STR_1_out, C_15_out, STR_out[3]);
  and STR_0 (STR_0_out[3], C_14_out, STR_out[3]);
  and INP_0 (INP_0_out[7], C_15_out, INP_out[3]);
  and BEQ_0 (BEQ_0_out[3], C_15_out, BEQ_out[3]);
  and and_5 (and_5_out, eq_1_eq[3], BEQ_0_out[3]);
  and STR (STR_out[3], out_30[7], out_30[6], out_30[5]);
  not not_3 (not_3_out[0], STR_out[3]);
  and INP (INP_out[3], ~out_30[7], out_30[6], out_30[5], out_30[4]);  // AND_Gate
  assign and_6_out = {4{INP_out[3]}} & {4{INP_out[3]}};  // AND_Gate and_6, 4 bits wide
  assign BEQ_IN_out = out_30[3:0] & {4{BEQ_0_out[3]}} & {4{eq_1_eq[3]}};  // AND_Gate BEQ_IN, 4 bits wide
  and BEQ (BEQ_out[3], ~out_30[7], out_30[6], ~out_30[5], ~out_30[4]);  // AND_Gate
  assign and_7_out = {4{BEQ_out[3]}} & {4{BEQ_out[3]}};  // AND_Gate and_7, 4 bits wide
  // AND_Gate and_8 is placed but not wired

  // Notes on the sheet:
  //   OP
  //   CU
endmodule

module RAM (
  input  CLK,
  input  READ_WRITE,
  input  [3:0] ADDR,
  input  [7:0] DR_IN,
  output [7:0] out_5,
  output [7:0] out_6,
  output [7:0] out_7,
  output [7:0] out_8,
  output [7:0] out_9,
  output [7:0] out_10,
  output [7:0] out_11,
  output [7:0] out_12,
  output [7:0] out_13,
  output [7:0] out_14,
  output [7:0] out_15,
  output [7:0] out_16,
  output [7:0] out_17,
  output [7:0] out_18,
  output [7:0] out_19,
  output [7:0] out_20,
  output [7:0] out_21,
  output [7:0] DR_OUT
);

  wire [0:0] not_29_out;
  wire [1:0] not_11_out;
  wire [1:1] not_20_out;
  wire [2:0] not_8_out, not_27_out;
  wire [2:1] not_18_out;
  wire [2:2] not_33_out;
  wire [3:0] not_1_out, not_5_out, not_22_out, not_25_out;
  wire [3:1] not_13_out, not_16_out;
  wire [3:2] not_30_out;
  wire [3:3] not_32_out;
  wire [7:0] _0000_data_out, _0001_data_out, _0010_data_out, _0011_data_out, _0100_data_out, _0101_data_out,
       _0110_data_out, _0111_data_out, _1000_data_out, _1001_data_out, _1010_data_out, _1011_data_out,
       _1100_data_out, _1101_data_out, _1110_data_out, _1111_data_out, and_1_out, or_1_out, undriven;

  RAM_BYTE _0000 (
    .CLK_IN(CLK), .MODE(READ_WRITE), .ADDR(not_1_out), .DATA_OUT(_0000_data_out), .DATA_IN(out_21),
    .CONTENTS(out_5));
  RAM_BYTE _0100 (
    .CLK_IN(CLK), .MODE(READ_WRITE), .ADDR({not_5_out[3], ADDR[2], not_5_out[1:0]}),
    .DATA_OUT(_0100_data_out), .DATA_IN(undriven), .CONTENTS(out_9));
  RAM_BYTE _1000 (
    .CLK_IN(CLK), .MODE(READ_WRITE), .ADDR({ADDR[3], not_8_out}), .DATA_OUT(_1000_data_out),
    .DATA_IN(out_21), .CONTENTS(out_13));
  RAM_BYTE _1100 (
    .CLK_IN(CLK), .MODE(READ_WRITE), .ADDR({ADDR[3:2], not_11_out}), .DATA_OUT(_1100_data_out),
    .DATA_IN(out_21), .CONTENTS(out_17));
  not not_1 (not_1_out[0], ADDR[0]);
  not not_2 (not_1_out[1], ADDR[1]);
  not not_3 (not_1_out[2], ADDR[2]);
  not not_4 (not_1_out[3], ADDR[3]);
  not not_5 (not_5_out[0], ADDR[0]);
  not not_6 (not_5_out[1], ADDR[1]);
  not not_7 (not_5_out[3], ADDR[3]);
  not not_8 (not_8_out[0], ADDR[0]);
  not not_9 (not_8_out[1], ADDR[1]);
  not not_10 (not_8_out[2], ADDR[2]);
  not not_11 (not_11_out[0], ADDR[0]);
  not not_12 (not_11_out[1], ADDR[1]);
  RAM_BYTE _0001 (
    .CLK_IN(CLK), .MODE(READ_WRITE), .ADDR({not_13_out, ADDR[0]}), .DATA_OUT(_0001_data_out),
    .DATA_IN(out_21), .CONTENTS(out_6));
  RAM_BYTE _0101 (
    .CLK_IN(CLK), .MODE(READ_WRITE), .ADDR({not_16_out[3], ADDR[2], not_16_out[1], ADDR[0]}),
    .DATA_OUT(_0101_data_out), .DATA_IN(undriven), .CONTENTS(out_10));
  RAM_BYTE _1001 (
    .CLK_IN(CLK), .MODE(READ_WRITE), .ADDR({ADDR[3], not_18_out, ADDR[0]}), .DATA_OUT(_1001_data_out),
    .DATA_IN(out_21), .CONTENTS(out_14));
  RAM_BYTE _1101 (
    .CLK_IN(CLK), .MODE(READ_WRITE), .ADDR({ADDR[3:2], not_20_out[1], ADDR[0]}), .DATA_OUT(_1101_data_out),
    .DATA_IN(out_21), .CONTENTS(out_18));
  not not_13 (not_13_out[1], ADDR[1]);
  not not_14 (not_13_out[2], ADDR[2]);
  not not_15 (not_13_out[3], ADDR[3]);
  not not_16 (not_16_out[1], ADDR[1]);
  not not_17 (not_16_out[3], ADDR[3]);
  not not_18 (not_18_out[1], ADDR[1]);
  not not_19 (not_18_out[2], ADDR[2]);
  not not_20 (not_20_out[1], ADDR[1]);
  // NOT_Gate not_21 has open pins: in=READ_WRITE, out=open
  assign or_1_out = _1100_data_out | _1000_data_out | _0100_data_out | _0000_data_out | _1101_data_out | _1001_data_out | _0101_data_out | _0001_data_out | and_1_out | _1110_data_out | _1010_data_out | _0110_data_out | _0010_data_out | _1111_data_out | _1011_data_out | _0111_data_out | _0011_data_out;  // OR_Gate or_1, 8 bits wide
  assign and_1_out = {8{READ_WRITE}} & DR_IN;  // AND_Gate and_1, 8 bits wide
  RAM_BYTE _0010 (
    .CLK_IN(CLK), .MODE(READ_WRITE), .ADDR({not_22_out[3:2], ADDR[1], not_22_out[0]}),
    .DATA_OUT(_0010_data_out), .DATA_IN(out_21), .CONTENTS(out_7));
  not not_22 (not_22_out[0], ADDR[0]);
  not not_23 (not_22_out[2], ADDR[2]);
  not not_24 (not_22_out[3], ADDR[3]);
  RAM_BYTE _0110 (
    .CLK_IN(CLK), .MODE(READ_WRITE), .ADDR({not_25_out[3], ADDR[2:1], not_25_out[0]}),
    .DATA_OUT(_0110_data_out), .DATA_IN(undriven), .CONTENTS(out_11));
  not not_25 (not_25_out[0], ADDR[0]);
  not not_26 (not_25_out[3], ADDR[3]);
  RAM_BYTE _1010 (
    .CLK_IN(CLK), .MODE(READ_WRITE), .ADDR({ADDR[3], not_27_out[2], ADDR[1], not_27_out[0]}),
    .DATA_OUT(_1010_data_out), .DATA_IN(out_21), .CONTENTS(out_15));
  not not_27 (not_27_out[0], ADDR[0]);
  not not_28 (not_27_out[2], ADDR[2]);
  RAM_BYTE _1110 (
    .CLK_IN(CLK), .MODE(READ_WRITE), .ADDR({ADDR[3:1], not_29_out[0]}), .DATA_OUT(_1110_data_out),
    .DATA_IN(out_21), .CONTENTS(out_19));
  not not_29 (not_29_out[0], ADDR[0]);
  DATA_REGISTER data_register_1 (.DATA_OUT(out_21), .DATA_IN(or_1_out), .CLK_IN(CLK));  // open: MODE
  RAM_BYTE _0011 (
    .CLK_IN(CLK), .MODE(READ_WRITE), .ADDR({not_30_out, ADDR[1:0]}), .DATA_OUT(_0011_data_out),
    .DATA_IN(out_21), .CONTENTS(out_8));
  RAM_BYTE _0111 (
    .CLK_IN(CLK), .MODE(READ_WRITE), .ADDR({not_32_out[3], ADDR[2:0]}), .DATA_OUT(_0111_data_out),
    .DATA_IN(undriven), .CONTENTS(out_12));
  RAM_BYTE _1011 (
    .CLK_IN(CLK), .MODE(READ_WRITE), .ADDR({ADDR[3], not_33_out[2], ADDR[1:0]}), .DATA_OUT(_1011_data_out),
    .DATA_IN(out_21), .CONTENTS(out_16));
  RAM_BYTE _1111 (
    .CLK_IN(CLK), .MODE(READ_WRITE), .ADDR(ADDR), .DATA_OUT(_1111_data_out), .DATA_IN(out_21),
    .CONTENTS(out_20));
  not not_30 (not_30_out[2], ADDR[2]);
  not not_31 (not_30_out[3], ADDR[3]);
  not not_32 (not_32_out[3], ADDR[3]);
  not not_33 (not_33_out[2], ADDR[2]);
  assign DR_OUT = out_21 & ~{8{READ_WRITE}};  // AND_Gate and_2, 8 bits wide

  // Notes on the sheet:
  //   read = 0, write = 1
endmodule

module RAM_BYTE (
  input  CLK_IN,
  input  [3:0] ADDR,
  input  MODE,
  input  [7:0] DATA_IN,
  output [7:0] DATA_OUT,
  output [7:0] CONTENTS
);

  wire and_1_out, and_3_out, and_4_out, and_6_out, and_7_out, and_9_out, and_10_out, and_12_out, and_13_out,
       and_15_out, and_16_out, and_18_out, and_19_out, and_21_out, and_22_out, and_24_out;

  and and_1 (and_1_out, DATA_IN[7], ADDR[3], ADDR[2], ADDR[1], ADDR[0], MODE);
  and and_2 (DATA_OUT[7], CONTENTS[7], ADDR[3], ADDR[2], ADDR[1], ADDR[0], ~MODE);  // AND_Gate
  S_R_Flip_Flop s_r_ff_1 (.S(and_1_out), .R(and_3_out), .clk(CLK_IN), .Q(CONTENTS[7]));  // open: reset, Qn, preset
  and and_3 (and_3_out, ~DATA_IN[7], ADDR[3], ADDR[2], ADDR[1], ADDR[0], MODE);  // AND_Gate
  and and_4 (and_4_out, DATA_IN[6], ADDR[3], ADDR[2], ADDR[1], ADDR[0], MODE);
  and and_5 (DATA_OUT[6], CONTENTS[6], ADDR[3], ADDR[2], ADDR[1], ADDR[0], ~MODE);  // AND_Gate
  S_R_Flip_Flop s_r_ff_2 (.S(and_4_out), .R(and_6_out), .clk(CLK_IN), .Q(CONTENTS[6]));  // open: reset, Qn, preset
  and and_6 (and_6_out, ~DATA_IN[6], ADDR[3], ADDR[2], ADDR[1], ADDR[0], MODE);  // AND_Gate
  S_R_Flip_Flop s_r_ff_3 (.S(and_7_out), .R(and_9_out), .clk(CLK_IN), .Q(CONTENTS[5]));  // open: reset, Qn, preset
  and and_7 (and_7_out, DATA_IN[5], ADDR[3], ADDR[2], ADDR[1], ADDR[0], MODE);
  and and_8 (DATA_OUT[5], CONTENTS[5], ADDR[3], ADDR[2], ADDR[1], ADDR[0], ~MODE);  // AND_Gate
  and and_9 (and_9_out, ~DATA_IN[5], ADDR[3], ADDR[2], ADDR[1], ADDR[0], MODE);  // AND_Gate
  and and_10 (and_10_out, DATA_IN[4], ADDR[3], ADDR[2], ADDR[1], ADDR[0], MODE);
  S_R_Flip_Flop s_r_ff_4 (.S(and_10_out), .R(and_12_out), .clk(CLK_IN), .Q(CONTENTS[4]));  // open: reset, Qn, preset
  and and_11 (DATA_OUT[4], CONTENTS[4], ADDR[3], ADDR[2], ADDR[1], ADDR[0], ~MODE);  // AND_Gate
  and and_12 (and_12_out, ~DATA_IN[4], ADDR[3], ADDR[2], ADDR[1], ADDR[0], MODE);  // AND_Gate
  and and_13 (and_13_out, DATA_IN[3], ADDR[3], ADDR[2], ADDR[1], ADDR[0], MODE);
  and and_14 (DATA_OUT[3], CONTENTS[3], ADDR[3], ADDR[2], ADDR[1], ADDR[0], ~MODE);  // AND_Gate
  S_R_Flip_Flop s_r_ff_5 (.S(and_13_out), .R(and_15_out), .clk(CLK_IN), .Q(CONTENTS[3]));  // open: reset, Qn, preset
  and and_15 (and_15_out, ~DATA_IN[3], ADDR[3], ADDR[2], ADDR[1], ADDR[0], MODE);  // AND_Gate
  and and_16 (and_16_out, DATA_IN[2], ADDR[3], ADDR[2], ADDR[1], ADDR[0], MODE);
  and and_17 (DATA_OUT[2], CONTENTS[2], ADDR[3], ADDR[2], ADDR[1], ADDR[0], ~MODE);  // AND_Gate
  S_R_Flip_Flop s_r_ff_6 (.S(and_16_out), .R(and_18_out), .clk(CLK_IN), .Q(CONTENTS[2]));  // open: reset, Qn, preset
  and and_18 (and_18_out, ~DATA_IN[2], ADDR[3], ADDR[2], ADDR[1], ADDR[0], MODE);  // AND_Gate
  S_R_Flip_Flop s_r_ff_7 (.S(and_19_out), .R(and_21_out), .clk(CLK_IN), .Q(CONTENTS[1]));  // open: reset, Qn, preset
  and and_19 (and_19_out, DATA_IN[1], ADDR[3], ADDR[2], ADDR[1], ADDR[0], MODE);
  and and_20 (DATA_OUT[1], CONTENTS[1], ADDR[3], ADDR[2], ADDR[1], ADDR[0], ~MODE);  // AND_Gate
  and and_21 (and_21_out, ~DATA_IN[1], ADDR[3], ADDR[2], ADDR[1], ADDR[0], MODE);  // AND_Gate
  and and_22 (and_22_out, DATA_IN[0], ADDR[3], ADDR[2], ADDR[1], ADDR[0], MODE);
  S_R_Flip_Flop s_r_ff_8 (.S(and_22_out), .R(and_24_out), .clk(CLK_IN), .Q(CONTENTS[0]));  // open: reset, Qn, preset
  and and_23 (DATA_OUT[0], CONTENTS[0], ADDR[3], ADDR[2], ADDR[1], ADDR[0], ~MODE);  // AND_Gate
  and and_24 (and_24_out, ~DATA_IN[0], ADDR[3], ADDR[2], ADDR[1], ADDR[0], MODE);  // AND_Gate
endmodule

module DATA_REGISTER (
  input  CLK_IN,
  input  [7:0] DATA_IN,
  input  MODE,
  output [7:0] DATA_OUT
);

  wire and_1_out, and_2_out, and_3_out, and_4_out, and_5_out, and_6_out, and_7_out, and_8_out, and_9_out,
       and_10_out, and_11_out, and_12_out, and_13_out, and_14_out, and_15_out, and_16_out;

  and and_1 (and_1_out, ~MODE, DATA_IN[7]);  // AND_Gate
  S_R_Flip_Flop s_r_ff_1 (.S(and_1_out), .R(and_2_out), .clk(CLK_IN), .Q(DATA_OUT[7]));  // open: reset, Qn, preset
  and and_2 (and_2_out, ~MODE, ~DATA_IN[7]);  // AND_Gate
  S_R_Flip_Flop s_r_ff_2 (.S(and_4_out), .R(and_3_out), .clk(CLK_IN), .Q(DATA_OUT[6]));  // open: reset, Qn, preset
  and and_3 (and_3_out, ~MODE, ~DATA_IN[6]);  // AND_Gate
  and and_4 (and_4_out, ~MODE, DATA_IN[6]);  // AND_Gate
  S_R_Flip_Flop s_r_ff_3 (.S(and_5_out), .R(and_6_out), .clk(CLK_IN), .Q(DATA_OUT[5]));  // open: reset, Qn, preset
  and and_5 (and_5_out, ~MODE, DATA_IN[5]);  // AND_Gate
  and and_6 (and_6_out, ~MODE, ~DATA_IN[5]);  // AND_Gate
  and and_7 (and_7_out, ~MODE, DATA_IN[4]);  // AND_Gate
  S_R_Flip_Flop s_r_ff_4 (.S(and_7_out), .R(and_8_out), .clk(CLK_IN), .Q(DATA_OUT[4]));  // open: reset, Qn, preset
  and and_8 (and_8_out, ~MODE, ~DATA_IN[4]);  // AND_Gate
  and and_9 (and_9_out, ~MODE, DATA_IN[3]);  // AND_Gate
  S_R_Flip_Flop s_r_ff_5 (.S(and_9_out), .R(and_10_out), .clk(CLK_IN), .Q(DATA_OUT[3]));  // open: reset, Qn, preset
  and and_10 (and_10_out, ~MODE, ~DATA_IN[3]);  // AND_Gate
  S_R_Flip_Flop s_r_ff_6 (.S(and_11_out), .R(and_12_out), .clk(CLK_IN), .Q(DATA_OUT[2]));  // open: reset, Qn, preset
  and and_11 (and_11_out, ~MODE, DATA_IN[2]);  // AND_Gate
  and and_12 (and_12_out, ~MODE, ~DATA_IN[2]);  // AND_Gate
  S_R_Flip_Flop s_r_ff_7 (.S(and_14_out), .R(and_13_out), .clk(CLK_IN), .Q(DATA_OUT[1]));  // open: reset, Qn, preset
  and and_13 (and_13_out, ~MODE, ~DATA_IN[1]);  // AND_Gate
  and and_14 (and_14_out, ~MODE, DATA_IN[1]);  // AND_Gate
  and and_15 (and_15_out, ~MODE, DATA_IN[0]);  // AND_Gate
  S_R_Flip_Flop s_r_ff_8 (.S(and_15_out), .R(and_16_out), .clk(CLK_IN), .Q(DATA_OUT[0]));  // open: reset, Qn, preset
  and and_16 (and_16_out, ~MODE, ~DATA_IN[0]);  // AND_Gate
endmodule

module ALU (
  input  [7:0] L_In,
  input  [7:0] R_In,
  input  [1:0] Op,
  output [7:0] A_Out,
  output [2:0] Status
);

  wire and_1_out, and_2_out, full_adder_1_c_out, full_adder_2_c_out, full_adder_3_c_out, full_adder_4_c_out,
       full_adder_5_c_out, full_adder_6_c_out, half_adder_1_c_out;
  wire [7:0] twos_comp_1_out;

  and and_1 (and_1_out, twos_comp_1_out[7], ~A_Out[7], R_In[7]);  // AND_Gate
  // Probe on L_In
  Twos_Comp twos_comp_1 (.In(L_In), .Out(twos_comp_1_out), .ADD_SUB(Op[0]));
  and and_2 (and_2_out, ~twos_comp_1_out[7], A_Out[7], ~R_In[7]);  // AND_Gate
  or or_1 (Status[2], and_2_out, and_1_out);
  // Probe on R_In
  Half_Adder half_adder_1 (.A(R_In[0]), .B(twos_comp_1_out[0]), .R(A_Out[0]), .C_Out(half_adder_1_c_out));
  Full_Adder full_adder_1 (
    .A(twos_comp_1_out[1]), .B(R_In[1]), .C_In(half_adder_1_c_out), .R(A_Out[1]), .C_Out(full_adder_1_c_out));
  Full_Adder full_adder_2 (
    .A(twos_comp_1_out[2]), .B(R_In[2]), .C_In(full_adder_1_c_out), .R(A_Out[2]), .C_Out(full_adder_2_c_out));
  Full_Adder full_adder_3 (
    .A(twos_comp_1_out[3]), .B(R_In[3]), .C_In(full_adder_2_c_out), .R(A_Out[3]), .C_Out(full_adder_3_c_out));
  Full_Adder full_adder_4 (
    .A(twos_comp_1_out[4]), .B(R_In[4]), .C_In(full_adder_3_c_out), .R(A_Out[4]), .C_Out(full_adder_4_c_out));
  Full_Adder full_adder_5 (
    .A(twos_comp_1_out[5]), .B(R_In[5]), .C_In(full_adder_4_c_out), .R(A_Out[5]), .C_Out(full_adder_5_c_out));
  Full_Adder full_adder_6 (
    .A(twos_comp_1_out[6]), .B(R_In[6]), .C_In(full_adder_5_c_out), .R(A_Out[6]), .C_Out(full_adder_6_c_out));
  Full_Adder full_adder_7 (
    .A(twos_comp_1_out[7]), .B(R_In[7]), .C_In(full_adder_6_c_out), .R(A_Out[7]));  // open: C_Out
  and Zero (Status[0], ~A_Out[0], ~A_Out[1], ~A_Out[2], ~A_Out[3], ~A_Out[4], ~A_Out[5], ~A_Out[6], ~A_Out[7]);  // AND_Gate
  // Probe on A_Out

  assign Status[1] = A_Out[7];

  // Notes on the sheet:
  //   00 Sub
  //   01 Add
  //   001 zero result
  //   010 negative result
  //   100 overflow
endmodule

module Half_Adder (
  input  A,
  input  B,
  output R,
  output C_Out
);

  wire or_1_out;

  and and_1 (C_Out, A, B);
  or or_1 (or_1_out, A, B);
  and and_2 (R, ~C_Out, or_1_out);  // AND_Gate
endmodule

module Full_Adder (
  input  A,
  input  B,
  input  C_In,
  output R,
  output C_Out
);

  wire A_B_out, A_C_out, and_1_out, and_2_out, and_3_out, B_C_out, or_1_out;

  and A_B (A_B_out, A, B);
  and A_C (A_C_out, A, C_In);
  and B_C (B_C_out, B, C_In);
  and and_1 (and_1_out, A, B, C_In);
  or or_1 (or_1_out, A, B, C_In);
  and and_2 (and_2_out, ~A_B_out, ~A_C_out, ~B_C_out);  // AND_Gate
  and and_3 (and_3_out, or_1_out, and_2_out);
  or or_2 (C_Out, A_B_out, A_C_out, B_C_out);
  or or_3 (R, and_1_out, and_3_out);
endmodule

module Twos_Comp (
  input  ADD_SUB,
  input  [7:0] In,
  output [7:0] Out
);

  wire and_1_out, and_2_out, and_3_out, and_4_out, and_5_out, and_6_out, and_7_out, and_8_out, and_9_out,
       and_10_out, and_11_out, and_12_out, and_13_out, and_14_out, and_15_out, and_16_out,
       half_adder_1_c_out, half_adder_2_c_out, half_adder_3_c_out, half_adder_4_c_out, half_adder_5_c_out,
       half_adder_6_c_out, half_adder_7_c_out, not_1_out, or_1_out, or_2_out, or_3_out, or_4_out, or_5_out,
       or_6_out, or_7_out, or_8_out;

  // Probe on In
  and and_1 (and_1_out, ~In[0], ~ADD_SUB);  // AND_Gate
  and and_2 (and_2_out, In[0], ADD_SUB);
  and and_3 (and_3_out, ~In[1], ~ADD_SUB);  // AND_Gate
  and and_4 (and_4_out, In[1], ADD_SUB);
  and and_5 (and_5_out, ~In[2], ~ADD_SUB);  // AND_Gate
  and and_6 (and_6_out, In[2], ADD_SUB);
  and and_7 (and_7_out, ~In[3], ~ADD_SUB);  // AND_Gate
  and and_8 (and_8_out, In[3], ADD_SUB);
  and and_9 (and_9_out, ~In[4], ~ADD_SUB);  // AND_Gate
  and and_10 (and_10_out, In[4], ADD_SUB);
  and and_11 (and_11_out, ~In[5], ~ADD_SUB);  // AND_Gate
  and and_12 (and_12_out, In[5], ADD_SUB);
  and and_13 (and_13_out, ~In[6], ~ADD_SUB);  // AND_Gate
  and and_14 (and_14_out, In[6], ADD_SUB);
  and and_15 (and_15_out, ~In[7], ~ADD_SUB);  // AND_Gate
  and and_16 (and_16_out, In[7], ADD_SUB);
  or or_1 (or_1_out, and_1_out, and_2_out);
  or or_2 (or_2_out, and_3_out, and_4_out);
  or or_3 (or_3_out, and_5_out, and_6_out);
  or or_4 (or_4_out, and_7_out, and_8_out);
  or or_5 (or_5_out, and_9_out, and_10_out);
  or or_6 (or_6_out, and_11_out, and_12_out);
  or or_7 (or_7_out, and_13_out, and_14_out);
  or or_8 (or_8_out, and_15_out, and_16_out);
  Half_Adder half_adder_1 (.A(or_1_out), .B(not_1_out), .R(Out[0]), .C_Out(half_adder_1_c_out));
  not not_1 (not_1_out, ADD_SUB);
  Half_Adder half_adder_2 (.A(or_2_out), .B(half_adder_1_c_out), .R(Out[1]), .C_Out(half_adder_2_c_out));
  Half_Adder half_adder_3 (.A(or_3_out), .B(half_adder_2_c_out), .R(Out[2]), .C_Out(half_adder_3_c_out));
  Half_Adder half_adder_4 (.A(or_4_out), .B(half_adder_3_c_out), .R(Out[3]), .C_Out(half_adder_4_c_out));
  Half_Adder half_adder_5 (.A(or_5_out), .B(half_adder_4_c_out), .R(Out[4]), .C_Out(half_adder_5_c_out));
  Half_Adder half_adder_6 (.A(or_6_out), .B(half_adder_5_c_out), .R(Out[5]), .C_Out(half_adder_6_c_out));
  Half_Adder half_adder_7 (.A(or_7_out), .B(half_adder_6_c_out), .R(Out[6]), .C_Out(half_adder_7_c_out));
  Half_Adder half_adder_8 (.A(or_8_out), .B(half_adder_7_c_out), .R(Out[7]));  // open: C_Out
  // Probe on Out

  // Notes on the sheet:
  //   0 for sub, 1 for add
endmodule

module DISPLAY (
  input  [3:0] in_1,
  input  [3:0] in_2,
  input  [3:0] in_3
);

  wire [6:0] encode_display_1_out_2, encode_display_2_out_2, encode_display_3_out_2;

  ENCODE_DISPLAY encode_display_1 (.out_2(encode_display_1_out_2), .in_1(in_1));
  _7_Segment_Display u_7_segment_display_1 (
    .g(encode_display_1_out_2[0]), .f(encode_display_1_out_2[1]), .a(encode_display_1_out_2[2]),
    .b(encode_display_1_out_2[3]), .e(encode_display_1_out_2[4]), .d(encode_display_1_out_2[5]),
    .c(encode_display_1_out_2[6]));  // open: dp
  ENCODE_DISPLAY encode_display_2 (.out_2(encode_display_2_out_2), .in_1(in_2));
  _7_Segment_Display u_7_segment_display_2 (
    .g(encode_display_2_out_2[0]), .f(encode_display_2_out_2[1]), .a(encode_display_2_out_2[2]),
    .b(encode_display_2_out_2[3]), .e(encode_display_2_out_2[4]), .d(encode_display_2_out_2[5]),
    .c(encode_display_2_out_2[6]));  // open: dp
  _7_Segment_Display u_7_segment_display_3 (
    .g(encode_display_3_out_2[0]), .f(encode_display_3_out_2[1]), .a(encode_display_3_out_2[2]),
    .b(encode_display_3_out_2[3]), .e(encode_display_3_out_2[4]), .d(encode_display_3_out_2[5]),
    .c(encode_display_3_out_2[6]));  // open: dp
  ENCODE_DISPLAY encode_display_3 (.out_2(encode_display_3_out_2), .in_1(in_3));
endmodule

module ENCODE_DISPLAY (
  input  [3:0] in_1,
  output [6:0] out_2
);

  wire I0_out, I1_out, I2_out, I3_out, I4_out, I5_out, I6_out, I7_out, I8_out, I9_out;

  or O6 (out_2[6], I9_out, I8_out, I7_out, I6_out, I5_out, I4_out, I3_out, I1_out, I0_out);
  and I9 (I9_out, in_1[3], ~in_1[2], ~in_1[1], in_1[0]);  // AND_Gate
  or O5 (out_2[5], I8_out, I6_out, I5_out, I3_out, I2_out, I0_out);
  and I8 (I8_out, in_1[3], ~in_1[2], ~in_1[1], ~in_1[0]);  // AND_Gate
  and I7 (I7_out, ~in_1[3], in_1[2], in_1[1], in_1[0]);  // AND_Gate
  or O4 (out_2[4], I8_out, I6_out, I2_out, I0_out);
  and I6 (I6_out, ~in_1[3], in_1[2], in_1[1], ~in_1[0]);  // AND_Gate
  or O3 (out_2[3], I9_out, I8_out, I7_out, I4_out, I3_out, I2_out, I1_out, I0_out);
  and I5 (I5_out, ~in_1[3], in_1[2], ~in_1[1], in_1[0]);  // AND_Gate
  and I4 (I4_out, ~in_1[3], in_1[2], ~in_1[1], ~in_1[0]);  // AND_Gate
  and I3 (I3_out, ~in_1[3], ~in_1[2], in_1[1], in_1[0]);  // AND_Gate
  or O2 (out_2[2], I9_out, I8_out, I7_out, I6_out, I5_out, I3_out, I2_out, I0_out);
  and I2 (I2_out, ~in_1[3], ~in_1[2], in_1[1], ~in_1[0]);  // AND_Gate
  or O1 (out_2[1], I9_out, I8_out, I6_out, I5_out, I4_out, I0_out);
  and I1 (I1_out, ~in_1[3], ~in_1[2], ~in_1[1], in_1[0]);  // AND_Gate
  and I0 (I0_out, ~in_1[3], ~in_1[2], ~in_1[1], ~in_1[0]);  // AND_Gate
  or O0 (out_2[0], I9_out, I8_out, I6_out, I5_out, I4_out, I3_out, I2_out);
endmodule

module GEN_REGISTER (
  input  CLK_IN,
  input  IN_OR_OUT,
  input  [7:0] DATA_IN,
  input  ADDR,
  output [7:0] DATA_OUT,
  output [7:0] CONTENTS
);

  wire and_1_out, and_2_out, and_3_out, and_4_out, and_5_out, and_6_out, and_7_out, and_8_out, and_10_out,
       and_11_out, and_12_out, and_13_out, and_14_out, and_15_out, and_16_out, and_17_out;

  and and_1 (and_1_out, DATA_IN[7], ~IN_OR_OUT, ADDR);  // AND_Gate
  S_R_Flip_Flop s_r_ff_1 (.S(and_1_out), .R(and_2_out), .clk(CLK_IN), .Q(CONTENTS[7]));  // open: reset, Qn, preset
  and and_2 (and_2_out, ~DATA_IN[7], ~IN_OR_OUT, ADDR);  // AND_Gate
  and and_3 (and_3_out, DATA_IN[6], ~IN_OR_OUT, ADDR);  // AND_Gate
  and and_4 (and_4_out, ~DATA_IN[6], ~IN_OR_OUT, ADDR);  // AND_Gate
  S_R_Flip_Flop s_r_ff_2 (.S(and_3_out), .R(and_4_out), .clk(CLK_IN), .Q(CONTENTS[6]));  // open: reset, Qn, preset
  and and_5 (and_5_out, DATA_IN[5], ~IN_OR_OUT, ADDR);  // AND_Gate
  S_R_Flip_Flop s_r_ff_3 (.S(and_5_out), .R(and_6_out), .clk(CLK_IN), .Q(CONTENTS[5]));  // open: reset, Qn, preset
  and and_6 (and_6_out, ~DATA_IN[5], ~IN_OR_OUT, ADDR);  // AND_Gate
  and and_7 (and_7_out, DATA_IN[4], ~IN_OR_OUT, ADDR);  // AND_Gate
  and and_8 (and_8_out, ~DATA_IN[4], ~IN_OR_OUT, ADDR);  // AND_Gate
  S_R_Flip_Flop s_r_ff_4 (.S(and_7_out), .R(and_8_out), .clk(CLK_IN), .Q(CONTENTS[4]));  // open: reset, Qn, preset
  assign DATA_OUT = {8{IN_OR_OUT}} & CONTENTS;  // AND_Gate and_9, 8 bits wide
  and and_10 (and_10_out, DATA_IN[3], ~IN_OR_OUT, ADDR);  // AND_Gate
  S_R_Flip_Flop s_r_ff_5 (.S(and_10_out), .R(and_11_out), .clk(CLK_IN), .Q(CONTENTS[3]));  // open: reset, Qn, preset
  and and_11 (and_11_out, ~DATA_IN[3], ~IN_OR_OUT, ADDR);  // AND_Gate
  and and_12 (and_12_out, DATA_IN[2], ~IN_OR_OUT, ADDR);  // AND_Gate
  S_R_Flip_Flop s_r_ff_6 (.S(and_12_out), .R(and_13_out), .clk(CLK_IN), .Q(CONTENTS[2]));  // open: reset, Qn, preset
  and and_13 (and_13_out, ~DATA_IN[2], ~IN_OR_OUT, ADDR);  // AND_Gate
  and and_14 (and_14_out, DATA_IN[1], ~IN_OR_OUT, ADDR);  // AND_Gate
  S_R_Flip_Flop s_r_ff_7 (.S(and_14_out), .R(and_15_out), .clk(CLK_IN), .Q(CONTENTS[1]));  // open: reset, Qn, preset
  and and_15 (and_15_out, ~DATA_IN[1], ~IN_OR_OUT, ADDR);  // AND_Gate
  and and_16 (and_16_out, DATA_IN[0], ~IN_OR_OUT, ADDR);  // AND_Gate
  S_R_Flip_Flop s_r_ff_8 (.S(and_16_out), .R(and_17_out), .clk(CLK_IN), .Q(CONTENTS[0]));  // open: reset, Qn, preset
  and and_17 (and_17_out, ~DATA_IN[0], ~IN_OR_OUT, ADDR);  // AND_Gate
endmodule

module KeyPad (
  input  Zero,
  input  One,
  input  Two,
  input  Three,
  input  Four,
  input  Five,
  input  Six,
  input  Seven,
  input  Eight,
  input  Nine,
  output [7:0] Output
);

  wire Active_out, and_1_out, nand_1_out, not_1_out, not_2_out, not_3_out, not_4_out, or_1_out, or_2_out,
       or_3_out, or_4_out, s_r_ff_2_q, s_r_ff_3_q, undriven, undriven_2, xnor_1_out;

  NotExactlyOne xnor_1 (
    .out(xnor_1_out), .in0(Zero), .in1(One), .in2(Two), .in3(Three), .in4(Four), .in5(Five), .in6(Six),
    .in7(Seven), .in8(Eight), .in9(Nine));
  nand nand_1 (nand_1_out, xnor_1_out, Active_out);
  or Active (Active_out, Nine, Eight, Seven, Six, Five, Four, Three, Two, One, Zero);
  buf and_1 (and_1_out, Active_out);  // AND_Gate
  or or_1 (or_1_out, One, Three, Five, Seven, Nine);
  not not_1 (not_1_out, or_1_out);
  and and_2 (Output[0], undriven, nand_1_out);
  and and_3 (Output[1], s_r_ff_2_q, nand_1_out);
  and and_4 (Output[2], s_r_ff_3_q, nand_1_out);
  and and_5 (Output[3], undriven_2, nand_1_out);
  S_R_Flip_Flop s_r_ff_1 (
    .S(or_1_out), .clk(or_1_out), .R(not_1_out), .preset(not_1_out), .reset(not_1_out));  // open: Q, Qn
  S_R_Flip_Flop s_r_ff_2 (.S(or_2_out), .R(not_2_out), .clk(and_1_out), .Q(s_r_ff_2_q));  // open: reset, Qn, preset
  or or_2 (or_2_out, Two, Three, Six, Seven);
  not not_2 (not_2_out, or_2_out);
  or or_3 (or_3_out, Four, Five, Six, Seven);
  not not_3 (not_3_out, or_3_out);
  S_R_Flip_Flop s_r_ff_3 (.S(or_3_out), .R(not_3_out), .clk(and_1_out), .Q(s_r_ff_3_q));  // open: reset, Qn, preset
  or or_4 (or_4_out, Eight, Nine);
  S_R_Flip_Flop s_r_ff_4 (
    .S(or_4_out), .clk(or_4_out), .R(not_4_out), .preset(not_4_out), .reset(not_4_out));  // open: Q, Qn
  not not_4 (not_4_out, or_4_out);

  assign Output[7:4] = 4'b0000;
endmodule

module MAR_Old (
  input  [3:0] InAdr,
  input  InOn,
  input  OutOn,
  input  Clock,
  output [3:0] OutAdr,
  output [3:0] Contents
);

  wire and_1_out, not_1_out, not_2_out, not_3_out, not_4_out;

  and and_1 (and_1_out, InOn, Clock);
  S_R_Flip_Flop s_r_ff_1 (.S(InAdr[0]), .R(not_1_out), .clk(and_1_out), .Q(Contents[0]));  // open: reset, Qn, preset
  not not_1 (not_1_out, InAdr[0]);
  S_R_Flip_Flop s_r_ff_2 (.S(InAdr[1]), .R(not_2_out), .clk(and_1_out), .Q(Contents[1]));  // open: reset, Qn, preset
  not not_2 (not_2_out, InAdr[1]);
  S_R_Flip_Flop s_r_ff_3 (.S(InAdr[2]), .R(not_3_out), .clk(and_1_out), .Q(Contents[2]));  // open: reset, Qn, preset
  not not_3 (not_3_out, InAdr[2]);
  S_R_Flip_Flop s_r_ff_4 (.S(InAdr[3]), .R(not_4_out), .clk(and_1_out), .Q(Contents[3]));  // open: reset, Qn, preset
  not not_4 (not_4_out, InAdr[3]);
  and and_2 (OutAdr[0], Contents[0], OutOn);
  and and_3 (OutAdr[1], Contents[1], OutOn);
  and and_4 (OutAdr[2], Contents[2], OutOn);
  and and_5 (OutAdr[3], Contents[3], OutOn);
endmodule

module MBR_Old (
  input  [1:0] InMode,
  input  [7:0] In_00,
  input  [7:0] In_11,
  input  [7:0] In_10,
  input  InOn,
  input  OutOn,
  input  Clock,
  output [7:0] Out_00,
  output [7:0] Out_11,
  output [7:0] Contents,
  output [7:0] Out_10
);

  wire and_1_out, and_2_out, and_3_out, and_4_out, and_5_out, and_6_out, and_7_out, and_8_out, and_9_out,
       and_10_out, and_11_out, and_12_out, and_13_out, and_14_out, and_15_out, and_16_out, and_17_out,
       and_18_out, and_19_out, and_20_out, and_21_out, and_22_out, and_23_out, and_24_out, and_25_out,
       and_26_out, and_27_out, and_28_out, not_1_out, not_2_out, not_3_out, not_4_out, not_5_out, not_6_out,
       not_7_out, not_8_out, or_1_out, or_2_out, or_3_out, or_4_out, or_5_out, or_6_out, or_7_out, or_8_out;

  and and_1 (and_1_out, ~InMode[0], InMode[1]);  // AND_Gate
  and and_2 (and_2_out, InOn, Clock);
  and and_3 (and_3_out, ~InMode[0], ~InMode[1]);  // AND_Gate
  and and_4 (and_4_out, InMode[0], InMode[1]);
  and and_5 (and_5_out, In_00[0], and_3_out);
  and and_6 (and_6_out, In_00[1], and_3_out);
  and and_7 (and_7_out, In_00[2], and_3_out);
  and and_8 (and_8_out, In_00[3], and_3_out);
  and and_9 (and_9_out, In_00[4], and_3_out);
  and and_10 (and_10_out, In_00[5], and_3_out);
  and and_11 (and_11_out, In_00[6], and_3_out);
  and and_12 (and_12_out, In_00[7], and_3_out);
  and and_13 (and_13_out, In_11[0], and_4_out);
  and and_14 (and_14_out, In_11[1], and_4_out);
  and and_15 (and_15_out, In_11[2], and_4_out);
  and and_16 (and_16_out, In_11[3], and_4_out);
  and and_17 (and_17_out, In_11[4], and_4_out);
  and and_18 (and_18_out, In_11[5], and_4_out);
  and and_19 (and_19_out, In_11[6], and_4_out);
  and and_20 (and_20_out, In_11[7], and_4_out);
  and and_21 (and_21_out, In_10[0], and_1_out);
  and and_22 (and_22_out, In_10[1], and_1_out);
  and and_23 (and_23_out, In_10[2], and_1_out);
  and and_24 (and_24_out, In_10[3], and_1_out);
  and and_25 (and_25_out, In_10[4], and_1_out);
  and and_26 (and_26_out, In_10[5], and_1_out);
  and and_27 (and_27_out, In_10[6], and_1_out);
  and and_28 (and_28_out, In_10[7], and_1_out);
  or or_1 (or_1_out, and_5_out, and_21_out, and_13_out);
  not not_1 (not_1_out, or_1_out);
  S_R_Flip_Flop s_r_ff_1 (.S(or_1_out), .R(not_1_out), .clk(and_2_out), .Q(Contents[0]));  // open: reset, Qn, preset
  S_R_Flip_Flop s_r_ff_2 (.S(or_2_out), .R(not_2_out), .clk(and_2_out), .Q(Contents[1]));  // open: reset, Qn, preset
  or or_2 (or_2_out, and_6_out, and_22_out, and_14_out);
  not not_2 (not_2_out, or_2_out);
  or or_3 (or_3_out, and_7_out, and_23_out, and_15_out);
  S_R_Flip_Flop s_r_ff_3 (.S(or_3_out), .R(not_3_out), .clk(and_2_out), .Q(Contents[2]));  // open: reset, Qn, preset
  not not_3 (not_3_out, or_3_out);
  S_R_Flip_Flop s_r_ff_4 (.S(or_4_out), .R(not_4_out), .clk(and_2_out), .Q(Contents[3]));  // open: reset, Qn, preset
  or or_4 (or_4_out, and_8_out, and_24_out, and_16_out);
  not not_4 (not_4_out, or_4_out);
  or or_5 (or_5_out, and_9_out, and_25_out, and_17_out);
  S_R_Flip_Flop s_r_ff_5 (.S(or_5_out), .R(not_5_out), .clk(and_2_out), .Q(Contents[4]));  // open: reset, Qn, preset
  not not_5 (not_5_out, or_5_out);
  S_R_Flip_Flop s_r_ff_6 (.S(or_6_out), .R(not_6_out), .clk(and_2_out), .Q(Contents[5]));  // open: reset, Qn, preset
  or or_6 (or_6_out, and_10_out, and_26_out, and_18_out);
  not not_6 (not_6_out, or_6_out);
  or or_7 (or_7_out, and_11_out, and_27_out, and_19_out);
  S_R_Flip_Flop s_r_ff_7 (.S(or_7_out), .R(not_7_out), .clk(and_2_out), .Q(Contents[6]));  // open: reset, Qn, preset
  not not_7 (not_7_out, or_7_out);
  S_R_Flip_Flop s_r_ff_8 (.S(or_8_out), .R(not_8_out), .clk(and_2_out), .Q(Contents[7]));  // open: reset, Qn, preset
  or or_8 (or_8_out, and_12_out, and_28_out, and_20_out);
  not not_8 (not_8_out, or_8_out);
  and and_29 (Out_00[0], Contents[0], OutOn, and_3_out);
  and and_30 (Out_00[1], Contents[1], OutOn, and_3_out);
  and and_31 (Out_00[2], Contents[2], OutOn, and_3_out);
  and and_32 (Out_00[3], Contents[3], OutOn, and_3_out);
  and and_33 (Out_00[4], Contents[4], OutOn, and_3_out);
  and and_34 (Out_00[5], Contents[5], OutOn, and_3_out);
  and and_35 (Out_00[6], Contents[6], OutOn, and_3_out);
  and and_36 (Out_00[7], Contents[7], OutOn, and_3_out);
  and and_37 (Out_11[0], Contents[0], OutOn, and_4_out);
  and and_38 (Out_11[1], Contents[1], OutOn, and_4_out);
  and and_39 (Out_11[2], Contents[2], OutOn, and_4_out);
  and and_40 (Out_11[3], Contents[3], OutOn, and_4_out);
  and and_41 (Out_11[4], Contents[4], OutOn, and_4_out);
  and and_42 (Out_11[5], Contents[5], OutOn, and_4_out);
  and and_43 (Out_11[6], Contents[6], OutOn, and_4_out);
  and and_44 (Out_11[7], Contents[7], OutOn, and_4_out);
  and and_45 (Out_10[0], Contents[0], OutOn, and_1_out);
  and and_46 (Out_10[1], Contents[1], OutOn, and_1_out);
  and and_47 (Out_10[2], Contents[2], OutOn, and_1_out);
  and and_48 (Out_10[3], Contents[3], OutOn, and_1_out);
  and and_49 (Out_10[4], Contents[4], OutOn, and_1_out);
  and and_50 (Out_10[5], Contents[5], OutOn, and_1_out);
  and and_51 (Out_10[6], Contents[6], OutOn, and_1_out);
  and and_52 (Out_10[7], Contents[7], OutOn, and_1_out);
endmodule

module DATA_BYTE (
  input  [7:0] Byte_In,
  input  CLK,
  input  NO_IN,
  output [7:0] Byte_Out
);

  wire and_1_out, and_2_out, and_3_out, and_4_out, and_5_out, and_6_out, and_7_out, and_8_out, and_9_out,
       and_10_out, and_11_out, and_12_out, and_13_out, and_14_out, and_15_out, and_16_out;

  and and_1 (and_1_out, ~NO_IN, Byte_In[0]);  // AND_Gate
  S_R_Flip_Flop s_r_ff_1 (.S(and_1_out), .R(and_2_out), .clk(CLK), .Q(Byte_Out[0]));  // open: reset, Qn, preset
  and and_2 (and_2_out, ~NO_IN, ~Byte_In[0]);  // AND_Gate
  and and_3 (and_3_out, ~NO_IN, Byte_In[1]);  // AND_Gate
  S_R_Flip_Flop s_r_ff_2 (.S(and_3_out), .R(and_4_out), .clk(CLK), .Q(Byte_Out[1]));  // open: reset, Qn, preset
  and and_4 (and_4_out, ~NO_IN, ~Byte_In[1]);  // AND_Gate
  S_R_Flip_Flop s_r_ff_3 (.S(and_5_out), .R(and_6_out), .clk(CLK), .Q(Byte_Out[2]));  // open: reset, Qn, preset
  and and_5 (and_5_out, ~NO_IN, Byte_In[2]);  // AND_Gate
  and and_6 (and_6_out, ~NO_IN, ~Byte_In[2]);  // AND_Gate
  S_R_Flip_Flop s_r_ff_4 (.S(and_7_out), .R(and_8_out), .clk(CLK), .Q(Byte_Out[3]));  // open: reset, Qn, preset
  and and_7 (and_7_out, ~NO_IN, Byte_In[3]);  // AND_Gate
  and and_8 (and_8_out, ~NO_IN, ~Byte_In[3]);  // AND_Gate
  S_R_Flip_Flop s_r_ff_5 (.S(and_9_out), .R(and_10_out), .clk(CLK), .Q(Byte_Out[4]));  // open: reset, Qn, preset
  and and_9 (and_9_out, ~NO_IN, Byte_In[4]);  // AND_Gate
  and and_10 (and_10_out, ~NO_IN, ~Byte_In[4]);  // AND_Gate
  S_R_Flip_Flop s_r_ff_6 (.S(and_11_out), .R(and_12_out), .clk(CLK), .Q(Byte_Out[5]));  // open: reset, Qn, preset
  and and_11 (and_11_out, ~NO_IN, Byte_In[5]);  // AND_Gate
  and and_12 (and_12_out, ~NO_IN, ~Byte_In[5]);  // AND_Gate
  and and_13 (and_13_out, ~NO_IN, Byte_In[6]);  // AND_Gate
  S_R_Flip_Flop s_r_ff_7 (.S(and_13_out), .R(and_14_out), .clk(CLK), .Q(Byte_Out[6]));  // open: reset, Qn, preset
  and and_14 (and_14_out, ~NO_IN, ~Byte_In[6]);  // AND_Gate
  and and_15 (and_15_out, ~NO_IN, Byte_In[7]);  // AND_Gate
  S_R_Flip_Flop s_r_ff_8 (.S(and_15_out), .R(and_16_out), .clk(CLK), .Q(Byte_Out[7]));  // open: reset, Qn, preset
  and and_16 (and_16_out, ~NO_IN, ~Byte_In[7]);  // AND_Gate
endmodule

module AR (
  input  CLK_IN,
  input  IN_OR_OUT,
  input  [3:0] ADR_IN,
  output [3:0] ADR_OUT
);

  wire and_1_out, and_2_out, and_3_out, and_4_out, and_6_out, and_7_out, and_8_out, and_9_out;
  wire [3:0] s_r_ff_4_q;

  S_R_Flip_Flop s_r_ff_1 (.S(and_2_out), .R(and_1_out), .clk(CLK_IN), .Q(s_r_ff_4_q[3]));  // open: reset, Qn, preset
  and and_1 (and_1_out, ~IN_OR_OUT, ~ADR_IN[3]);  // AND_Gate
  and and_2 (and_2_out, ~IN_OR_OUT, ADR_IN[3]);  // AND_Gate
  S_R_Flip_Flop s_r_ff_2 (.S(and_3_out), .R(and_4_out), .clk(CLK_IN), .Q(s_r_ff_4_q[2]));  // open: reset, Qn, preset
  and and_3 (and_3_out, ~IN_OR_OUT, ADR_IN[2]);  // AND_Gate
  and and_4 (and_4_out, ~IN_OR_OUT, ~ADR_IN[2]);  // AND_Gate
  assign ADR_OUT = {4{IN_OR_OUT}} & s_r_ff_4_q;  // AND_Gate and_5, 4 bits wide
  and and_6 (and_6_out, ~IN_OR_OUT, ADR_IN[1]);  // AND_Gate
  S_R_Flip_Flop s_r_ff_3 (.S(and_6_out), .R(and_7_out), .clk(CLK_IN), .Q(s_r_ff_4_q[1]));  // open: reset, Qn, preset
  and and_7 (and_7_out, ~IN_OR_OUT, ~ADR_IN[1]);  // AND_Gate
  and and_8 (and_8_out, ~IN_OR_OUT, ADR_IN[0]);  // AND_Gate
  S_R_Flip_Flop s_r_ff_4 (.S(and_8_out), .R(and_9_out), .clk(CLK_IN), .Q(s_r_ff_4_q[0]));  // open: reset, Qn, preset
  and and_9 (and_9_out, ~IN_OR_OUT, ~ADR_IN[0]);  // AND_Gate

  // Notes on the sheet:
  //   in (receiving data) : 0
  //   out (outputting data) : 1
endmodule

module PC (
  input  IN_MODE,
  input  NO_IN,
  input  CLK,
  input  [3:0] IN_1,
  input  [3:0] IN_0,
  output [3:0] OUT_0
);

  wire and_3_out, and_4_out, and_5_out, and_6_out, and_7_out, and_8_out, and_9_out, and_10_out;
  wire [3:0] and_1_out, and_2_out, or_1_out;

  assign and_1_out = {4{IN_MODE}} & IN_1;  // AND_Gate and_1, 4 bits wide
  assign or_1_out = and_1_out | and_2_out;  // OR_Gate or_1, 4 bits wide
  assign and_2_out = ~{4{IN_MODE}} & IN_0;  // AND_Gate and_2, 4 bits wide
  and and_3 (and_3_out, ~NO_IN, or_1_out[0]);  // AND_Gate
  and and_4 (and_4_out, ~or_1_out[0], ~NO_IN);  // AND_Gate
  and and_5 (and_5_out, ~NO_IN, or_1_out[1]);  // AND_Gate
  and and_6 (and_6_out, ~NO_IN, ~or_1_out[1]);  // AND_Gate
  and and_7 (and_7_out, ~NO_IN, or_1_out[2]);  // AND_Gate
  and and_8 (and_8_out, ~NO_IN, ~or_1_out[2]);  // AND_Gate
  and and_9 (and_9_out, ~NO_IN, or_1_out[3]);  // AND_Gate
  and and_10 (and_10_out, ~NO_IN, ~or_1_out[3]);  // AND_Gate
  S_R_Flip_Flop s_r_ff_1 (.S(and_3_out), .R(and_4_out), .clk(CLK), .Q(OUT_0[0]));  // open: reset, Qn, preset
  S_R_Flip_Flop s_r_ff_2 (.S(and_5_out), .R(and_6_out), .clk(CLK), .Q(OUT_0[1]));  // open: reset, Qn, preset
  S_R_Flip_Flop s_r_ff_3 (.S(and_7_out), .R(and_8_out), .clk(CLK), .Q(OUT_0[2]));  // open: reset, Qn, preset
  S_R_Flip_Flop s_r_ff_4 (.S(and_9_out), .R(and_10_out), .clk(CLK), .Q(OUT_0[3]));  // open: reset, Qn, preset

  // Notes on the sheet:
  //   Input from INC
  //   Input from IR
endmodule

module INC (
  input  ON_0,
  input  [3:0] IN_0,
  output [3:0] OUT_0
);

  wire half_adder_1_c_out, half_adder_2_c_out, half_adder_3_c_out;

  Half_Adder half_adder_1 (.A(IN_0[0]), .B(ON_0), .R(OUT_0[0]), .C_Out(half_adder_1_c_out));
  Half_Adder half_adder_2 (.A(IN_0[1]), .B(half_adder_1_c_out), .R(OUT_0[1]), .C_Out(half_adder_2_c_out));
  Half_Adder half_adder_3 (.A(IN_0[2]), .B(half_adder_2_c_out), .R(OUT_0[2]), .C_Out(half_adder_3_c_out));
  Half_Adder half_adder_4 (.A(IN_0[3]), .B(half_adder_3_c_out), .R(OUT_0[3]));  // open: C_Out
endmodule

module STATUS (
  input  [2:0] in_1,
  input  CLK,
  output [2:0] out_3
);

  D_Flip_Flop d_ff_1 (.D(in_1[0]), .clk(CLK), .Q(out_3[0]));  // open: Qn, preset, reset
  D_Flip_Flop d_ff_2 (.D(in_1[1]), .clk(CLK), .Q(out_3[1]));  // open: Qn, preset, reset
  D_Flip_Flop d_ff_3 (.D(in_1[2]), .clk(CLK), .Q(out_3[2]));  // open: Qn, preset, reset
endmodule

module MBR (
  input  [7:0] IN_0,
  input  IN_MODE,
  input  CLK,
  output [7:0] Contents,
  output [7:0] OUT_0
);

  wire and_1_out, and_2_out, and_3_out, and_4_out, and_5_out, and_6_out, and_7_out, and_8_out, and_9_out,
       and_10_out, and_11_out, and_12_out, and_14_out, and_15_out, and_16_out, and_17_out;

  and and_1 (and_1_out, IN_0[0], ~IN_MODE);  // AND_Gate
  and and_2 (and_2_out, ~IN_0[0], ~IN_MODE);  // AND_Gate
  S_R_Flip_Flop s_r_ff_1 (.S(and_1_out), .R(and_2_out), .clk(CLK), .Q(Contents[0]));  // open: reset, Qn, preset
  and and_3 (and_3_out, IN_0[1], ~IN_MODE);  // AND_Gate
  and and_4 (and_4_out, ~IN_0[1], ~IN_MODE);  // AND_Gate
  S_R_Flip_Flop s_r_ff_2 (.S(and_3_out), .R(and_4_out), .clk(CLK), .Q(Contents[1]));  // open: reset, Qn, preset
  and and_5 (and_5_out, IN_0[2], ~IN_MODE);  // AND_Gate
  and and_6 (and_6_out, ~IN_0[2], ~IN_MODE);  // AND_Gate
  S_R_Flip_Flop s_r_ff_3 (.S(and_5_out), .R(and_6_out), .clk(CLK), .Q(Contents[2]));  // open: reset, Qn, preset
  and and_7 (and_7_out, IN_0[3], ~IN_MODE);  // AND_Gate
  and and_8 (and_8_out, ~IN_0[3], ~IN_MODE);  // AND_Gate
  S_R_Flip_Flop s_r_ff_4 (.S(and_7_out), .R(and_8_out), .Q(Contents[3]));  // open: clk, reset, Qn, preset
  S_R_Flip_Flop s_r_ff_5 (.S(and_9_out), .R(and_10_out), .clk(CLK), .Q(Contents[4]));  // open: reset, Qn, preset
  and and_9 (and_9_out, IN_0[4], ~IN_MODE);  // AND_Gate
  and and_10 (and_10_out, ~IN_0[4], ~IN_MODE);  // AND_Gate
  and and_11 (and_11_out, IN_0[5], ~IN_MODE);  // AND_Gate
  S_R_Flip_Flop s_r_ff_6 (.S(and_11_out), .R(and_12_out), .clk(CLK), .Q(Contents[5]));  // open: reset, Qn, preset
  and and_12 (and_12_out, ~IN_0[5], ~IN_MODE);  // AND_Gate
  assign OUT_0 = {8{IN_MODE}} & Contents;  // AND_Gate and_13, 8 bits wide
  and and_14 (and_14_out, IN_0[6], ~IN_MODE);  // AND_Gate
  S_R_Flip_Flop s_r_ff_7 (.S(and_14_out), .R(and_15_out), .clk(CLK), .Q(Contents[6]));  // open: reset, Qn, preset
  and and_15 (and_15_out, ~IN_0[6], ~IN_MODE);  // AND_Gate
  S_R_Flip_Flop s_r_ff_8 (.S(and_16_out), .R(and_17_out), .clk(CLK), .Q(Contents[7]));  // open: reset, Qn, preset
  and and_16 (and_16_out, IN_0[7], ~IN_MODE);  // AND_Gate
  and and_17 (and_17_out, ~IN_0[7], ~IN_MODE);  // AND_Gate

  // Notes on the sheet:
  //   0= IN
  //   1=OUT
endmodule

module COUNT (
  input  IN_MODE,
  input  NO_IN,
  input  CLK,
  input  [3:0] IN_1,
  input  [3:0] IN_0,
  output [3:0] OUT_0
);

  wire and_3_out, and_4_out, and_5_out, and_6_out, and_7_out, and_8_out, and_9_out, and_10_out;
  wire [3:0] and_1_out, and_2_out, or_1_out;

  assign and_1_out = {4{IN_MODE}} & IN_1;  // AND_Gate and_1, 4 bits wide
  assign or_1_out = and_1_out | and_2_out;  // OR_Gate or_1, 4 bits wide
  assign and_2_out = ~{4{IN_MODE}} & IN_0;  // AND_Gate and_2, 4 bits wide
  and and_3 (and_3_out, ~NO_IN, or_1_out[0]);  // AND_Gate
  and and_4 (and_4_out, ~or_1_out[0], ~NO_IN);  // AND_Gate
  and and_5 (and_5_out, ~NO_IN, or_1_out[1]);  // AND_Gate
  and and_6 (and_6_out, ~NO_IN, ~or_1_out[1]);  // AND_Gate
  and and_7 (and_7_out, ~NO_IN, or_1_out[2]);  // AND_Gate
  and and_8 (and_8_out, ~NO_IN, ~or_1_out[2]);  // AND_Gate
  and and_9 (and_9_out, ~NO_IN, or_1_out[3]);  // AND_Gate
  and and_10 (and_10_out, ~NO_IN, ~or_1_out[3]);  // AND_Gate
  S_R_Flip_Flop s_r_ff_1 (.S(and_3_out), .R(and_4_out), .clk(CLK), .Q(OUT_0[0]));  // open: reset, Qn, preset
  S_R_Flip_Flop s_r_ff_2 (.S(and_5_out), .R(and_6_out), .clk(CLK), .Q(OUT_0[1]));  // open: reset, Qn, preset
  S_R_Flip_Flop s_r_ff_3 (.S(and_7_out), .R(and_8_out), .clk(CLK), .Q(OUT_0[2]));  // open: reset, Qn, preset
  S_R_Flip_Flop s_r_ff_4 (.S(and_9_out), .R(and_10_out), .clk(CLK), .Q(OUT_0[3]));  // open: reset, Qn, preset

  // Notes on the sheet:
  //   Input from INC
  //   Input from IR
endmodule

module MAR (
  input  [3:0] InAdr,
  input  In_Out,
  input  Clock,
  output [3:0] OutAdr,
  output [3:0] Contents
);

  wire and_1_out, and_2_out, and_3_out, and_4_out, and_5_out, and_6_out, and_7_out, and_8_out;

  S_R_Flip_Flop s_r_ff_1 (.S(and_1_out), .R(and_2_out), .clk(Clock), .Q(Contents[0]));  // open: reset, Qn, preset
  and and_1 (and_1_out, InAdr[0], ~In_Out);  // AND_Gate
  and and_2 (and_2_out, ~InAdr[0], ~In_Out);  // AND_Gate
  S_R_Flip_Flop s_r_ff_2 (.S(and_3_out), .R(and_4_out), .clk(Clock), .Q(Contents[1]));  // open: reset, Qn, preset
  and and_3 (and_3_out, InAdr[1], ~In_Out);  // AND_Gate
  and and_4 (and_4_out, ~InAdr[1], ~In_Out);  // AND_Gate
  S_R_Flip_Flop s_r_ff_3 (.S(and_5_out), .R(and_6_out), .clk(Clock), .Q(Contents[2]));  // open: reset, Qn, preset
  and and_5 (and_5_out, InAdr[2], ~In_Out);  // AND_Gate
  and and_6 (and_6_out, ~InAdr[2], ~In_Out);  // AND_Gate
  S_R_Flip_Flop s_r_ff_4 (.S(and_7_out), .R(and_8_out), .clk(Clock), .Q(Contents[3]));  // open: reset, Qn, preset
  and and_7 (and_7_out, InAdr[3], ~In_Out);  // AND_Gate
  and and_8 (and_8_out, ~InAdr[3], ~In_Out);  // AND_Gate
  and and_9 (OutAdr[0], Contents[0], In_Out);
  and and_10 (OutAdr[1], Contents[1], In_Out);
  and and_11 (OutAdr[2], Contents[2], In_Out);
  and and_12 (OutAdr[3], Contents[3], In_Out);
endmodule

module EQ (
  input  [7:0] IN_1,
  input  [7:0] IN_0,
  output EQ
);

  wire and_1_out, and_2_out, and_3_out, and_4_out, and_5_out, and_6_out, and_7_out, and_8_out, and_9_out,
       and_10_out, and_11_out, and_12_out, and_13_out, and_14_out, and_15_out, and_16_out, or_1_out,
       or_2_out, or_3_out, or_4_out, or_5_out, or_6_out, or_7_out, or_8_out;

  and and_1 (and_1_out, IN_1[0], IN_0[0]);
  or or_1 (or_1_out, and_1_out, and_2_out);
  and and_2 (and_2_out, ~IN_1[0], ~IN_0[0]);  // AND_Gate
  and and_3 (and_3_out, IN_1[1], IN_0[1]);
  or or_2 (or_2_out, and_3_out, and_4_out);
  and and_4 (and_4_out, ~IN_1[1], ~IN_0[1]);  // AND_Gate
  and and_5 (and_5_out, IN_1[2], IN_0[2]);
  or or_3 (or_3_out, and_5_out, and_6_out);
  and and_6 (and_6_out, ~IN_1[2], ~IN_0[2]);  // AND_Gate
  and and_7 (and_7_out, IN_1[3], IN_0[3]);
  or or_4 (or_4_out, and_7_out, and_8_out);
  and and_8 (and_8_out, ~IN_1[3], ~IN_0[3]);  // AND_Gate
  and and_9 (and_9_out, IN_1[4], IN_0[4]);
  or or_5 (or_5_out, and_9_out, and_10_out);
  and and_10 (and_10_out, ~IN_1[4], ~IN_0[4]);  // AND_Gate
  and and_11 (and_11_out, IN_1[5], IN_0[5]);
  or or_6 (or_6_out, and_11_out, and_12_out);
  and and_12 (and_12_out, ~IN_1[5], ~IN_0[5]);  // AND_Gate
  and and_13 (and_13_out, IN_1[6], IN_0[6]);
  or or_7 (or_7_out, and_13_out, and_14_out);
  and and_14 (and_14_out, ~IN_1[6], ~IN_0[6]);  // AND_Gate
  and and_15 (and_15_out, IN_1[7], IN_0[7]);
  or or_8 (or_8_out, and_15_out, and_16_out);
  and and_16 (and_16_out, ~IN_1[7], ~IN_0[7]);  // AND_Gate
  and and_17 (EQ, or_1_out, or_2_out, or_3_out, or_4_out, or_5_out, or_6_out, or_7_out, or_8_out);
endmodule
