// Logisim project Small_Components.circ as structural Verilog: 7 circuits, main circuit Half_Adder
module Half_Adder (
  input  A,
  input  B,
  output R,
  output C_Out
);

  wire or_1_out;

  and and_1 (C_Out, A, B);
  or or_1 (or_1_out, A, B);
  and and_2 (R, ~C_Out, or_1_out);  // AND_Gate
endmodule

module Full_Adder (
  input  A,
  input  B,
  input  C_In,
  output R,
  output C_Out
);

  wire A_B_out, A_C_out, and_1_out, and_2_out, and_3_out, B_C_out, or_1_out;

  and A_B (A_B_out, A, B);
  and A_C (A_C_out, A, C_In);
  and B_C (B_C_out, B, C_In);
  and and_1 (and_1_out, A, B, C_In);
  or or_1 (or_1_out, A, B, C_In);
  and and_2 (and_2_out, ~A_B_out, ~A_C_out, ~B_C_out);  // AND_Gate
  and and_3 (and_3_out, or_1_out, and_2_out);
  or or_2 (C_Out, A_B_out, A_C_out, B_C_out);
  or or_3 (R, and_1_out, and_3_out);
endmodule

module DATA_BYTE (
  input  [7:0] Byte_In,
  input  CLK,
  input  NO_IN,
  output [7:0] Byte_Out
);

  wire and_1_out, and_2_out, and_3_out, and_4_out, and_5_out, and_6_out, and_7_out, and_8_out, and_9_out,
       and_10_out, and_11_out, and_12_out, and_13_out, and_14_out, and_15_out, and_16_out;

  S_R_Flip_Flop s_r_ff_1 (.S(and_1_out), .R(and_2_out), .clk(CLK), .Q(Byte_Out[0]));  // open: reset, Qn, preset
  and and_1 (and_1_out, ~NO_IN, Byte_In[0]);  // AND_Gate
  and and_2 (and_2_out, ~NO_IN, ~Byte_In[0]);  // AND_Gate
  and and_3 (and_3_out, ~NO_IN, Byte_In[1]);  // AND_Gate
  S_R_Flip_Flop s_r_ff_2 (.S(and_3_out), .R(and_4_out), .clk(CLK), .Q(Byte_Out[1]));  // open: reset, Qn, preset
  and and_4 (and_4_out, ~NO_IN, ~Byte_In[1]);  // AND_Gate
  and and_5 (and_5_out, ~NO_IN, Byte_In[2]);  // AND_Gate
  S_R_Flip_Flop s_r_ff_3 (.S(and_5_out), .R(and_6_out), .clk(CLK), .Q(Byte_Out[2]));  // open: reset, Qn, preset
  and and_6 (and_6_out, ~NO_IN, ~Byte_In[2]);  // AND_Gate
  and and_7 (and_7_out, ~NO_IN, Byte_In[3]);  // AND_Gate
  S_R_Flip_Flop s_r_ff_4 (.S(and_7_out), .R(and_8_out), .clk(CLK), .Q(Byte_Out[3]));  // open: reset, Qn, preset
  and and_8 (and_8_out, ~NO_IN, ~Byte_In[3]);  // AND_Gate
  S_R_Flip_Flop s_r_ff_5 (.S(and_9_out), .R(and_10_out), .clk(CLK), .Q(Byte_Out[4]));  // open: reset, Qn, preset
  and and_9 (and_9_out, ~NO_IN, Byte_In[4]);  // AND_Gate
  and and_10 (and_10_out, ~NO_IN, ~Byte_In[4]);  // AND_Gate
  S_R_Flip_Flop s_r_ff_6 (.S(and_11_out), .R(and_12_out), .clk(CLK), .Q(Byte_Out[5]));  // open: reset, Qn, preset
  and and_11 (and_11_out, ~NO_IN, Byte_In[5]);  // AND_Gate
  and and_12 (and_12_out, ~NO_IN, ~Byte_In[5]);  // AND_Gate
  and and_13 (and_13_out, ~NO_IN, Byte_In[6]);  // AND_Gate
  S_R_Flip_Flop s_r_ff_7 (.S(and_13_out), .R(and_14_out), .clk(CLK), .Q(Byte_Out[6]));  // open: reset, Qn, preset
  and and_14 (and_14_out, ~NO_IN, ~Byte_In[6]);  // AND_Gate
  S_R_Flip_Flop s_r_ff_8 (.S(and_15_out), .R(and_16_out), .clk(CLK), .Q(Byte_Out[7]));  // open: reset, Qn, preset
  and and_15 (and_15_out, ~NO_IN, Byte_In[7]);  // AND_Gate
  and and_16 (and_16_out, ~NO_IN, ~Byte_In[7]);  // AND_Gate
endmodule

module INC_OLD (
  input  PLUS_1,
  input  [7:0] in_2,
  output [7:0] out_3
);

  wire half_adder_1_c_out, half_adder_2_c_out, half_adder_3_c_out, half_adder_4_c_out, half_adder_5_c_out,
       half_adder_6_c_out, half_adder_7_c_out;

  Half_Adder half_adder_1 (.A(in_2[0]), .B(PLUS_1), .R(out_3[0]), .C_Out(half_adder_1_c_out));
  Half_Adder half_adder_2 (.A(in_2[1]), .B(half_adder_1_c_out), .R(out_3[1]), .C_Out(half_adder_2_c_out));
  Half_Adder half_adder_3 (.A(in_2[2]), .B(half_adder_2_c_out), .R(out_3[2]), .C_Out(half_adder_3_c_out));
  Half_Adder half_adder_4 (.A(in_2[3]), .B(half_adder_3_c_out), .R(out_3[3]), .C_Out(half_adder_4_c_out));
  Half_Adder half_adder_5 (.A(in_2[4]), .B(half_adder_4_c_out), .R(out_3[4]), .C_Out(half_adder_5_c_out));
  Half_Adder half_adder_6 (.A(in_2[5]), .B(half_adder_5_c_out), .R(out_3[5]), .C_Out(half_adder_6_c_out));
  Half_Adder half_adder_7 (.A(in_2[6]), .B(half_adder_6_c_out), .R(out_3[6]), .C_Out(half_adder_7_c_out));
  Half_Adder half_adder_8 (.A(in_2[7]), .B(half_adder_7_c_out), .R(out_3[7]));  // open: C_Out
endmodule

module PC_INC (
  input  INC_ON,
  input  CLK
);

  wire [7:0] inc_old_1_out_3, PC_p3;

  INC_OLD inc_old_1 (.PLUS_1(INC_ON), .in_2(PC_p3), .out_3(inc_old_1_out_3));
  // DATA_BYTE PC: pin names not known; wires that end beside it: inc_old_1_out_3, CLK, PC_p3
  // Probe on PC_p3

  // Notes on the sheet:
  //   INC
endmodule

module PC (
  input  IN_MODE,
  input  NO_IN,
  input  CLK,
  input  [3:0] IN_1,
  input  [3:0] IN_0,
  output [3:0] OUT_0
);

  wire and_3_out, and_4_out, and_5_out, and_6_out, and_7_out, and_8_out, and_9_out, and_10_out;
  wire [3:0] and_1_out, and_2_out, or_1_out;

  assign and_1_out = {4{IN_MODE}} & IN_1;  // AND_Gate and_1, 4 bits wide
  assign or_1_out = and_1_out | and_2_out;  // OR_Gate or_1, 4 bits wide
  assign and_2_out = ~{4{IN_MODE}} & IN_0;  // AND_Gate and_2, 4 bits wide
  and and_3 (and_3_out, ~NO_IN, or_1_out[0]);  // AND_Gate
  and and_4 (and_4_out, ~or_1_out[0], ~NO_IN);  // AND_Gate
  and and_5 (and_5_out, ~NO_IN, or_1_out[1]);  // AND_Gate
  and and_6 (and_6_out, ~NO_IN, ~or_1_out[1]);  // AND_Gate
  and and_7 (and_7_out, ~NO_IN, or_1_out[2]);  // AND_Gate
  and and_8 (and_8_out, ~NO_IN, ~or_1_out[2]);  // AND_Gate
  and and_9 (and_9_out, ~NO_IN, or_1_out[3]);  // AND_Gate
  and and_10 (and_10_out, ~NO_IN, ~or_1_out[3]);  // AND_Gate
  S_R_Flip_Flop s_r_ff_1 (.S(and_3_out), .R(and_4_out), .clk(CLK), .Q(OUT_0[0]));  // open: reset, Qn, preset
  S_R_Flip_Flop s_r_ff_2 (.S(and_5_out), .R(and_6_out), .clk(CLK), .Q(OUT_0[1]));  // open: reset, Qn, preset
  S_R_Flip_Flop s_r_ff_3 (.S(and_7_out), .R(and_8_out), .clk(CLK), .Q(OUT_0[2]));  // open: reset, Qn, preset
  S_R_Flip_Flop s_r_ff_4 (.S(and_9_out), .R(and_10_out), .clk(CLK), .Q(OUT_0[3]));  // open: reset, Qn, preset

  // Notes on the sheet:
  //   Input from INC
  //   Input from IR
endmodule

module INC (
  input  ON_0,
  input  [3:0] IN_0,
  output [3:0] OUT_0
);

  wire half_adder_1_c_out, half_adder_2_c_out, half_adder_3_c_out;

  Half_Adder half_adder_1 (.A(IN_0[0]), .B(ON_0), .R(OUT_0[0]), .C_Out(half_adder_1_c_out));
  Half_Adder half_adder_2 (.A(IN_0[1]), .B(half_adder_1_c_out), .R(OUT_0[1]), .C_Out(half_adder_2_c_out));
  Half_Adder half_adder_3 (.A(IN_0[2]), .B(half_adder_2_c_out), .R(OUT_0[2]), .C_Out(half_adder_3_c_out));
  Half_Adder half_adder_4 (.A(IN_0[3]), .B(half_adder_3_c_out), .R(OUT_0[3]));  // open: C_Out
endmodule
