// Logisim project DISPLAY.circ as structural Verilog: 2 circuits, main circuit DISPLAY
module DISPLAY (
  input  [3:0] in_1,
  input  [3:0] in_2,
  input  [3:0] in_3
);

  wire [6:0] encode_display_1_out_2, encode_display_2_out_2, encode_display_3_out_2;

  ENCODE_DISPLAY encode_display_1 (.out_2(encode_display_1_out_2), .in_1(in_1));
  _7_Segment_Display u_7_segment_display_1 (
    .g(encode_display_1_out_2[0]), .f(encode_display_1_out_2[1]), .a(encode_display_1_out_2[2]),
    .b(encode_display_1_out_2[3]), .e(encode_display_1_out_2[4]), .d(encode_display_1_out_2[5]),
    .c(encode_display_1_out_2[6]));  // open: dp
  ENCODE_DISPLAY encode_display_2 (.out_2(encode_display_2_out_2), .in_1(in_2));
  _7_Segment_Display u_7_segment_display_2 (
    .g(encode_display_2_out_2[0]), .f(encode_display_2_out_2[1]), .a(encode_display_2_out_2[2]),
    .b(encode_display_2_out_2[3]), .e(encode_display_2_out_2[4]), .d(encode_display_2_out_2[5]),
    .c(encode_display_2_out_2[6]));  // open: dp
  _7_Segment_Display u_7_segment_display_3 (
    .g(encode_display_3_out_2[0]), .f(encode_display_3_out_2[1]), .a(encode_display_3_out_2[2]),
    .b(encode_display_3_out_2[3]), .e(encode_display_3_out_2[4]), .d(encode_display_3_out_2[5]),
    .c(encode_display_3_out_2[6]));  // open: dp
  ENCODE_DISPLAY encode_display_3 (.out_2(encode_display_3_out_2), .in_1(in_3));
endmodule

module ENCODE_DISPLAY (
  input  [3:0] in_1,
  output [6:0] out_2
);

  wire _0_out, _1_2_out, _2_2_out, _3_2_out, _4_2_out, _5_2_out, _6_2_out, _7_out, _8_out, _9_out;

  or _6 (out_2[6], _9_out, _8_out, _7_out, _6_2_out, _5_2_out, _4_2_out, _3_2_out, _1_2_out, _0_out);
  and _9 (_9_out, in_1[3], ~in_1[2], ~in_1[1], in_1[0]);  // AND_Gate
  or _5 (out_2[5], _8_out, _6_2_out, _5_2_out, _3_2_out, _2_2_out, _0_out);
  and _8 (_8_out, in_1[3], ~in_1[2], ~in_1[1], ~in_1[0]);  // AND_Gate
  and _7 (_7_out, ~in_1[3], in_1[2], in_1[1], in_1[0]);  // AND_Gate
  or _4 (out_2[4], _8_out, _6_2_out, _2_2_out, _0_out);
  and _6_2 (_6_2_out, ~in_1[3], in_1[2], in_1[1], ~in_1[0]);  // AND_Gate
  or _3 (out_2[3], _9_out, _8_out, _7_out, _4_2_out, _3_2_out, _2_2_out, _1_2_out, _0_out);
  and _5_2 (_5_2_out, ~in_1[3], in_1[2], ~in_1[1], in_1[0]);  // AND_Gate
  and _4_2 (_4_2_out, ~in_1[3], in_1[2], ~in_1[1], ~in_1[0]);  // AND_Gate
  and _3_2 (_3_2_out, ~in_1[3], ~in_1[2], in_1[1], in_1[0]);  // AND_Gate
  or _2 (out_2[2], _9_out, _8_out, _7_out, _6_2_out, _5_2_out, _3_2_out, _2_2_out, _0_out);
  and _2_2 (_2_2_out, ~in_1[3], ~in_1[2], in_1[1], ~in_1[0]);  // AND_Gate
  or _1 (out_2[1], _9_out, _8_out, _6_2_out, _5_2_out, _4_2_out, _0_out);
  and _1_2 (_1_2_out, ~in_1[3], ~in_1[2], ~in_1[1], in_1[0]);  // AND_Gate
  and _0 (_0_out, ~in_1[3], ~in_1[2], ~in_1[1], ~in_1[0]);  // AND_Gate
  or _0_2 (out_2[0], _9_out, _8_out, _6_2_out, _5_2_out, _4_2_out, _3_2_out, _2_2_out);
endmodule
