// Logisim project computer.circ as structural Verilog: 8 circuits, main circuit main
module main (
  input  _0,
  input  _1,
  input  _2,
  input  _3,
  input  _4,
  input  _5,
  input  _6,
  input  _7,
  input  _8,
  input  _9,
  output [7:0] out_11
);

  wire clock_1_out;

  KeyPad keypad_1 (
    ._0(_0), ._1(_1), ._2(_2), ._3(_3), ._4(_4), ._5(_5), ._6(_6), ._7(_7), ._8(_8), ._9(_9),
    .Clock(clock_1_out), .Output(out_11));
  Clock clock_1 (.out(clock_1_out));

  // Notes on the sheet:
  //   Demo to show it works as a box
endmodule

module RAM (
  input  READ_WRITE,
  input  [3:0] ADDR
);

  wire CLK_out;
  wire [0:0] not_28_out;
  wire [1:0] not_11_out;
  wire [1:1] not_20_out;
  wire [2:0] not_8_out, not_26_out;
  wire [2:1] not_18_out;
  wire [2:2] not_32_out;
  wire [3:0] not_1_out, not_5_out, not_21_out, not_24_out;
  wire [3:1] not_13_out, not_16_out;
  wire [3:2] not_29_out;
  wire [3:3] not_31_out;
  wire [7:0] _0000_data_out, _0_q, _0001_data_out, _0010_data_out, _0011_data_out, _0100_data_out,
       _0101_data_out, _0110_data_out, _0111_data_out, _1000_data_out, _1001_data_out, _1010_data_out,
       _1011_data_out, _1100_data_out, _1101_data_out, _1110_data_out, _1111_data_out, or_1_out, undriven;

  Clock CLK (.out(CLK_out));
  RAM_BYTE _0000 (.CLK_IN(CLK_out), .MODE(READ_WRITE), .ADDR(not_1_out), .DATA_OUT(_0000_data_out), .DATA_IN(_0_q));
  RAM_BYTE _0100 (
    .CLK_IN(CLK_out), .MODE(READ_WRITE), .ADDR({not_5_out[3], ADDR[2], not_5_out[1:0]}),
    .DATA_OUT(_0100_data_out), .DATA_IN(undriven));
  RAM_BYTE _1000 (
    .CLK_IN(CLK_out), .MODE(READ_WRITE), .ADDR({ADDR[3], not_8_out}), .DATA_OUT(_1000_data_out),
    .DATA_IN(_0_q));
  RAM_BYTE _1100 (
    .CLK_IN(CLK_out), .MODE(READ_WRITE), .ADDR({ADDR[3:2], not_11_out}), .DATA_OUT(_1100_data_out),
    .DATA_IN(_0_q));
  not not_1 (not_1_out[0], ADDR[0]);
  not not_2 (not_1_out[1], ADDR[1]);
  not not_3 (not_1_out[2], ADDR[2]);
  not not_4 (not_1_out[3], ADDR[3]);
  not not_5 (not_5_out[0], ADDR[0]);
  not not_6 (not_5_out[1], ADDR[1]);
  not not_7 (not_5_out[3], ADDR[3]);
  not not_8 (not_8_out[0], ADDR[0]);
  not not_9 (not_8_out[1], ADDR[1]);
  not not_10 (not_8_out[2], ADDR[2]);
  not not_11 (not_11_out[0], ADDR[0]);
  not not_12 (not_11_out[1], ADDR[1]);
  D_Flip_Flop _7 (.clk(CLK_out), .D(or_1_out[7]), .Q(_0_q[7]));  // open: Qn, preset, en, reset
  RAM_BYTE _0001 (
    .CLK_IN(CLK_out), .MODE(READ_WRITE), .ADDR({not_13_out, ADDR[0]}), .DATA_OUT(_0001_data_out),
    .DATA_IN(_0_q));
  RAM_BYTE _0101 (
    .CLK_IN(CLK_out), .MODE(READ_WRITE), .ADDR({not_16_out[3], ADDR[2], not_16_out[1], ADDR[0]}),
    .DATA_OUT(_0101_data_out), .DATA_IN(undriven));
  RAM_BYTE _1001 (
    .CLK_IN(CLK_out), .MODE(READ_WRITE), .ADDR({ADDR[3], not_18_out, ADDR[0]}), .DATA_OUT(_1001_data_out),
    .DATA_IN(_0_q));
  RAM_BYTE _1101 (
    .CLK_IN(CLK_out), .MODE(READ_WRITE), .ADDR({ADDR[3:2], not_20_out[1], ADDR[0]}),
    .DATA_OUT(_1101_data_out), .DATA_IN(_0_q));
  D_Flip_Flop _6 (.clk(CLK_out), .D(or_1_out[6]), .Q(_0_q[6]));  // open: Qn, preset, en, reset
  not not_13 (not_13_out[1], ADDR[1]);
  not not_14 (not_13_out[2], ADDR[2]);
  not not_15 (not_13_out[3], ADDR[3]);
  not not_16 (not_16_out[1], ADDR[1]);
  not not_17 (not_16_out[3], ADDR[3]);
  not not_18 (not_18_out[1], ADDR[1]);
  not not_19 (not_18_out[2], ADDR[2]);
  not not_20 (not_20_out[1], ADDR[1]);
  D_Flip_Flop _5 (.clk(CLK_out), .D(or_1_out[5]), .Q(_0_q[5]));  // open: Qn, preset, en, reset
  D_Flip_Flop _4 (.clk(CLK_out), .D(or_1_out[4]), .Q(_0_q[4]));  // open: Qn, preset, en, reset
  assign or_1_out = _1100_data_out | _1000_data_out | _0100_data_out | _0000_data_out | _1101_data_out | _1001_data_out | _0101_data_out | _0001_data_out | _1110_data_out | _1010_data_out | _0110_data_out | _0010_data_out | _1111_data_out | _1011_data_out | _0111_data_out | _0011_data_out;  // OR_Gate or_1, 8 bits wide
  RAM_BYTE _0010 (
    .CLK_IN(CLK_out), .MODE(READ_WRITE), .ADDR({not_21_out[3:2], ADDR[1], not_21_out[0]}),
    .DATA_OUT(_0010_data_out), .DATA_IN(_0_q));
  not not_21 (not_21_out[0], ADDR[0]);
  not not_22 (not_21_out[2], ADDR[2]);
  not not_23 (not_21_out[3], ADDR[3]);
  RAM_BYTE _0110 (
    .CLK_IN(CLK_out), .MODE(READ_WRITE), .ADDR({not_24_out[3], ADDR[2:1], not_24_out[0]}),
    .DATA_OUT(_0110_data_out), .DATA_IN(undriven));
  not not_24 (not_24_out[0], ADDR[0]);
  not not_25 (not_24_out[3], ADDR[3]);
  RAM_BYTE _1010 (
    .CLK_IN(CLK_out), .MODE(READ_WRITE), .ADDR({ADDR[3], not_26_out[2], ADDR[1], not_26_out[0]}),
    .DATA_OUT(_1010_data_out), .DATA_IN(_0_q));
  not not_26 (not_26_out[0], ADDR[0]);
  not not_27 (not_26_out[2], ADDR[2]);
  RAM_BYTE _1110 (
    .CLK_IN(CLK_out), .MODE(READ_WRITE), .ADDR({ADDR[3:1], not_28_out[0]}), .DATA_OUT(_1110_data_out),
    .DATA_IN(_0_q));
  not not_28 (not_28_out[0], ADDR[0]);
  D_Flip_Flop _3 (.clk(CLK_out), .D(or_1_out[3]), .Q(_0_q[3]));  // open: Qn, preset, en, reset
  D_Flip_Flop _2 (.clk(CLK_out), .D(or_1_out[2]), .Q(_0_q[2]));  // open: Qn, preset, en, reset
  D_Flip_Flop _1 (.clk(CLK_out), .D(or_1_out[1]), .Q(_0_q[1]));  // open: Qn, preset, en, reset
  RAM_BYTE _0011 (
    .CLK_IN(CLK_out), .MODE(READ_WRITE), .ADDR({not_29_out, ADDR[1:0]}), .DATA_OUT(_0011_data_out),
    .DATA_IN(_0_q));
  RAM_BYTE _0111 (
    .CLK_IN(CLK_out), .MODE(READ_WRITE), .ADDR({not_31_out[3], ADDR[2:0]}), .DATA_OUT(_0111_data_out),
    .DATA_IN(undriven));
  RAM_BYTE _1011 (
    .CLK_IN(CLK_out), .MODE(READ_WRITE), .ADDR({ADDR[3], not_32_out[2], ADDR[1:0]}),
    .DATA_OUT(_1011_data_out), .DATA_IN(_0_q));
  RAM_BYTE _1111 (.CLK_IN(CLK_out), .MODE(READ_WRITE), .ADDR(ADDR), .DATA_OUT(_1111_data_out), .DATA_IN(_0_q));
  D_Flip_Flop _0 (.clk(CLK_out), .D(or_1_out[0]), .Q(_0_q[0]));  // open: Qn, preset, en, reset
  not not_29 (not_29_out[2], ADDR[2]);
  not not_30 (not_29_out[3], ADDR[3]);
  not not_31 (not_31_out[3], ADDR[3]);
  not not_32 (not_32_out[2], ADDR[2]);

  // Notes on the sheet:
  //   read = 0, write = 1
endmodule

module RAM_BYTE (
  input  CLK_IN,
  input  [3:0] ADDR,
  input  MODE,
  input  [7:0] DATA_IN,
  output [7:0] DATA_OUT
);

  wire and_1_out, and_3_out, and_4_out, and_6_out, and_7_out, and_9_out, and_10_out, and_12_out, and_13_out,
       and_15_out, and_16_out, and_18_out, and_19_out, and_21_out, and_22_out, and_24_out, s_r_ff_1_q,
       s_r_ff_2_q, s_r_ff_3_q, s_r_ff_4_q, s_r_ff_5_q, s_r_ff_6_q, s_r_ff_7_q, s_r_ff_8_q;

  and and_1 (and_1_out, DATA_IN[7], ADDR[3], ADDR[2], ADDR[1], ADDR[0], MODE);
  and and_2 (DATA_OUT[7], s_r_ff_1_q, ADDR[3], ADDR[2], ADDR[1], ADDR[0], ~MODE);  // AND_Gate
  S_R_Flip_Flop s_r_ff_1 (.S(and_1_out), .clk(CLK_IN), .R(and_3_out), .Q(s_r_ff_1_q));  // open: Qn, preset, reset, en
  and and_3 (and_3_out, ~DATA_IN[7], ADDR[3], ADDR[2], ADDR[1], ADDR[0], MODE);  // AND_Gate
  and and_4 (and_4_out, DATA_IN[6], ADDR[3], ADDR[2], ADDR[1], ADDR[0], MODE);
  and and_5 (DATA_OUT[6], s_r_ff_2_q, ADDR[3], ADDR[2], ADDR[1], ADDR[0], ~MODE);  // AND_Gate
  S_R_Flip_Flop s_r_ff_2 (.S(and_4_out), .clk(CLK_IN), .R(and_6_out), .Q(s_r_ff_2_q));  // open: Qn, preset, reset, en
  and and_6 (and_6_out, ~DATA_IN[6], ADDR[3], ADDR[2], ADDR[1], ADDR[0], MODE);  // AND_Gate
  and and_7 (and_7_out, DATA_IN[5], ADDR[3], ADDR[2], ADDR[1], ADDR[0], MODE);
  and and_8 (DATA_OUT[5], s_r_ff_3_q, ADDR[3], ADDR[2], ADDR[1], ADDR[0], ~MODE);  // AND_Gate
  S_R_Flip_Flop s_r_ff_3 (.S(and_7_out), .clk(CLK_IN), .R(and_9_out), .Q(s_r_ff_3_q));  // open: Qn, preset, reset, en
  and and_9 (and_9_out, ~DATA_IN[5], ADDR[3], ADDR[2], ADDR[1], ADDR[0], MODE);  // AND_Gate
  and and_10 (and_10_out, DATA_IN[4], ADDR[3], ADDR[2], ADDR[1], ADDR[0], MODE);
  and and_11 (DATA_OUT[4], s_r_ff_4_q, ADDR[3], ADDR[2], ADDR[1], ADDR[0], ~MODE);  // AND_Gate
  S_R_Flip_Flop s_r_ff_4 (.S(and_10_out), .clk(CLK_IN), .R(and_12_out), .Q(s_r_ff_4_q));  // open: Qn, preset, reset, en
  and and_12 (and_12_out, ~DATA_IN[4], ADDR[3], ADDR[2], ADDR[1], ADDR[0], MODE);  // AND_Gate
  and and_13 (and_13_out, DATA_IN[3], ADDR[3], ADDR[2], ADDR[1], ADDR[0], MODE);
  and and_14 (DATA_OUT[3], s_r_ff_5_q, ADDR[3], ADDR[2], ADDR[1], ADDR[0], ~MODE);  // AND_Gate
  S_R_Flip_Flop s_r_ff_5 (.S(and_13_out), .clk(CLK_IN), .R(and_15_out), .Q(s_r_ff_5_q));  // open: Qn, preset, reset, en
  and and_15 (and_15_out, ~DATA_IN[3], ADDR[3], ADDR[2], ADDR[1], ADDR[0], MODE);  // AND_Gate
  and and_16 (and_16_out, DATA_IN[2], ADDR[3], ADDR[2], ADDR[1], ADDR[0], MODE);
  and and_17 (DATA_OUT[2], s_r_ff_6_q, ADDR[3], ADDR[2], ADDR[1], ADDR[0], ~MODE);  // AND_Gate
  S_R_Flip_Flop s_r_ff_6 (.S(and_16_out), .clk(CLK_IN), .R(and_18_out), .Q(s_r_ff_6_q));  // open: Qn, preset, reset, en
  and and_18 (and_18_out, ~DATA_IN[2], ADDR[3], ADDR[2], ADDR[1], ADDR[0], MODE);  // AND_Gate
  and and_19 (and_19_out, DATA_IN[1], ADDR[3], ADDR[2], ADDR[1], ADDR[0], MODE);
  and and_20 (DATA_OUT[1], s_r_ff_7_q, ADDR[3], ADDR[2], ADDR[1], ADDR[0], ~MODE);  // AND_Gate
  S_R_Flip_Flop s_r_ff_7 (.S(and_19_out), .clk(CLK_IN), .R(and_21_out), .Q(s_r_ff_7_q));  // open: Qn, preset, reset, en
  and and_21 (and_21_out, ~DATA_IN[1], ADDR[3], ADDR[2], ADDR[1], ADDR[0], MODE);  // AND_Gate
  and and_22 (and_22_out, DATA_IN[0], ADDR[3], ADDR[2], ADDR[1], ADDR[0], MODE);
  and and_23 (DATA_OUT[0], s_r_ff_8_q, ADDR[3], ADDR[2], ADDR[1], ADDR[0], ~MODE);  // AND_Gate
  S_R_Flip_Flop s_r_ff_8 (.S(and_22_out), .clk(CLK_IN), .R(and_24_out), .Q(s_r_ff_8_q));  // open: Qn, preset, reset, en
  and and_24 (and_24_out, ~DATA_IN[0], ADDR[3], ADDR[2], ADDR[1], ADDR[0], MODE);  // AND_Gate
endmodule

module KeyPad (
  input  _0,
  input  _1,
  input  _2,
  input  _3,
  input  _4,
  input  _5,
  input  _6,
  input  _7,
  input  _8,
  input  _9,
  input  Clock,
  output [7:0] Output
);

  wire Active_out, and_1_out, not_1_out, not_2_out, not_3_out, not_4_out, or_1_out, or_2_out, or_3_out,
       or_4_out;

  or Active (Active_out, _9, _8, _7, _6, _5, _4, _3, _2, _1, _0);
  or or_1 (or_1_out, _1, _3, _5, _7, _9);
  not not_1 (not_1_out, or_1_out);
  and and_1 (and_1_out, Active_out, Clock);
  S_R_Flip_Flop s_r_ff_1 (.S(or_1_out), .clk(and_1_out), .R(not_1_out), .Q(Output[0]));  // open: Qn, preset, reset, en
  or or_2 (or_2_out, _2, _3, _6, _7);
  S_R_Flip_Flop s_r_ff_2 (.S(or_2_out), .clk(and_1_out), .R(not_2_out), .Q(Output[1]));  // open: Qn, preset, reset, en
  not not_2 (not_2_out, or_2_out);
  or or_3 (or_3_out, _4, _5, _6, _7);
  not not_3 (not_3_out, or_3_out);
  S_R_Flip_Flop s_r_ff_3 (.S(or_3_out), .clk(and_1_out), .R(not_3_out), .Q(Output[2]));  // open: Qn, preset, reset, en
  or or_4 (or_4_out, _8, _9);
  S_R_Flip_Flop s_r_ff_4 (.S(or_4_out), .clk(and_1_out), .R(not_4_out), .Q(Output[3]));  // open: Qn, preset, reset, en
  not not_4 (not_4_out, or_4_out);

  assign Output[7:4] = 4'b0000;
endmodule

module ALU (
  input  [7:0] L_Input_Register,
  input  [7:0] R_Input_Register,
  input  [1:0] Op_Code,
  output [7:0] A,
  output [2:0] Status
);

  wire and_1_out, and_2_out, full_adder_1_c_out, full_adder_2_c_out, full_adder_3_c_out, full_adder_4_c_out,
       full_adder_5_c_out, full_adder_6_c_out, half_adder_1_c_out;
  wire [7:0] twos_comp_1_out;

  and and_1 (and_1_out, twos_comp_1_out[7], ~A[7], R_Input_Register[7]);  // AND_Gate
  // Probe on L_Input_Register
  Twos_Comp twos_comp_1 (.In(L_Input_Register), .Out(twos_comp_1_out), .ADD_SUB(Op_Code[0]));
  and and_2 (and_2_out, ~twos_comp_1_out[7], A[7], ~R_Input_Register[7]);  // AND_Gate
  or or_1 (Status[2], and_2_out, and_1_out);
  // Probe on R_Input_Register
  Half_Adder half_adder_1 (.A(R_Input_Register[0]), .B(twos_comp_1_out[0]), .R(A[0]), .C_Out(half_adder_1_c_out));
  Full_Adder full_adder_1 (
    .A(twos_comp_1_out[1]), .B(R_Input_Register[1]), .C_In(half_adder_1_c_out), .R(A[1]),
    .C_Out(full_adder_1_c_out));
  Full_Adder full_adder_2 (
    .A(twos_comp_1_out[2]), .B(R_Input_Register[2]), .C_In(full_adder_1_c_out), .R(A[2]),
    .C_Out(full_adder_2_c_out));
  Full_Adder full_adder_3 (
    .A(twos_comp_1_out[3]), .B(R_Input_Register[3]), .C_In(full_adder_2_c_out), .R(A[3]),
    .C_Out(full_adder_3_c_out));
  Full_Adder full_adder_4 (
    .A(twos_comp_1_out[4]), .B(R_Input_Register[4]), .C_In(full_adder_3_c_out), .R(A[4]),
    .C_Out(full_adder_4_c_out));
  Full_Adder full_adder_5 (
    .A(twos_comp_1_out[5]), .B(R_Input_Register[5]), .C_In(full_adder_4_c_out), .R(A[5]),
    .C_Out(full_adder_5_c_out));
  Full_Adder full_adder_6 (
    .A(twos_comp_1_out[6]), .B(R_Input_Register[6]), .C_In(full_adder_5_c_out), .R(A[6]),
    .C_Out(full_adder_6_c_out));
  Full_Adder full_adder_7 (
    .A(twos_comp_1_out[7]), .B(R_Input_Register[7]), .C_In(full_adder_6_c_out), .R(A[7]));  // open: C_Out
  and Zero (Status[0], ~A[0], ~A[1], ~A[2], ~A[3], ~A[4], ~A[5], ~A[6], ~A[7]);  // AND_Gate
  // Probe on A

  assign Status[1] = A[7];

  // Notes on the sheet:
  //   00 Sub
  //   01 Add
  //   001 zero result
  //   010 negative result
  //   100 overflow
endmodule

module Half_Adder (
  input  A,
  input  B,
  output R,
  output C_Out
);

  wire or_1_out;

  and and_1 (C_Out, A, B);
  or or_1 (or_1_out, A, B);
  and and_2 (R, ~C_Out, or_1_out);  // AND_Gate
endmodule

module Full_Adder (
  input  A,
  input  B,
  input  C_In,
  output R,
  output C_Out
);

  wire A__B_out, A_C_out, and_1_out, and_2_out, and_3_out, B_C_out, or_1_out;

  and A__B (A__B_out, A, B);
  and A_C (A_C_out, A, C_In);
  and B_C (B_C_out, B, C_In);
  and and_1 (and_1_out, A, B, C_In);
  or or_1 (or_1_out, A, B, C_In);
  and and_2 (and_2_out, ~A__B_out, ~A_C_out, ~B_C_out);  // AND_Gate
  and and_3 (and_3_out, or_1_out, and_2_out);
  or or_2 (C_Out, A__B_out, A_C_out, B_C_out);
  or or_3 (R, and_1_out, and_3_out);
endmodule

module Twos_Comp (
  input  ADD_SUB,
  input  [7:0] In,
  output [7:0] Out
);

  wire and_1_out, and_2_out, and_3_out, and_4_out, and_5_out, and_6_out, and_7_out, and_8_out, and_9_out,
       and_10_out, and_11_out, and_12_out, and_13_out, and_14_out, and_15_out, and_16_out,
       half_adder_1_c_out, half_adder_2_c_out, half_adder_3_c_out, half_adder_4_c_out, half_adder_5_c_out,
       half_adder_6_c_out, half_adder_7_c_out, not_1_out, or_1_out, or_2_out, or_3_out, or_4_out, or_5_out,
       or_6_out, or_7_out, or_8_out;

  // Probe on In
  and and_1 (and_1_out, ~In[0], ~ADD_SUB);  // AND_Gate
  and and_2 (and_2_out, In[0], ADD_SUB);
  and and_3 (and_3_out, ~In[1], ~ADD_SUB);  // AND_Gate
  and and_4 (and_4_out, In[1], ADD_SUB);
  and and_5 (and_5_out, ~In[2], ~ADD_SUB);  // AND_Gate
  and and_6 (and_6_out, In[2], ADD_SUB);
  and and_7 (and_7_out, ~In[3], ~ADD_SUB);  // AND_Gate
  and and_8 (and_8_out, In[3], ADD_SUB);
  and and_9 (and_9_out, ~In[4], ~ADD_SUB);  // AND_Gate
  and and_10 (and_10_out, In[4], ADD_SUB);
  and and_11 (and_11_out, ~In[5], ~ADD_SUB);  // AND_Gate
  and and_12 (and_12_out, In[5], ADD_SUB);
  and and_13 (and_13_out, ~In[6], ~ADD_SUB);  // AND_Gate
  and and_14 (and_14_out, In[6], ADD_SUB);
  and and_15 (and_15_out, ~In[7], ~ADD_SUB);  // AND_Gate
  and and_16 (and_16_out, In[7], ADD_SUB);
  or or_1 (or_1_out, and_1_out, and_2_out);
  or or_2 (or_2_out, and_3_out, and_4_out);
  or or_3 (or_3_out, and_5_out, and_6_out);
  or or_4 (or_4_out, and_7_out, and_8_out);
  or or_5 (or_5_out, and_9_out, and_10_out);
  or or_6 (or_6_out, and_11_out, and_12_out);
  or or_7 (or_7_out, and_13_out, and_14_out);
  or or_8 (or_8_out, and_15_out, and_16_out);
  Half_Adder half_adder_1 (.A(or_1_out), .B(not_1_out), .R(Out[0]), .C_Out(half_adder_1_c_out));
  not not_1 (not_1_out, ADD_SUB);
  Half_Adder half_adder_2 (.A(or_2_out), .B(half_adder_1_c_out), .R(Out[1]), .C_Out(half_adder_2_c_out));
  Half_Adder half_adder_3 (.A(or_3_out), .B(half_adder_2_c_out), .R(Out[2]), .C_Out(half_adder_3_c_out));
  Half_Adder half_adder_4 (.A(or_4_out), .B(half_adder_3_c_out), .R(Out[3]), .C_Out(half_adder_4_c_out));
  Half_Adder half_adder_5 (.A(or_5_out), .B(half_adder_4_c_out), .R(Out[4]), .C_Out(half_adder_5_c_out));
  Half_Adder half_adder_6 (.A(or_6_out), .B(half_adder_5_c_out), .R(Out[5]), .C_Out(half_adder_6_c_out));
  Half_Adder half_adder_7 (.A(or_7_out), .B(half_adder_6_c_out), .R(Out[6]), .C_Out(half_adder_7_c_out));
  Half_Adder half_adder_8 (.A(or_8_out), .B(half_adder_7_c_out), .R(Out[7]));  // open: C_Out
  // Probe on Out

  // Notes on the sheet:
  //   0 for sub, 1 for add
endmodule
